// Logisim project cpu21_riscv.circ as structural Verilog: 13 circuits, main circuit ◆单周期硬布线控制器_封装2
module \单周期_单级中断  (
  input  LEFT,
  input  RIGHT,
  input  START,
  input  CLK,
  input  UP,
  input  DOWN,
  input  RST,
  output \碰撞信号 ,
  output \边界警告 ,
  output [31:0] \行1 ,
  output [31:0] \行2 ,
  output [31:0] \行3 ,
  output [31:0] \行4 ,
  output [31:0] \行5 ,
  output [31:0] \行6 ,
  output [31:0] \行7 ,
  output [31:0] \行8 ,
  output [31:0] \行9 ,
  output [31:0] \行10 ,
  output [31:0] \行11 ,
  output [31:0] \行12 ,
  output [31:0] \行13 ,
  output [31:0] \行14 ,
  output [31:0] \行15 ,
  output [31:0] \行16 ,
  output [31:0] \行17 ,
  output [31:0] \行18 ,
  output [31:0] \行19 ,
  output [31:0] \行20 ,
  output [31:0] \行21 ,
  output [31:0] \行22 ,
  output [31:0] \行23 ,
  output [31:0] \行24 ,
  output [31:0] \行25 ,
  output [31:0] \行26 ,
  output [31:0] \行27 ,
  output [31:0] \行28 ,
  output [31:0] \行29 ,
  output [31:0] \行30 ,
  output [31:0] \行31 ,
  output [31:0] \行32 
);

  wire \_1号中断请求信号 , \_1号同步清零信号 , \_2号中断请求信号 , \_2号同步清零信号 , \_3号中断请求信号 , \_3号同步清零信号 , \_4号中断请求信号 ,
       \_4号同步清零信号 , \_5号中断请求信号 , \_5号同步清零信号 , \_6号中断请求信号 , \_6号同步清零信号 , alu_1_equal, alu_1_out_4, and_1_out,
       and_2_out, and_3_out, and_4_out, and_5_out, and_6_out, and_7_out, and_8_out, and_15_out, and_16_out,
       and_17_out, and_18_out, and_21_out, and_22_out, and_23_out, and_24_out, B_type, clock_1_out,
       comparator_1_eq, comparator_2_eq, comparator_3_eq, comparator_4_eq, comparator_5_eq, comparator_6_eq,
       comparator_7_eq, comparator_8_eq, comparator_9_eq, comparator_10_eq, comparator_11_eq,
       comparator_12_eq, comparator_12_lt, comparator_13_eq, comparator_13_gt, comparator_15_eq,
       comparator_15_gt, comparator_16_lt, comparator_17_eq, controlled_buffer_6_out,
       controlled_inverter_1_out, controlled_inverter_2_out, controlled_inverter_3_out, d_ff_1_q, d_ff_2_q,
       d_ff_3_q, d_ff_4_q, d_ff_5_q, d_ff_6_q, d_ff_7_q, d_ff_8_q, ecall, Go, I_type, IE_q, IR1, IR2, IR3,
       IR4, IR5, IR6, IRA, IRB, IRC, IRD, IRE, IRF, J_typpe, MemWrite, multiplexer_3_out, nand_1_out,
       nor_2_out, not_1_out, not_2_out, not_3_out, not_4_out, or_7_out, or_8_out, or_9_out, or_10_out,
       or_11_out, or_12_out, or_13_out, or_21_out, or_22_out, or_23_out, or_25_out, priority_encoder_1_gs,
       register_1_q, register_2_q, RegWrite, S_type, U_type, W1, W2, W3, W4, W5, W6,
       \单周期硬布线控制器_封装2_1_alu_src , \单周期硬布线控制器_封装2_1_beq , \单周期硬布线控制器_封装2_1_bge , \单周期硬布线控制器_封装2_1_bne ,
       \单周期硬布线控制器_封装2_1_jalr , \单周期硬布线控制器_封装2_1_lbu , \单周期硬布线控制器_封装2_1_memtoreg , \单周期硬布线控制器_封装2_1_uret ,
       \子弹内存访问 , \子弹屏幕刷新 , \子弹左移 , \小车消失 , \正常内存访问 , \飞机内存访问 , \飞机屏幕刷新 ;
  wire [2:0] priority_encoder_1_out, \中断编号_q ;
  wire [3:0] \单周期硬布线控制器_封装2_1_alu_op ;
  wire [4:0] multiplexer_6_out, multiplexer_7_out;
  wire [7:0] multiplexer_10_out, ram_1_data, ram_1_data_2, ram_1_data_3, ram_1_data_4;
  wire [9:0] ADDR;
  wire [12:0] CNT_num;
  wire [15:0] counter_3_q, \总周期数 ;
  wire [31:0] a7, adder_1_out, adder_2_out, adder_3_out, alu_1_result, and_19_out, bit_extender_1_out,
       bit_extender_2_out, bit_extender_3_out, bit_extender_4_out, bit_extender_5_out, bit_extender_6_out,
       controlled_buffer_1_out, controlled_buffer_7_out, IR, LedData, MDin, mEPC_q, multiplexer_1_out,
       multiplexer_2_out, multiplexer_4_out, multiplexer_5_out, multiplexer_8_out, multiplexer_9_out,
       multiplexer_11_out, PC, RDin, shifter_1_out, \地图备份寄存器堆_1_行1 , \地图备份寄存器堆_1_行2 , \地图备份寄存器堆_1_行3 ,
       \地图备份寄存器堆_1_行4 , \地图备份寄存器堆_1_行5 , \地图备份寄存器堆_1_行6 , \地图备份寄存器堆_1_行7 , \地图备份寄存器堆_1_行8 , \地图备份寄存器堆_1_行9 ,
       \地图备份寄存器堆_1_行10 , \地图备份寄存器堆_1_行11 , \地图备份寄存器堆_1_行12 , \地图备份寄存器堆_1_行13 , \地图备份寄存器堆_1_行14 ,
       \地图备份寄存器堆_1_行15 , \地图备份寄存器堆_1_行16 , \地图备份寄存器堆_1_行17 , \地图备份寄存器堆_1_行18 , \地图备份寄存器堆_1_行19 ,
       \地图备份寄存器堆_1_行20 , \地图备份寄存器堆_1_行21 , \地图备份寄存器堆_1_行22 , \地图备份寄存器堆_1_行23 , \地图备份寄存器堆_1_行24 ,
       \地图备份寄存器堆_1_行25 , \地图备份寄存器堆_1_行26 , \地图备份寄存器堆_1_行27 , \地图备份寄存器堆_1_行28 , \地图备份寄存器堆_1_行29 ,
       \地图备份寄存器堆_1_行30 , \地图备份寄存器堆_1_行31 , \地图备份寄存器堆_1_行32 , \地图备份寄存器堆_2_行1 , \地图备份寄存器堆_2_行2 ,
       \地图备份寄存器堆_2_行3 , \地图备份寄存器堆_2_行4 , \地图备份寄存器堆_2_行5 , \地图备份寄存器堆_2_行6 , \地图备份寄存器堆_2_行7 , \地图备份寄存器堆_2_行8 ,
       \地图备份寄存器堆_2_行9 , \地图备份寄存器堆_2_行10 , \地图备份寄存器堆_2_行11 , \地图备份寄存器堆_2_行12 , \地图备份寄存器堆_2_行13 ,
       \地图备份寄存器堆_2_行14 , \地图备份寄存器堆_2_行15 , \地图备份寄存器堆_2_行16 , \地图备份寄存器堆_2_行17 , \地图备份寄存器堆_2_行18 ,
       \地图备份寄存器堆_2_行19 , \地图备份寄存器堆_2_行20 , \地图备份寄存器堆_2_行21 , \地图备份寄存器堆_2_行22 , \地图备份寄存器堆_2_行23 ,
       \地图备份寄存器堆_2_行24 , \地图备份寄存器堆_2_行25 , \地图备份寄存器堆_2_行26 , \地图备份寄存器堆_2_行27 , \地图备份寄存器堆_2_行28 ,
       \地图备份寄存器堆_2_行29 , \地图备份寄存器堆_2_行30 , \地图备份寄存器堆_2_行31 , \地图备份寄存器堆_2_行32 , \子弹内存输出 , \点阵显示寄存器堆_1__1_2 ,
       \点阵显示寄存器堆_1__2_2 , \点阵显示寄存器堆_1__3_2 , \点阵显示寄存器堆_1__4_2 , \点阵显示寄存器堆_1__5_2 , \点阵显示寄存器堆_1__6_2 ,
       \点阵显示寄存器堆_1__7_2 , \点阵显示寄存器堆_1__8_2 , \点阵显示寄存器堆_1__9_2 , \点阵显示寄存器堆_1__10_2 , \点阵显示寄存器堆_1__11_2 ,
       \点阵显示寄存器堆_1__12_2 , \点阵显示寄存器堆_1__13_2 , \点阵显示寄存器堆_1__14_2 , \点阵显示寄存器堆_1__15_2 , \点阵显示寄存器堆_1__16_2 ,
       \点阵显示寄存器堆_1__17_2 , \点阵显示寄存器堆_1__18_2 , \点阵显示寄存器堆_1__19_2 , \点阵显示寄存器堆_1__20_2 , \点阵显示寄存器堆_1__21_2 ,
       \点阵显示寄存器堆_1__22_2 , \点阵显示寄存器堆_1__23_2 , \点阵显示寄存器堆_1__24_2 , \点阵显示寄存器堆_1__25_2 , \点阵显示寄存器堆_1__26_2 ,
       \点阵显示寄存器堆_1__27_2 , \点阵显示寄存器堆_1__28_2 , \点阵显示寄存器堆_1__29_2 , \点阵显示寄存器堆_1__30_2 , \点阵显示寄存器堆_1__31_2 ,
       \点阵显示寄存器堆_1__32_2 , \点阵显示寄存器堆_2__1_2 , \点阵显示寄存器堆_2__2_2 , \点阵显示寄存器堆_2__3_2 , \点阵显示寄存器堆_2__4_2 ,
       \点阵显示寄存器堆_2__5_2 , \点阵显示寄存器堆_2__6_2 , \点阵显示寄存器堆_2__7_2 , \点阵显示寄存器堆_2__8_2 , \点阵显示寄存器堆_2__9_2 ,
       \点阵显示寄存器堆_2__10_2 , \点阵显示寄存器堆_2__11_2 , \点阵显示寄存器堆_2__12_2 , \点阵显示寄存器堆_2__13_2 , \点阵显示寄存器堆_2__14_2 ,
       \点阵显示寄存器堆_2__15_2 , \点阵显示寄存器堆_2__16_2 , \点阵显示寄存器堆_2__17_2 , \点阵显示寄存器堆_2__18_2 , \点阵显示寄存器堆_2__19_2 ,
       \点阵显示寄存器堆_2__20_2 , \点阵显示寄存器堆_2__21_2 , \点阵显示寄存器堆_2__22_2 , \点阵显示寄存器堆_2__23_2 , \点阵显示寄存器堆_2__24_2 ,
       \点阵显示寄存器堆_2__25_2 , \点阵显示寄存器堆_2__26_2 , \点阵显示寄存器堆_2__27_2 , \点阵显示寄存器堆_2__28_2 , \点阵显示寄存器堆_2__29_2 ,
       \点阵显示寄存器堆_2__30_2 , \点阵显示寄存器堆_2__31_2 , \点阵显示寄存器堆_2__32_2 , \选择电路_1__1 , \选择电路_1__1_2 , \选择电路_1__1_3 ,
       \选择电路_1__1_4 , \选择电路_1__2 , \选择电路_1__2_2 , \选择电路_1__2_3 , \选择电路_1__2_4 , \选择电路_1__3 , \选择电路_1__3_2 ,
       \选择电路_1__3_3 , \选择电路_1__3_4 , \选择电路_1__4 , \选择电路_1__4_2 , \选择电路_1__4_3 , \选择电路_1__4_4 , \选择电路_1__5 ,
       \选择电路_1__5_2 , \选择电路_1__5_3 , \选择电路_1__5_4 , \选择电路_1__6 , \选择电路_1__6_2 , \选择电路_1__6_3 , \选择电路_1__6_4 ,
       \选择电路_1__7 , \选择电路_1__7_2 , \选择电路_1__7_3 , \选择电路_1__7_4 , \选择电路_1__8 , \选择电路_1__8_2 , \选择电路_1__8_3 ,
       \选择电路_1__8_4 , \飞机内存输出 ;

  Multiplexer #(.select(3), .width(32), .disabled("Z"), .enable("false")) multiplexer_1 (
    .in0(32'h304c), .in1(32'h3010), .in2(32'h3004), .in3(32'h3088), .in4(32'h30d4), .in5(32'h312c),
    .out(multiplexer_1_out), .sel(priority_encoder_1_out));  // open: in6, in7
  Priority_Encoder #(.select(3), .disabled("Z")) priority_encoder_1 (
    .in0(\_1号中断请求信号 ), .in1(\_2号中断请求信号 ), .in2(\_3号中断请求信号 ), .in3(\_4号中断请求信号 ), .in4(\_5号中断请求信号 ),
    .in5(\_6号中断请求信号 ), .out(priority_encoder_1_out), .gs(priority_encoder_1_gs));  // open: in6, in7, en_out, en_in
  not not_1 (not_1_out, priority_encoder_1_gs);
  Multiplexer #(.select(1), .width(32), .disabled("Z"), .enable("false")) multiplexer_2 (
    .in0(adder_1_out), .in1(and_19_out), .out(multiplexer_2_out), .sel(or_21_out));
  Register #(.width(1), .trigger("rising"), .Select("low")) IE (
    .D(multiplexer_3_out), .Q(IE_q), .clk(CLK));  // open: en, clr
  Multiplexer #(.select(1), .width(1), .disabled("Z"), .enable("false")) multiplexer_3 (
    .in0(not_1_out), .in1(1'b1), .out(multiplexer_3_out), .sel(\单周期硬布线控制器_封装2_1_uret ));
  LED #(.active("true")) \_1号中断等待指示灯  (.in(W1));
  LED #(.active("true")) \_2号中断等待指示灯  (.in(W2));
  LED #(.active("true")) \_3号中断等待指示灯  (.in(W3));
  LED #(.active("true")) \_4号中断等待指示灯  (.in(W4));
  LED #(.active("true")) \_5号中断等待指示灯  (.in(W5));
  LED #(.active("true")) \_6号中断等待指示灯  (.in(W6));
  and and_1 (and_1_out, priority_encoder_1_gs, IE_q);
  Comparator #(.width(16), .mode("twosComplement")) comparator_1 (
    .a(16'h23b), .b(\总周期数 ), .eq(comparator_1_eq));  // open: gt, lt
  Comparator #(.width(16), .mode("twosComplement")) comparator_2 (
    .a(\总周期数 ), .b(16'h1), .eq(comparator_2_eq));  // open: gt, lt
  Comparator #(.width(16), .mode("twosComplement")) comparator_3 (
    .a(\总周期数 ), .b(16'h4), .eq(comparator_3_eq));  // open: gt, lt
  Comparator #(.width(16), .mode("twosComplement")) comparator_4 (
    .a(\总周期数 ), .b(16'h7), .eq(comparator_4_eq));  // open: gt, lt
  D_Flip_Flop #(.trigger("rising"), .Pre_Clr_Positions("LEGACY"), .NegatePresetClear("false"), .enable("true"), .NewFFLayout("false")) d_ff_1 (
    .clk(IR1), .D(1'b1), .Q(d_ff_1_q), .reset(\_1号中断请求信号 ));  // open: Qn, preset, en
  or or_1 (W1, \_1号中断请求信号 , d_ff_1_q);
  D_Flip_Flop #(.trigger("rising"), .Pre_Clr_Positions("LEGACY"), .NegatePresetClear("false"), .enable("true"), .NewFFLayout("false")) d_ff_2 (
    .clk(IR2), .D(1'b1), .Q(d_ff_2_q), .reset(\_2号中断请求信号 ));  // open: Qn, preset, en
  or or_2 (W2, \_2号中断请求信号 , d_ff_2_q);
  D_Flip_Flop #(.trigger("rising"), .Pre_Clr_Positions("LEGACY"), .NegatePresetClear("false"), .enable("true"), .NewFFLayout("false")) d_ff_3 (
    .clk(IR3), .D(1'b1), .Q(d_ff_3_q), .reset(\_3号中断请求信号 ));  // open: Qn, preset, en
  or or_3 (W3, \_3号中断请求信号 , d_ff_3_q);
  D_Flip_Flop #(.trigger("rising"), .Pre_Clr_Positions("LEGACY"), .NegatePresetClear("false"), .enable("true"), .NewFFLayout("false")) d_ff_4 (
    .clk(IR4), .D(1'b1), .Q(d_ff_4_q), .reset(\_4号中断请求信号 ));  // open: Qn, preset, en
  or or_4 (W4, \_4号中断请求信号 , d_ff_4_q);
  D_Flip_Flop #(.trigger("rising"), .Pre_Clr_Positions("LEGACY"), .NegatePresetClear("false"), .enable("true"), .NewFFLayout("false")) d_ff_5 (
    .clk(IR5), .D(1'b1), .Q(d_ff_5_q), .reset(\_5号中断请求信号 ));  // open: Qn, preset, en
  or or_5 (W5, \_5号中断请求信号 , d_ff_5_q);
  D_Flip_Flop #(.trigger("rising"), .Pre_Clr_Positions("LEGACY"), .NegatePresetClear("false"), .enable("true"), .NewFFLayout("false")) d_ff_6 (
    .clk(IR6), .D(1'b1), .Q(d_ff_6_q), .reset(\_6号中断请求信号 ));  // open: Qn, preset, en
  or or_6 (W6, \_6号中断请求信号 , d_ff_6_q);
  // Probe on \总周期数 
  Multiplexer #(.select(1), .width(32), .disabled("Z"), .enable("false")) multiplexer_4 (
    .in0(multiplexer_2_out), .in1(multiplexer_1_out), .out(multiplexer_4_out), .sel(and_1_out));
  Multiplexer #(.select(1), .width(32), .disabled("Z"), .enable("false")) multiplexer_5 (
    .in0(multiplexer_4_out), .in1(mEPC_q), .out(multiplexer_5_out), .sel(\单周期硬布线控制器_封装2_1_uret ));
  Register #(.width(32), .trigger("rising"), .Select("low")) mEPC (
    .D(multiplexer_2_out), .en(and_1_out), .Q(mEPC_q), .clk(CLK), .clr(RST));
  or or_7 (or_7_out, comparator_1_eq, comparator_2_eq);
  assign controlled_inverter_1_out = or_7_out ? ~CLK : 1'bz;  // Controlled_Inverter controlled_inverter_1
  assign controlled_inverter_2_out = comparator_3_eq ? ~CLK : 1'bz;  // Controlled_Inverter controlled_inverter_2
  assign controlled_inverter_3_out = comparator_4_eq ? ~CLK : 1'bz;  // Controlled_Inverter controlled_inverter_3
  Register #(.width(32), .trigger("rising"), .Select("low")) u_PC (
    .D(multiplexer_5_out), .Q(PC), .clk(CLK), .clr(RST));  // open: en
  Pull_Resistor #(.pull(0)) pull_resistor_1 (.node(controlled_inverter_1_out));
  Pull_Resistor #(.pull(0)) pull_resistor_2 (.node(controlled_inverter_2_out));
  Pull_Resistor #(.pull(0)) pull_resistor_3 (.node(controlled_inverter_3_out));
  or or_8 (or_8_out, d_ff_1_q, \_1号中断请求信号 );
  and and_2 (and_2_out, or_8_out, ~\_1号同步清零信号 );  // AND_Gate
  or or_9 (or_9_out, d_ff_2_q, \_2号中断请求信号 );
  and and_3 (and_3_out, or_9_out, ~\_2号同步清零信号 );  // AND_Gate
  or or_10 (or_10_out, d_ff_3_q, \_3号中断请求信号 );
  and and_4 (and_4_out, or_10_out, ~\_3号同步清零信号 );  // AND_Gate
  or or_11 (or_11_out, d_ff_4_q, \_4号中断请求信号 );
  and and_5 (and_5_out, or_11_out, ~\_4号同步清零信号 );  // AND_Gate
  or or_12 (or_12_out, d_ff_5_q, \_5号中断请求信号 );
  and and_6 (and_6_out, or_12_out, ~\_5号同步清零信号 );  // AND_Gate
  or or_13 (or_13_out, d_ff_6_q, \_6号中断请求信号 );
  and and_7 (and_7_out, or_13_out, ~\_6号同步清零信号 );  // AND_Gate
  Register #(.width(3), .trigger("rising"), .Select("low")) \u_中断编号  (
    .D(priority_encoder_1_out), .en(and_1_out), .Q(\中断编号_q ), .clk(CLK));  // open: clr
  D_Flip_Flop #(.trigger("rising"), .Pre_Clr_Positions("LEGACY"), .NegatePresetClear("false"), .enable("true"), .NewFFLayout("false")) u_IR1 (
    .clk(CLK), .D(and_2_out), .Q(\_1号中断请求信号 ), .reset(RST));  // open: Qn, preset, en
  D_Flip_Flop #(.trigger("rising"), .Pre_Clr_Positions("LEGACY"), .NegatePresetClear("false"), .enable("true"), .NewFFLayout("false")) u_IR2 (
    .clk(CLK), .D(and_3_out), .Q(\_2号中断请求信号 ), .reset(RST));  // open: Qn, preset, en
  D_Flip_Flop #(.trigger("rising"), .Pre_Clr_Positions("LEGACY"), .NegatePresetClear("false"), .enable("true"), .NewFFLayout("false")) u_IR3 (
    .clk(CLK), .D(and_4_out), .Q(\_3号中断请求信号 ), .reset(RST));  // open: Qn, preset, en
  D_Flip_Flop #(.trigger("rising"), .Pre_Clr_Positions("LEGACY"), .NegatePresetClear("false"), .enable("true"), .NewFFLayout("false")) u_IR4 (
    .clk(CLK), .D(and_5_out), .Q(\_4号中断请求信号 ), .reset(RST));  // open: Qn, preset, en
  D_Flip_Flop #(.trigger("rising"), .Pre_Clr_Positions("LEGACY"), .NegatePresetClear("false"), .enable("true"), .NewFFLayout("false")) u_IR5 (
    .clk(CLK), .D(and_6_out), .Q(\_5号中断请求信号 ), .reset(RST));  // open: Qn, preset, en
  D_Flip_Flop #(.trigger("rising"), .Pre_Clr_Positions("LEGACY"), .NegatePresetClear("false"), .enable("true"), .NewFFLayout("false")) u_IR6 (
    .clk(CLK), .D(and_7_out), .Q(\_6号中断请求信号 ), .reset(RST));  // open: Qn, preset, en
  or or_14 (IR1, LEFT, IRA);
  or or_15 (IR4, UP, IRD);
  Demultiplexer #(.select(3), .width(1), .tristate("false"), .disabled(0), .enable("true")) demultiplexer_1 (
    .out0(\_1号同步清零信号 ), .out1(\_2号同步清零信号 ), .out2(\_3号同步清零信号 ), .out3(\_4号同步清零信号 ), .out4(\_5号同步清零信号 ),
    .out5(\_6号同步清零信号 ), .in(\单周期硬布线控制器_封装2_1_uret ), .sel(\中断编号_q ), .en(\单周期硬布线控制器_封装2_1_uret ));  // open: out6, out7
  // RiscV_Probe riscv_probe_1: pin names not known; wires that end beside it: IR, \_3号同步清零信号 
  Adder #(.width(32)) adder_1 (.a(PC), .b(32'h4), .out(adder_1_out));  // open: cin, cout
  ROM #(.addrWidth(10), .dataWidth(32), .Select("high")) rom_1 (.addr(PC[11:2]), .data(IR));
  or or_16 (IR2, RIGHT, IRB);
  or or_17 (IR5, DOWN, IRE);
  \单周期硬布线控制器_封装2  \u_单周期硬布线控制器_封装2_1  (
    .OP(IR[6:2]), .Funct({IR[30], IR[25], IR[14:12]}), .in_3(IR[21]), .ALU_OP(\单周期硬布线控制器_封装2_1_alu_op ),
    .uret(\单周期硬布线控制器_封装2_1_uret ), .MemToReg(\单周期硬布线控制器_封装2_1_memtoreg ), .ecall(ecall), .MemWrite(MemWrite),
    .ALU_SRC(\单周期硬布线控制器_封装2_1_alu_src ), .RegWrite(RegWrite), .S_type(S_type), .Beq(\单周期硬布线控制器_封装2_1_beq ),
    .Bne(\单周期硬布线控制器_封装2_1_bne ), .Jalr(\单周期硬布线控制器_封装2_1_jalr ), .JAL(J_typpe), .LUI(U_type),
    .LBU(\单周期硬布线控制器_封装2_1_lbu ), .BGE(\单周期硬布线控制器_封装2_1_bge ));  // open: csrrsi, csrrci
  Multiplexer #(.select(1), .width(5), .disabled("Z"), .enable("false")) multiplexer_6 (
    .in0(IR[19:15]), .in1(5'b10001), .out(multiplexer_6_out), .sel(ecall));
  Multiplexer #(.select(1), .width(5), .disabled("Z"), .enable("false")) multiplexer_7 (
    .in0(IR[24:20]), .in1(5'b01010), .out(multiplexer_7_out), .sel(ecall));
  or or_18 (IR3, START, IRC);
  buf or_19 (IR6, IRF);  // OR_Gate
  assign bit_extender_1_out = {{20{IR[31]}}, IR[31:20]};  // Bit_Extender bit_extender_1
  assign bit_extender_2_out = {{20{IR[31]}}, {IR[31:25], IR[11:7]}};  // Bit_Extender bit_extender_2
  assign bit_extender_3_out = {{20{IR[31]}}, {IR[31], IR[7], IR[30:25], IR[11:8]}};  // Bit_Extender bit_extender_3
  assign bit_extender_4_out = {{12{IR[31]}}, {IR[31], IR[19:12], IR[20], IR[30:21]}};  // Bit_Extender bit_extender_4
  assign bit_extender_5_out = {{12{IR[31]}}, IR[31:12]};  // Bit_Extender bit_extender_5
  assign controlled_buffer_1_out = I_type ? bit_extender_1_out : 32'bz;  // Controlled_Buffer controlled_buffer_1
  assign controlled_buffer_1_out = S_type ? bit_extender_2_out : 32'bz;  // Controlled_Buffer controlled_buffer_2
  assign controlled_buffer_1_out = B_type ? bit_extender_3_out : 32'bz;  // Controlled_Buffer controlled_buffer_3
  assign controlled_buffer_1_out = J_typpe ? bit_extender_4_out : 32'bz;  // Controlled_Buffer controlled_buffer_4
  assign controlled_buffer_1_out = U_type ? bit_extender_5_out : 32'bz;  // Controlled_Buffer controlled_buffer_5
  or or_20 (B_type, \单周期硬布线控制器_封装2_1_beq , \单周期硬布线控制器_封装2_1_bne , \单周期硬布线控制器_封装2_1_bge );
  Regifile regifile_1 (
    .Din(RDin), .Clk(CLK), .R1(a7), .R2(MDin), .WE(RegWrite), .W_num(IR[11:7]), .R1_num(multiplexer_6_out),
    .R2_num(multiplexer_7_out));
  nor nor_1 (I_type, S_type, B_type, J_typpe, U_type);
  Multiplexer #(.select(1), .width(32), .disabled("Z"), .enable("false")) multiplexer_8 (
    .in0(MDin), .in1(controlled_buffer_1_out), .out(multiplexer_8_out), .sel(\单周期硬布线控制器_封装2_1_alu_src ));
  Comparator #(.width(32), .mode("twosComplement")) comparator_5 (
    .a(a7), .b(32'h22), .eq(comparator_5_eq));  // open: gt, lt
  Comparator #(.width(32), .mode("twosComplement")) comparator_6 (
    .a(a7), .b(32'h64), .eq(comparator_6_eq));  // open: gt, lt
  Comparator #(.width(32), .mode("twosComplement")) comparator_7 (
    .a(a7), .b(32'h25), .eq(comparator_7_eq));  // open: gt, lt
  Comparator #(.width(32), .mode("twosComplement")) comparator_8 (
    .a(a7), .b(32'h24), .eq(comparator_8_eq));  // open: gt, lt
  Comparator #(.width(32), .mode("twosComplement")) comparator_9 (
    .a(a7), .b(32'h23), .eq(comparator_9_eq));  // open: gt, lt
  Comparator #(.width(32), .mode("twosComplement")) comparator_10 (
    .a(a7), .b(32'h22), .eq(comparator_10_eq));  // open: gt, lt
  Comparator #(.width(32), .mode("twosComplement")) comparator_11 (
    .a(a7), .b(32'h5a), .eq(comparator_11_eq));  // open: gt, lt
  and and_8 (and_8_out, alu_1_out_4, \单周期硬布线控制器_封装2_1_bge );
  ALU alu_1 (
    .X(a7), .Y(multiplexer_8_out), .AluOP(\单周期硬布线控制器_封装2_1_alu_op ), .Equal(alu_1_equal),
    .Result({alu_1_result[31:12], ADDR, alu_1_result[1:0]}), .out_4(alu_1_out_4));  // open: Result_2, out_6
  Shifter #(.width(32), .shift("ll")) shifter_1 (.in(controlled_buffer_1_out), .\dist (5'b00001), .out(shifter_1_out));
  Multiplexer #(.select(1), .width(32), .disabled("Z"), .enable("false")) multiplexer_9 (
    .in0(PC), .in1(a7), .out(multiplexer_9_out), .sel(\单周期硬布线控制器_封装2_1_jalr ));
  not not_2 (not_2_out, comparator_5_eq);
  and and_9 (\边界警告 , comparator_6_eq, ecall);
  and and_10 (IRF, comparator_7_eq, ecall);
  and and_11 (\碰撞信号 , comparator_8_eq, ecall);
  and and_12 (\飞机屏幕刷新 , comparator_9_eq, ecall);
  and and_13 (\子弹屏幕刷新 , comparator_10_eq, ecall);
  and and_14 (\子弹左移 , comparator_11_eq, ecall);
  D_Flip_Flop #(.trigger("high"), .Pre_Clr_Positions("LEGACY"), .NegatePresetClear("false"), .enable("true"), .NewFFLayout("false")) d_ff_7 (.Q(d_ff_7_q));  // open: clk, D, Qn, preset, en, reset
  // Probe on 13'h2f4
  not not_3 (not_3_out, alu_1_equal);
  and and_15 (and_15_out, alu_1_equal, \单周期硬布线控制器_封装2_1_beq );
  and and_16 (and_16_out, not_3_out, \单周期硬布线控制器_封装2_1_bne );
  Adder #(.width(32)) adder_2 (.a(shifter_1_out), .b(multiplexer_9_out), .out(adder_2_out));  // open: cin, cout
  Register #(.width(32), .trigger("rising"), .Select("low")) \Led寄存器  (
    .D(MDin), .en(and_17_out), .Q(LedData), .clk(CLK));  // open: clr
  and and_17 (and_17_out, comparator_5_eq, ecall);
  and and_18 (and_18_out, ecall, not_2_out);
  Comparator #(.width(13), .mode("twosComplement")) comparator_12 (
    .a(CNT_num), .b(13'h2f4), .eq(comparator_12_eq), .lt(comparator_12_lt));  // open: gt
  Clock #(.highDuration(1), .lowDuration(1)) clock_1 (.out(clock_1_out));
  or or_21 (or_21_out, J_typpe, \单周期硬布线控制器_封装2_1_jalr , and_15_out, and_16_out, and_8_out);
  assign and_19_out = adder_2_out & 32'hfffffffe;  // AND_Gate and_19, 32 bits wide
  Counter #(.width(13), .max('h1fff), .ongoal("stay"), .trigger("rising"), .behavior("old")) counter_1 (
    .count(comparator_12_lt), .Q(CNT_num), .clk(clock_1_out));  // open: load, D, carry, clr, preset
  or or_22 (or_22_out, d_ff_8_q, and_18_out);
  nand nand_1 (nand_1_out, d_ff_7_q, comparator_12_eq);
  not not_4 (not_4_out, d_ff_8_q);
  D_Flip_Flop #(.trigger("falling"), .Pre_Clr_Positions("ABOVE_BELOW"), .NegatePresetClear("false"), .enable("false"), .NewFFLayout("true")) d_ff_8 (
    .clk(CLK), .D(or_22_out), .Q(d_ff_8_q), .reset(Go));  // open: Qn, preset
  Comparator #(.width(10), .mode("unsigned")) comparator_13 (
    .a(ADDR), .b(10'h40), .gt(comparator_13_gt), .eq(comparator_13_eq));  // open: lt
  assign controlled_buffer_6_out = nand_1_out ? clock_1_out : 1'bz;  // Controlled_Buffer controlled_buffer_6
  Pull_Resistor #(.pull(1)) pull_resistor_4 (.node(controlled_buffer_6_out));
  RAM #(.addrWidth(10), .dataWidth(32), .bus("separate"), .Select("high")) ram_1 (
    .addr(ADDR), .din(MDin), .data({ram_1_data_4, ram_1_data_3, ram_1_data_2, ram_1_data}), .str(MemWrite),
    .clk(CLK));  // open: sel, ld, clr
  Multiplexer #(.select(2), .width(8), .disabled("Z"), .enable("false")) multiplexer_10 (
    .in0(ram_1_data), .in1(ram_1_data_2), .in2(ram_1_data_3), .in3(ram_1_data_4), .out(multiplexer_10_out),
    .sel(alu_1_result[1:0]));
  Counter #(.width(16), .max('hffff), .ongoal("wrap"), .trigger("rising"), .behavior("new")) counter_2 (
    .count(not_4_out), .Q(\总周期数 ), .clk(CLK));  // open: load, D, carry, clr, preset, down
  Comparator #(.width(10), .mode("unsigned")) comparator_14 (.a(ADDR), .b(10'h20), .lt(\飞机内存访问 ));  // open: gt, eq
  or or_23 (or_23_out, comparator_15_gt, comparator_15_eq);
  Comparator #(.width(10), .mode("unsigned")) comparator_15 (
    .a(ADDR), .b(10'h20), .gt(comparator_15_gt), .eq(comparator_15_eq));  // open: lt
  Comparator #(.width(10), .mode("unsigned")) comparator_16 (
    .a(ADDR), .b(10'h40), .lt(comparator_16_lt));  // open: gt, eq
  or or_24 (\正常内存访问 , comparator_13_gt, comparator_13_eq);
  assign bit_extender_6_out = {{24{1'b0}}, multiplexer_10_out};  // Bit_Extender bit_extender_6
  and and_20 (\子弹内存访问 , or_23_out, comparator_16_lt);
  assign controlled_buffer_7_out = \飞机内存访问  ? \飞机内存输出  : 32'bz;  // Controlled_Buffer controlled_buffer_7
  assign controlled_buffer_7_out = \子弹内存访问  ? \子弹内存输出  : 32'bz;  // Controlled_Buffer controlled_buffer_8
  assign controlled_buffer_7_out = \正常内存访问  ? {ram_1_data_4, ram_1_data_3, ram_1_data_2, ram_1_data} : 32'bz;  // Controlled_Buffer controlled_buffer_9
  Multiplexer #(.select(1), .width(32), .disabled("Z"), .enable("false")) multiplexer_11 (
    .in0(controlled_buffer_7_out), .in1(bit_extender_6_out), .out(multiplexer_11_out),
    .sel(\单周期硬布线控制器_封装2_1_lbu ));
  nor nor_2 (nor_2_out, \单周期硬布线控制器_封装2_1_memtoreg , or_25_out);
  assign RDin = nor_2_out ? {alu_1_result[31:12], ADDR, alu_1_result[1:0]} : 32'bz;  // Controlled_Buffer controlled_buffer_10
  or or_25 (or_25_out, \单周期硬布线控制器_封装2_1_jalr , J_typpe);
  assign RDin = \单周期硬布线控制器_封装2_1_memtoreg  ? multiplexer_11_out : 32'bz;  // Controlled_Buffer controlled_buffer_11
  assign RDin = or_25_out ? adder_3_out : 32'bz;  // Controlled_Buffer controlled_buffer_12
  Adder #(.width(32)) adder_3 (.a(32'h4), .b(PC), .out(adder_3_out));  // open: cin, cout
  and and_21 (and_21_out, MemWrite, \飞机内存访问 );
  \地图备份寄存器堆  \u_地图备份寄存器堆_1  (
    .\写使能 (and_21_out), .Addr(ADDR), .CLK(CLK), .Data(MDin), .\行1 (\地图备份寄存器堆_1_行1 ), .\行2 (\地图备份寄存器堆_1_行2 ),
    .\行3 (\地图备份寄存器堆_1_行3 ), .\行4 (\地图备份寄存器堆_1_行4 ), .\行5 (\地图备份寄存器堆_1_行5 ), .\行6 (\地图备份寄存器堆_1_行6 ),
    .\行7 (\地图备份寄存器堆_1_行7 ), .\行8 (\地图备份寄存器堆_1_行8 ), .RST(RST), .\全体位移 (1'b0), .\行9 (\地图备份寄存器堆_1_行9 ),
    .\行10 (\地图备份寄存器堆_1_行10 ), .\行11 (\地图备份寄存器堆_1_行11 ), .\行12 (\地图备份寄存器堆_1_行12 ), .\行13 (\地图备份寄存器堆_1_行13 ),
    .\行14 (\地图备份寄存器堆_1_行14 ), .\行15 (\地图备份寄存器堆_1_行15 ), .\行16 (\地图备份寄存器堆_1_行16 ), .\行17 (\地图备份寄存器堆_1_行17 ),
    .\行18 (\地图备份寄存器堆_1_行18 ), .\行19 (\地图备份寄存器堆_1_行19 ), .\行20 (\地图备份寄存器堆_1_行20 ), .\行21 (\地图备份寄存器堆_1_行21 ),
    .\行22 (\地图备份寄存器堆_1_行22 ), .\行23 (\地图备份寄存器堆_1_行23 ), .\行24 (\地图备份寄存器堆_1_行24 ), .\行25 (\地图备份寄存器堆_1_行25 ),
    .\行26 (\地图备份寄存器堆_1_行26 ), .\行27 (\地图备份寄存器堆_1_行27 ), .\行28 (\地图备份寄存器堆_1_行28 ), .\行29 (\地图备份寄存器堆_1_行29 ),
    .\行30 (\地图备份寄存器堆_1_行30 ), .\行31 (\地图备份寄存器堆_1_行31 ), .\行32 (\地图备份寄存器堆_1_行32 ), .Mem(\飞机内存输出 ));
  and and_22 (and_22_out, MemWrite, \子弹内存访问 );
  \地图备份寄存器堆  \u_地图备份寄存器堆_2  (
    .\写使能 (and_22_out), .Addr(ADDR), .CLK(CLK), .Data(MDin), .\行1 (\地图备份寄存器堆_2_行1 ), .\行2 (\地图备份寄存器堆_2_行2 ),
    .\行3 (\地图备份寄存器堆_2_行3 ), .\行4 (\地图备份寄存器堆_2_行4 ), .\行5 (\地图备份寄存器堆_2_行5 ), .\行6 (\地图备份寄存器堆_2_行6 ),
    .\行7 (\地图备份寄存器堆_2_行7 ), .\行8 (\地图备份寄存器堆_2_行8 ), .RST(RST), .\全体位移 (\子弹左移 ), .\行9 (\地图备份寄存器堆_2_行9 ),
    .\行10 (\地图备份寄存器堆_2_行10 ), .\行11 (\地图备份寄存器堆_2_行11 ), .\行12 (\地图备份寄存器堆_2_行12 ), .\行13 (\地图备份寄存器堆_2_行13 ),
    .\行14 (\地图备份寄存器堆_2_行14 ), .\行15 (\地图备份寄存器堆_2_行15 ), .\行16 (\地图备份寄存器堆_2_行16 ), .\行17 (\地图备份寄存器堆_2_行17 ),
    .\行18 (\地图备份寄存器堆_2_行18 ), .\行19 (\地图备份寄存器堆_2_行19 ), .\行20 (\地图备份寄存器堆_2_行20 ), .\行21 (\地图备份寄存器堆_2_行21 ),
    .\行22 (\地图备份寄存器堆_2_行22 ), .\行23 (\地图备份寄存器堆_2_行23 ), .\行24 (\地图备份寄存器堆_2_行24 ), .\行25 (\地图备份寄存器堆_2_行25 ),
    .\行26 (\地图备份寄存器堆_2_行26 ), .\行27 (\地图备份寄存器堆_2_行27 ), .\行28 (\地图备份寄存器堆_2_行28 ), .\行29 (\地图备份寄存器堆_2_行29 ),
    .\行30 (\地图备份寄存器堆_2_行30 ), .\行31 (\地图备份寄存器堆_2_行31 ), .\行32 (\地图备份寄存器堆_2_行32 ), .Mem(\子弹内存输出 ));
  Button _1 (.out(IRA));
  \点阵显示寄存器堆  \u_点阵显示寄存器堆_1  (
    .\写使能 (\飞机屏幕刷新 ), ._1(\地图备份寄存器堆_1_行1 ), ._2(\地图备份寄存器堆_1_行9 ), ._3(\地图备份寄存器堆_1_行17 ),
    ._4(\地图备份寄存器堆_1_行25 ), ._5(\地图备份寄存器堆_1_行2 ), ._6(\地图备份寄存器堆_1_行10 ), ._7(\地图备份寄存器堆_1_行18 ),
    ._8(\地图备份寄存器堆_1_行26 ), ._9(\地图备份寄存器堆_1_行3 ), ._10(\地图备份寄存器堆_1_行11 ), ._11(\地图备份寄存器堆_1_行19 ),
    ._12(\地图备份寄存器堆_1_行27 ), ._13(\地图备份寄存器堆_1_行4 ), ._14(\地图备份寄存器堆_1_行12 ), ._15(\地图备份寄存器堆_1_行20 ),
    ._16(\地图备份寄存器堆_1_行28 ), ._17(\地图备份寄存器堆_1_行5 ), ._18(\地图备份寄存器堆_1_行13 ), ._19(\地图备份寄存器堆_1_行21 ),
    ._20(\地图备份寄存器堆_1_行29 ), ._21(\地图备份寄存器堆_1_行6 ), ._22(\地图备份寄存器堆_1_行14 ), ._23(\地图备份寄存器堆_1_行22 ),
    ._24(\地图备份寄存器堆_1_行30 ), ._25(\地图备份寄存器堆_1_行7 ), ._26(\地图备份寄存器堆_1_行15 ), ._27(\地图备份寄存器堆_1_行23 ),
    ._28(\地图备份寄存器堆_1_行31 ), ._29(\地图备份寄存器堆_1_行8 ), ._30(\地图备份寄存器堆_1_行16 ), ._31(\地图备份寄存器堆_1_行24 ),
    ._32(\地图备份寄存器堆_1_行32 ), .CLK(CLK), ._1_2(\点阵显示寄存器堆_1__1_2 ), ._2_2(\点阵显示寄存器堆_1__2_2 ),
    ._3_2(\点阵显示寄存器堆_1__3_2 ), ._4_2(\点阵显示寄存器堆_1__4_2 ), ._5_2(\点阵显示寄存器堆_1__5_2 ), ._6_2(\点阵显示寄存器堆_1__6_2 ),
    ._7_2(\点阵显示寄存器堆_1__7_2 ), ._8_2(\点阵显示寄存器堆_1__8_2 ), ._9_2(\点阵显示寄存器堆_1__9_2 ), ._10_2(\点阵显示寄存器堆_1__10_2 ),
    ._11_2(\点阵显示寄存器堆_1__11_2 ), ._12_2(\点阵显示寄存器堆_1__12_2 ), ._13_2(\点阵显示寄存器堆_1__13_2 ),
    ._14_2(\点阵显示寄存器堆_1__14_2 ), ._15_2(\点阵显示寄存器堆_1__15_2 ), ._16_2(\点阵显示寄存器堆_1__16_2 ),
    ._17_2(\点阵显示寄存器堆_1__17_2 ), ._18_2(\点阵显示寄存器堆_1__18_2 ), ._19_2(\点阵显示寄存器堆_1__19_2 ),
    ._20_2(\点阵显示寄存器堆_1__20_2 ), ._21_2(\点阵显示寄存器堆_1__21_2 ), ._22_2(\点阵显示寄存器堆_1__22_2 ),
    ._23_2(\点阵显示寄存器堆_1__23_2 ), ._24_2(\点阵显示寄存器堆_1__24_2 ), ._25_2(\点阵显示寄存器堆_1__25_2 ),
    ._26_2(\点阵显示寄存器堆_1__26_2 ), ._27_2(\点阵显示寄存器堆_1__27_2 ), ._28_2(\点阵显示寄存器堆_1__28_2 ),
    ._29_2(\点阵显示寄存器堆_1__29_2 ), ._30_2(\点阵显示寄存器堆_1__30_2 ), ._31_2(\点阵显示寄存器堆_1__31_2 ),
    ._32_2(\点阵显示寄存器堆_1__32_2 ), .RST(RST));
  Button _4 (.out(IRD));
  Button _3 (.out(IRC));
  Button _2 (.out(IRB));
  Button _5 (.out(IRE));
  LED #(.active("true")) led_1 (.in(W1));
  LED #(.active("true")) led_2 (.in(W2));
  LED #(.active("true")) led_3 (.in(W3));
  LED #(.active("true")) led_4 (.in(W4));
  LED #(.active("true")) led_5 (.in(W5));
  LED #(.active("true")) led_6 (.in(W6));
  \选择电路  \u_选择电路_1  (
    .in_3(\点阵显示寄存器堆_1__1_2 ), .in_4(\点阵显示寄存器堆_1__5_2 ), .in_5(\点阵显示寄存器堆_1__9_2 ), .in_6(\点阵显示寄存器堆_1__13_2 ),
    .in_7(\点阵显示寄存器堆_1__17_2 ), .in_8(\点阵显示寄存器堆_1__21_2 ), .in_9(\点阵显示寄存器堆_1__25_2 ),
    .in_10(\点阵显示寄存器堆_1__29_2 ), .in_11(\点阵显示寄存器堆_1__2_2 ), .in_12(\点阵显示寄存器堆_1__6_2 ),
    .in_13(\点阵显示寄存器堆_1__10_2 ), .in_14(\点阵显示寄存器堆_1__14_2 ), .in_15(\点阵显示寄存器堆_1__18_2 ),
    .in_16(\点阵显示寄存器堆_1__22_2 ), .in_17(\点阵显示寄存器堆_1__26_2 ), .in_18(\点阵显示寄存器堆_1__30_2 ),
    .in_19(\点阵显示寄存器堆_1__3_2 ), .in_20(\点阵显示寄存器堆_1__7_2 ), .in_21(\点阵显示寄存器堆_1__11_2 ),
    .in_22(\点阵显示寄存器堆_1__15_2 ), .in_23(\点阵显示寄存器堆_1__19_2 ), .in_24(\点阵显示寄存器堆_1__23_2 ),
    .in_25(\点阵显示寄存器堆_1__27_2 ), .in_26(\点阵显示寄存器堆_1__31_2 ), .in_27(\点阵显示寄存器堆_1__4_2 ),
    .in_28(\点阵显示寄存器堆_1__8_2 ), .in_29(\点阵显示寄存器堆_1__12_2 ), .in_30(\点阵显示寄存器堆_1__16_2 ),
    .in_31(\点阵显示寄存器堆_1__20_2 ), .in_32(\点阵显示寄存器堆_1__24_2 ), .in_33(\点阵显示寄存器堆_1__28_2 ),
    .in_34(\点阵显示寄存器堆_1__32_2 ), ._1(\选择电路_1__1 ), ._2(\选择电路_1__2 ), ._3(\选择电路_1__3 ), ._4(\选择电路_1__4 ),
    ._5(\选择电路_1__5 ), ._6(\选择电路_1__6 ), ._7(\选择电路_1__7 ), ._8(\选择电路_1__8 ), ._1_2(\选择电路_1__1_2 ),
    ._2_2(\选择电路_1__2_2 ), ._3_2(\选择电路_1__3_2 ), ._4_2(\选择电路_1__4_2 ), ._5_2(\选择电路_1__5_2 ),
    ._6_2(\选择电路_1__6_2 ), ._7_2(\选择电路_1__7_2 ), ._8_2(\选择电路_1__8_2 ), ._1_3(\选择电路_1__1_3 ),
    ._2_3(\选择电路_1__2_3 ), ._3_3(\选择电路_1__3_3 ), ._4_3(\选择电路_1__4_3 ), ._5_3(\选择电路_1__5_3 ),
    ._6_3(\选择电路_1__6_3 ), ._7_3(\选择电路_1__7_3 ), ._8_3(\选择电路_1__8_3 ), ._1_4(\选择电路_1__1_4 ),
    ._2_4(\选择电路_1__2_4 ), ._3_4(\选择电路_1__3_4 ), ._4_4(\选择电路_1__4_4 ), ._5_4(\选择电路_1__5_4 ),
    ._6_4(\选择电路_1__6_4 ), ._7_4(\选择电路_1__7_4 ), ._8_4(\选择电路_1__8_4 ), .\碰撞 (\小车消失 ), .END(1'b0));
  \点阵显示寄存器堆  \u_点阵显示寄存器堆_2  (
    .\写使能 (\子弹屏幕刷新 ), ._1(\地图备份寄存器堆_2_行1 ), ._2(\地图备份寄存器堆_2_行9 ), ._3(\地图备份寄存器堆_2_行17 ),
    ._4(\地图备份寄存器堆_2_行25 ), ._5(\地图备份寄存器堆_2_行2 ), ._6(\地图备份寄存器堆_2_行10 ), ._7(\地图备份寄存器堆_2_行18 ),
    ._8(\地图备份寄存器堆_2_行26 ), ._9(\地图备份寄存器堆_2_行3 ), ._10(\地图备份寄存器堆_2_行11 ), ._11(\地图备份寄存器堆_2_行19 ),
    ._12(\地图备份寄存器堆_2_行27 ), ._13(\地图备份寄存器堆_2_行4 ), ._14(\地图备份寄存器堆_2_行12 ), ._15(\地图备份寄存器堆_2_行20 ),
    ._16(\地图备份寄存器堆_2_行28 ), ._17(\地图备份寄存器堆_2_行5 ), ._18(\地图备份寄存器堆_2_行13 ), ._19(\地图备份寄存器堆_2_行21 ),
    ._20(\地图备份寄存器堆_2_行29 ), ._21(\地图备份寄存器堆_2_行6 ), ._22(\地图备份寄存器堆_2_行14 ), ._23(\地图备份寄存器堆_2_行22 ),
    ._24(\地图备份寄存器堆_2_行30 ), ._25(\地图备份寄存器堆_2_行7 ), ._26(\地图备份寄存器堆_2_行15 ), ._27(\地图备份寄存器堆_2_行23 ),
    ._28(\地图备份寄存器堆_2_行31 ), ._29(\地图备份寄存器堆_2_行8 ), ._30(\地图备份寄存器堆_2_行16 ), ._31(\地图备份寄存器堆_2_行24 ),
    ._32(\地图备份寄存器堆_2_行32 ), .CLK(CLK), ._1_2(\点阵显示寄存器堆_2__1_2 ), ._2_2(\点阵显示寄存器堆_2__2_2 ),
    ._3_2(\点阵显示寄存器堆_2__3_2 ), ._4_2(\点阵显示寄存器堆_2__4_2 ), ._5_2(\点阵显示寄存器堆_2__5_2 ), ._6_2(\点阵显示寄存器堆_2__6_2 ),
    ._7_2(\点阵显示寄存器堆_2__7_2 ), ._8_2(\点阵显示寄存器堆_2__8_2 ), ._9_2(\点阵显示寄存器堆_2__9_2 ), ._10_2(\点阵显示寄存器堆_2__10_2 ),
    ._11_2(\点阵显示寄存器堆_2__11_2 ), ._12_2(\点阵显示寄存器堆_2__12_2 ), ._13_2(\点阵显示寄存器堆_2__13_2 ),
    ._14_2(\点阵显示寄存器堆_2__14_2 ), ._15_2(\点阵显示寄存器堆_2__15_2 ), ._16_2(\点阵显示寄存器堆_2__16_2 ),
    ._17_2(\点阵显示寄存器堆_2__17_2 ), ._18_2(\点阵显示寄存器堆_2__18_2 ), ._19_2(\点阵显示寄存器堆_2__19_2 ),
    ._20_2(\点阵显示寄存器堆_2__20_2 ), ._21_2(\点阵显示寄存器堆_2__21_2 ), ._22_2(\点阵显示寄存器堆_2__22_2 ),
    ._23_2(\点阵显示寄存器堆_2__23_2 ), ._24_2(\点阵显示寄存器堆_2__24_2 ), ._25_2(\点阵显示寄存器堆_2__25_2 ),
    ._26_2(\点阵显示寄存器堆_2__26_2 ), ._27_2(\点阵显示寄存器堆_2__27_2 ), ._28_2(\点阵显示寄存器堆_2__28_2 ),
    ._29_2(\点阵显示寄存器堆_2__29_2 ), ._30_2(\点阵显示寄存器堆_2__30_2 ), ._31_2(\点阵显示寄存器堆_2__31_2 ),
    ._32_2(\点阵显示寄存器堆_2__32_2 ), .RST(RST));
  Register #(.width(1), .trigger("rising"), .Select("low")) register_1 (
    .D(and_23_out), .Q(register_1_q), .clk(CLK));  // open: en, clr
  assign \行1  = \选择电路_1__1  | \点阵显示寄存器堆_2__1_2 ;  // OR_Gate or_26, 32 bits wide
  D_Flip_Flop #(.trigger("rising"), .Pre_Clr_Positions("LEGACY"), .NegatePresetClear("false"), .enable("true"), .NewFFLayout("false")) d_ff_9 (
    .clk(\碰撞信号 ), .D(1'b1), .Q(\小车消失 ), .reset(register_1_q));  // open: Qn, preset, en
  and and_23 (and_23_out, register_2_q, comparator_17_eq);
  assign \行3  = \选择电路_1__3  | \点阵显示寄存器堆_2__9_2 ;  // OR_Gate or_27, 32 bits wide
  assign \行4  = \选择电路_1__4  | \点阵显示寄存器堆_2__13_2 ;  // OR_Gate or_28, 32 bits wide
  assign \行2  = \选择电路_1__2  | \点阵显示寄存器堆_2__5_2 ;  // OR_Gate or_29, 32 bits wide
  Counter #(.width(16), .max('hffff), .ongoal("stay"), .trigger("rising"), .behavior("new")) counter_3 (
    .load(\碰撞信号 ), .D(16'h1f), .Q(counter_3_q), .clk(and_24_out), .down(1'b1));  // open: count, carry, clr, preset
  and and_24 (and_24_out, \小车消失 , CLK);
  Register #(.width(1), .trigger("rising"), .Select("low")) register_2 (
    .D(\小车消失 ), .Q(register_2_q), .clk(CLK));  // open: en, clr
  assign \行5  = \选择电路_1__5  | \点阵显示寄存器堆_2__17_2 ;  // OR_Gate or_30, 32 bits wide
  assign \行6  = \选择电路_1__6  | \点阵显示寄存器堆_2__21_2 ;  // OR_Gate or_31, 32 bits wide
  assign \行8  = \选择电路_1__8  | \点阵显示寄存器堆_2__29_2 ;  // OR_Gate or_32, 32 bits wide
  assign \行9  = \选择电路_1__1_2  | \点阵显示寄存器堆_2__2_2 ;  // OR_Gate or_33, 32 bits wide
  assign \行7  = \选择电路_1__7  | \点阵显示寄存器堆_2__25_2 ;  // OR_Gate or_34, 32 bits wide
  Comparator #(.width(16), .mode("unsigned")) comparator_17 (
    .a(counter_3_q), .b({16{1'b0}}), .eq(comparator_17_eq));  // open: gt, lt
  assign \行10  = \选择电路_1__2_2  | \点阵显示寄存器堆_2__6_2 ;  // OR_Gate or_35, 32 bits wide
  assign \行12  = \选择电路_1__4_2  | \点阵显示寄存器堆_2__14_2 ;  // OR_Gate or_36, 32 bits wide
  assign \行11  = \选择电路_1__3_2  | \点阵显示寄存器堆_2__10_2 ;  // OR_Gate or_37, 32 bits wide
  assign \行13  = \选择电路_1__5_2  | \点阵显示寄存器堆_2__18_2 ;  // OR_Gate or_38, 32 bits wide
  assign \行14  = \选择电路_1__6_2  | \点阵显示寄存器堆_2__22_2 ;  // OR_Gate or_39, 32 bits wide
  assign \行17  = \选择电路_1__1_3  | \点阵显示寄存器堆_2__3_2 ;  // OR_Gate or_40, 32 bits wide
  assign \行16  = \选择电路_1__8_2  | \点阵显示寄存器堆_2__30_2 ;  // OR_Gate or_41, 32 bits wide
  assign \行15  = \选择电路_1__7_2  | \点阵显示寄存器堆_2__26_2 ;  // OR_Gate or_42, 32 bits wide
  assign \行19  = \选择电路_1__3_3  | \点阵显示寄存器堆_2__11_2 ;  // OR_Gate or_43, 32 bits wide
  assign \行18  = \选择电路_1__2_3  | \点阵显示寄存器堆_2__7_2 ;  // OR_Gate or_44, 32 bits wide
  assign \行20  = \选择电路_1__4_3  | \点阵显示寄存器堆_2__15_2 ;  // OR_Gate or_45, 32 bits wide
  assign \行22  = \选择电路_1__6_3  | \点阵显示寄存器堆_2__23_2 ;  // OR_Gate or_46, 32 bits wide
  assign \行21  = \选择电路_1__5_3  | \点阵显示寄存器堆_2__19_2 ;  // OR_Gate or_47, 32 bits wide
  assign \行25  = \选择电路_1__1_4  | \点阵显示寄存器堆_2__4_2 ;  // OR_Gate or_48, 32 bits wide
  assign \行24  = \选择电路_1__8_3  | \点阵显示寄存器堆_2__31_2 ;  // OR_Gate or_49, 32 bits wide
  assign \行23  = \选择电路_1__7_3  | \点阵显示寄存器堆_2__27_2 ;  // OR_Gate or_50, 32 bits wide
  assign \行26  = \选择电路_1__2_4  | \点阵显示寄存器堆_2__8_2 ;  // OR_Gate or_51, 32 bits wide
  assign \行28  = \选择电路_1__4_4  | \点阵显示寄存器堆_2__16_2 ;  // OR_Gate or_52, 32 bits wide
  assign \行27  = \选择电路_1__3_4  | \点阵显示寄存器堆_2__12_2 ;  // OR_Gate or_53, 32 bits wide
  assign \行30  = \选择电路_1__6_4  | \点阵显示寄存器堆_2__24_2 ;  // OR_Gate or_54, 32 bits wide
  assign \行29  = \选择电路_1__5_4  | \点阵显示寄存器堆_2__20_2 ;  // OR_Gate or_55, 32 bits wide
  assign \行31  = \选择电路_1__7_4  | \点阵显示寄存器堆_2__28_2 ;  // OR_Gate or_56, 32 bits wide
  assign \行32  = \选择电路_1__8_4  | \点阵显示寄存器堆_2__32_2 ;  // OR_Gate or_57, 32 bits wide

  // Notes on the sheet:
  //   左
  //   右
  //   开始
  //   上
  //   下
  //   碰撞检测
  //   IE 用于开关中断，1 表示开中断，0 表是关中断
  //   IE寄存器建议采用同步置位和复位方式
  //   中断优先级 1 < 2 < 3，
  //   每一个多路选择器都可以优化为三态门
  //   中断编号
  //   中断请求
  //   单级中断测试信号模拟器
  //   数码管输出应该用寄存器锁存，否则显示数据只能一闪而过
  //   Reset 
  //   Reset 
  //   Reset 
  //   Reset 
  //   Reset 
  //   Reset 
  //   指令存储器
  //   pc+4
  //   contents of rom_1 (hex, n*v repeats v):
  //   1c000e63 9463 100093 200073 1112023 2008863 6c00f93 11fa8063 4a8a93 fe0aaa23 fe8aac23 fe9aae23
  //   12aa023 13aa223 14aa423 2300893 73 12883 200073 1112023 2008863 1000f93 dfa8263 ffca8a93 aa623
  //   fe8aac23 fe9aae23 12aa023 13aa223 14aa423 2300893 73 12883 200073 1112023 4008063 1b00f93 9fb0463
  //   1b0b13 145413 14d493 195913 19d993 1a5a13 fe8aac23 fe9aae23 12aa023 13aa223 14aa423 2300893 73 12883
  //   200073 1112023 2008e63 40b0063 fffb0b13 141413 149493 191913 199993 1a1a13 fe8aac23 fe9aae23 12aa023
  //   13aa223 14aa423 2300893 73 12883 200073 6400893 73 12883 200073 1112023 78aa283 7caa303 80aa383
  //   84aae03 88aae83 82ff33 f0c63 2400893 73 fff44f13 1e2f2b3 65aac23 937f33 f0c63 2400893 73 fff4cf13
  //   1e37333 66aae23 123ff33 f0c63 2400893 73 fff94f13 1e3f3b3 87aa023 13e7f33 f0c63 2400893 73 fff9cf13
  //   1ee7e33 9caa223 14eff33 f0c63 2400893 73 fffa4f13 1eefeb3 9daa423 100213 1112023 200073 7fc00113
  //   40000113 93 2000413 b000493 f800913 b000993 2000a13 1741413 1749493 1791913 1799993 17a1a13 4000a93
  //   100b13 fff00b93 1702023 1702223 7702c23 7702e23 2423 2623 2823 2a23 2c23 2e23 2002023 2002223
  //   2002423 2002623 2002823 2002a23 2002c23 2002e23 4002223 4002423 4002623 4002823 4002a23 4002c23
  //   4002e23 6002023 6002223 6002423 6002623 6002823 6002a23 8000b93 ba023 ba223 ba423 ba623 ba823 baa23
  //   bac23 bae23 20ba023 20ba223 20ba423 20ba623 20ba823 20baa23 20bac23 20bae23 40ba223 40ba423 40ba623
  //   40ba823 40baa23 40bac23 40bae23 60ba023 60ba223 60ba423 60ba623 60ba823 60baa23 60bac23 60bae23
  //   20000193 418613 4000513 100593 a1a023 b62023 5000513 100593 a1a423 b62423 1800513 100593 2a1a023
  //   2b62023 2400513 100593 2a1a823 2b62823 3400513 100593 4a1a023 4b62023 c00513 100593 4a1ac23 4b62c23
  //   3c00513 100593 6a1a823 6b62823 c00513 100593 6a1ac23 6b62c23 1000513 100593 8a1a423 8b62423 c00513
  //   100593 8a1ac23 8b62c23 7400513 100593 aa1a023 ab62023 4c00513 100593 ca1ac23 cb62c23 c00513 100593
  //   ea1a823 eb62823 4000513 100593 10a1a023 10b62023 4c00513 100593 12a1a023 12b62023 6c00513 100593
  //   16a1a023 16b62023 800513 100593 16a1a423 16b62423 3000513 100593 16a1a823 16b62823 2400513 100593
  //   18a1a023 18b62023 4800513 100593 1ca1a823 1cb62823 c00513 100593 1ea1a023 1eb62023 2000513 100593
  //   22a1a023 22b62023 2c00513 100593 22a1a823 22b62823 4c00513 100593 28a1a023 28b62023 1000513 100593
  //   2aa1a823 2ab62823 1400513 100593 2ea1a023 2eb62023 6400513 100593 30a1a823 30b62823 3c00513 100593
  //   30a1ac23 30b62c23 5000513 100593 34a1a423 34b62423 6800513 100593 36a1a023 36b62023 5400513 100593
  //   38a1a023 38b62023 4400513 100593 3aa1a823 3ab62823 5c00513 100593 3aa1ac23 3ab62c23 1c00513 100593
  //   3ca1ac23 3cb62c23 40018193 418613 6400513 100593 a1a023 b62023 7000513 100593 a1a423 b62423 5c00513
  //   100593 a1a823 b62823 6400513 100593 a1ac23 b62c23 2c00513 100593 4a1a423 4b62423 3000513 100593
  //   4a1ac23 4b62c23 4000513 100593 6a1a023 6b62023 7400513 100593 6a1a423 6b62423 6800513 100593 6a1a823
  //   6b62823 3c00513 100593 6a1ac23 6b62c23 c00513 100593 8a1a423 8b62423 6800513 100593 8a1a823 8b62823
  //   2c00513 100593 aa1a023 ab62023 2000513 100593 ca1a423 cb62423 5000513 100593 ca1a823 cb62823 6400513
  //   100593 ea1a023 eb62023 2400513 100593 ea1a423 eb62423 6400513 100593 10a1a023 10b62023 6400513
  //   100593 10a1a423 10b62423 6800513 100593 10a1ac23 10b62c23 800513 100593 12a1a023 12b62023 4c00513
  //   100593 12a1ac23 12b62c23 3000513 100593 14a1a423 14b62423 c00513 100593 14a1a823 14b62823 3c00513
  //   100593 16a1a023 16b62023 3800513 100593 16a1a423 16b62423 1000513 100593 16a1ac23 16b62c23 7000513
  //   100593 18a1a023 18b62023 6000513 100593 18a1ac23 18b62c23 5000513 100593 1aa1a023 1ab62023 4000513
  //   100593 1aa1a423 1ab62423 3800513 100593 1aa1a823 1ab62823 1800513 100593 1ca1a023 1cb62023 4c00513
  //   100593 1ca1a423 1cb62423 1400513 100593 1ea1a023 1eb62023 5800513 100593 1ea1a423 1eb62423 2800513
  //   100593 1ea1ac23 1eb62c23 5000513 100593 20a1a423 20b62423 5c00513 100593 20a1ac23 20b62c23 2400513
  //   100593 22a1a023 22b62023 3000513 100593 22a1a423 22b62423 4800513 100593 22a1a823 22b62823 3000513
  //   100593 22a1ac23 22b62c23 7400513 100593 24a1a023 24b62023 7400513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
  //   I型指令
  //   S型指令
  //   B型指令
  //   J型指令
  //   U型指令
  //   $a7
  //   $a0
  //   控制位
  //   暂停节拍，不能为0
  //   戳工具置1进入计数暂停模式，ctrl+k时钟自动运行到对应节拍暂停
  //   ctrl+k关闭时钟连续运行，将控制位置零，进入单步调试模式调试
  //   上升沿
  //   下降沿
  //   halt
  //   可计数暂停的时钟源
  //   数据存储器
  //   中断源
  //   中断源
  //   中断等待指示
endmodule

module \单周期硬布线控制器_封装2  (
  input  [4:0] OP,
  input  [4:0] Funct,
  input  in_3,
  output [3:0] ALU_OP,
  output uret,
  output MemToReg,
  output ecall,
  output MemWrite,
  output ALU_SRC,
  output RegWrite,
  output S_type,
  output Beq,
  output Bne,
  output JAL,
  output Jalr,
  output LUI,
  output LBU,
  output BGE,
  output csrrsi,
  output csrrci
);

  wire \控制信号自动生成_1_ecall ;

  \运算控制器自动生成  \u_运算控制器自动生成_1  (
    .OP2(OP[0]), .OP3(OP[1]), .OP4(OP[2]), .OP5(OP[3]), .OP6(OP[4]), .F12(Funct[0]), .F13(Funct[1]),
    .F14(Funct[2]), .F25(Funct[3]), .F30(Funct[4]), .S0(ALU_OP[0]), .S1(ALU_OP[1]), .S2(ALU_OP[2]),
    .S3(ALU_OP[3]));
  \控制信号自动生成  \u_控制信号自动生成_1  (
    .OP2(OP[0]), .OP3(OP[1]), .OP4(OP[2]), .OP5(OP[3]), .OP6(OP[4]), .MemToReg(MemToReg), .F12(Funct[0]),
    .F13(Funct[1]), .F14(Funct[2]), .F25(Funct[3]), .F30(Funct[4]), .MemWrite(MemWrite), .ALU_SRC(ALU_SRC),
    .RegWrite(RegWrite), .ecall(\控制信号自动生成_1_ecall ), .S_Type(S_type), .BEQ(Beq), .BNE(Bne), .JAL(JAL),
    .JALR(Jalr), .LUI(LUI), .LBU(LBU), .BGE(BGE));
  \中断信号自动生成  \u_中断信号自动生成_1  (
    .OP2(OP[0]), .OP3(OP[1]), .OP4(OP[2]), .OP5(OP[3]), .OP6(OP[4]), .F12(Funct[0]), .F13(Funct[1]),
    .F14(Funct[2]), .F25(Funct[3]), .F30(Funct[4]), .csrrsi(csrrsi), .csrrci(csrrci));
  and and_1 (uret, in_3, \控制信号自动生成_1_ecall );
  and and_2 (ecall, ~in_3, \控制信号自动生成_1_ecall );  // AND_Gate

  // Other names for the same wires on the sheet: IR21 = in_3; OP_CODE[4:0] = OP

  // Notes on the sheet:
  //   运算器控制器，根据指令生成运算器功能选择信号
  //   控制信号生成，产生数据通路需要的其他控制信号
endmodule

// 运算器控制器
module \运算控制器自动生成  (
  input  OP2,
  input  OP3,
  input  OP4,
  input  OP5,
  input  OP6,
  input  F12,
  input  F13,
  input  F14,
  input  F25,
  input  F30,
  output S0,
  output S1,
  output S2,
  output S3
);

  wire and_1_out, and_2_out, and_3_out, and_4_out, and_5_out, and_6_out, and_7_out, and_8_out, and_9_out,
       and_10_out, and_11_out, and_12_out, and_13_out, and_14_out, and_15_out, and_16_out, and_17_out,
       and_18_out, and_19_out, and_20_out, and_21_out, and_22_out, and_23_out, and_24_out, and_25_out,
       and_26_out, and_27_out, and_28_out, and_29_out, and_30_out, and_31_out, and_32_out, and_33_out,
       and_34_out, and_35_out, and_36_out, and_37_out, not_1_out, not_2_out, not_3_out, not_4_out, not_5_out,
       not_6_out, not_7_out, not_8_out, not_9_out, not_10_out, not_11_out, not_12_out, not_13_out,
       not_14_out, not_15_out, not_16_out, not_17_out, not_18_out, not_19_out, not_20_out, not_21_out,
       not_22_out, not_23_out, not_24_out, not_25_out, not_26_out, not_27_out, not_28_out, not_29_out,
       not_30_out, not_31_out, not_32_out, not_33_out, not_34_out, not_35_out, not_36_out, not_37_out,
       not_38_out, not_39_out, not_40_out, not_41_out, not_42_out, not_43_out, not_44_out, not_45_out,
       not_46_out, not_47_out, not_48_out, not_49_out, not_50_out, not_51_out, not_52_out, not_53_out,
       not_54_out, not_55_out, not_56_out, not_57_out, not_58_out, not_59_out, not_60_out, not_61_out,
       not_62_out, not_63_out, not_64_out, not_65_out, not_66_out, not_67_out, not_68_out, not_69_out,
       not_70_out, not_71_out, not_72_out, not_73_out, not_74_out, not_75_out, not_76_out, not_77_out,
       not_78_out, not_79_out, not_80_out, not_81_out, not_82_out, not_83_out, not_84_out, not_85_out,
       not_86_out, not_87_out, not_88_out, not_89_out, not_90_out, not_91_out, not_92_out, not_93_out,
       not_94_out, not_95_out, not_96_out, not_97_out, not_98_out, not_99_out, not_100_out, not_101_out,
       not_102_out, not_103_out, not_104_out, not_105_out, not_106_out, not_107_out, not_108_out,
       not_109_out, not_110_out, not_111_out, not_112_out, not_113_out, not_114_out, not_115_out,
       not_116_out, not_117_out, not_118_out, not_119_out, not_120_out, not_121_out, not_122_out,
       not_123_out, not_124_out, not_125_out, not_126_out, not_127_out, not_128_out, not_129_out,
       not_130_out, not_131_out, not_132_out, not_133_out, not_134_out, not_135_out, not_136_out,
       not_137_out, not_138_out, not_139_out, not_140_out, not_141_out, not_142_out, not_143_out,
       not_144_out, not_145_out, not_146_out, not_147_out, not_148_out, not_149_out, not_150_out,
       not_151_out, not_152_out, not_153_out, not_154_out, not_155_out, not_156_out, not_157_out,
       not_158_out, not_159_out, not_160_out, not_161_out, not_162_out, not_163_out, not_164_out,
       not_165_out, not_166_out, not_167_out, not_168_out, not_169_out, not_170_out, not_171_out,
       not_172_out, not_173_out, not_174_out, not_175_out, not_176_out, not_177_out, not_178_out,
       not_179_out, not_180_out, not_181_out, not_182_out, not_183_out, not_184_out, not_185_out,
       not_186_out, not_187_out, not_188_out;

  not not_1 (not_1_out, F30);
  not not_2 (not_2_out, F25);
  not not_3 (not_3_out, F14);
  not not_4 (not_4_out, F13);
  not not_5 (not_5_out, F12);
  not not_6 (not_6_out, OP6);
  not not_7 (not_7_out, OP3);
  not not_8 (not_8_out, OP2);
  not not_9 (not_9_out, OP6);
  not not_10 (not_10_out, OP3);
  not not_11 (not_11_out, OP2);
  not not_12 (not_12_out, F14);
  not not_13 (not_13_out, F12);
  not not_14 (not_14_out, OP6);
  not not_15 (not_15_out, OP3);
  not not_16 (not_16_out, OP2);
  not not_17 (not_17_out, F14);
  not not_18 (not_18_out, F13);
  not not_19 (not_19_out, F12);
  not not_20 (not_20_out, OP6);
  not not_21 (not_21_out, OP5);
  not not_22 (not_22_out, OP3);
  not not_23 (not_23_out, OP2);
  not not_24 (not_24_out, OP6);
  not not_25 (not_25_out, OP5);
  not not_26 (not_26_out, OP3);
  not not_27 (not_27_out, OP2);
  not not_28 (not_28_out, F13);
  not not_29 (not_29_out, F12);
  not not_30 (not_30_out, OP6);
  not not_31 (not_31_out, OP5);
  not not_32 (not_32_out, OP3);
  not not_33 (not_33_out, OP2);
  not not_34 (not_34_out, F14);
  not not_35 (not_35_out, F12);
  not not_36 (not_36_out, OP6);
  not not_37 (not_37_out, OP5);
  not not_38 (not_38_out, OP3);
  not not_39 (not_39_out, OP2);
  not not_40 (not_40_out, F25);
  not not_41 (not_41_out, F13);
  not not_42 (not_42_out, OP6);
  not not_43 (not_43_out, OP5);
  not not_44 (not_44_out, OP3);
  not not_45 (not_45_out, OP2);
  not not_46 (not_46_out, F14);
  not not_47 (not_47_out, F12);
  not not_48 (not_48_out, OP6);
  not not_49 (not_49_out, OP5);
  not not_50 (not_50_out, OP4);
  not not_51 (not_51_out, OP3);
  not not_52 (not_52_out, OP2);
  not not_53 (not_53_out, F14);
  not not_54 (not_54_out, F12);
  not not_55 (not_55_out, OP6);
  not not_56 (not_56_out, OP4);
  not not_57 (not_57_out, OP3);
  not not_58 (not_58_out, OP2);
  not not_59 (not_59_out, OP6);
  not not_60 (not_60_out, OP3);
  not not_61 (not_61_out, F13);
  not not_62 (not_62_out, OP4);
  not not_63 (not_63_out, OP3);
  not not_64 (not_64_out, OP2);
  not not_65 (not_65_out, F25);
  not not_66 (not_66_out, F14);
  not not_67 (not_67_out, F13);
  not not_68 (not_68_out, F12);
  not not_69 (not_69_out, OP6);
  not not_70 (not_70_out, OP3);
  not not_71 (not_71_out, OP2);
  not not_72 (not_72_out, OP6);
  not not_73 (not_73_out, OP3);
  not not_74 (not_74_out, OP2);
  not not_75 (not_75_out, F14);
  not not_76 (not_76_out, F12);
  not not_77 (not_77_out, OP6);
  not not_78 (not_78_out, OP3);
  not not_79 (not_79_out, OP2);
  not not_80 (not_80_out, OP6);
  not not_81 (not_81_out, OP5);
  not not_82 (not_82_out, OP3);
  not not_83 (not_83_out, OP2);
  not not_84 (not_84_out, F14);
  not not_85 (not_85_out, F12);
  not not_86 (not_86_out, OP6);
  not not_87 (not_87_out, OP5);
  not not_88 (not_88_out, OP3);
  not not_89 (not_89_out, OP2);
  not not_90 (not_90_out, F30);
  not not_91 (not_91_out, F25);
  not not_92 (not_92_out, F13);
  not not_93 (not_93_out, OP6);
  not not_94 (not_94_out, OP5);
  not not_95 (not_95_out, OP3);
  not not_96 (not_96_out, OP2);
  not not_97 (not_97_out, F13);
  not not_98 (not_98_out, OP6);
  not not_99 (not_99_out, OP3);
  not not_100 (not_100_out, OP2);
  not not_101 (not_101_out, F13);
  not not_102 (not_102_out, OP4);
  not not_103 (not_103_out, OP3);
  not not_104 (not_104_out, OP2);
  not not_105 (not_105_out, F30);
  not not_106 (not_106_out, F25);
  not not_107 (not_107_out, F14);
  not not_108 (not_108_out, F13);
  not not_109 (not_109_out, F12);
  not not_110 (not_110_out, OP6);
  not not_111 (not_111_out, OP3);
  not not_112 (not_112_out, OP2);
  not not_113 (not_113_out, F25);
  not not_114 (not_114_out, F14);
  not not_115 (not_115_out, F13);
  not not_116 (not_116_out, F12);
  not not_117 (not_117_out, OP6);
  not not_118 (not_118_out, OP3);
  not not_119 (not_119_out, OP2);
  not not_120 (not_120_out, OP6);
  not not_121 (not_121_out, OP3);
  not not_122 (not_122_out, OP2);
  not not_123 (not_123_out, F14);
  not not_124 (not_124_out, OP6);
  not not_125 (not_125_out, OP3);
  not not_126 (not_126_out, OP2);
  not not_127 (not_127_out, F14);
  not not_128 (not_128_out, F13);
  not not_129 (not_129_out, F12);
  not not_130 (not_130_out, OP6);
  not not_131 (not_131_out, OP5);
  not not_132 (not_132_out, OP3);
  not not_133 (not_133_out, OP2);
  not not_134 (not_134_out, OP6);
  not not_135 (not_135_out, OP5);
  not not_136 (not_136_out, OP3);
  not not_137 (not_137_out, OP2);
  not not_138 (not_138_out, F14);
  not not_139 (not_139_out, F12);
  not not_140 (not_140_out, OP6);
  not not_141 (not_141_out, OP5);
  not not_142 (not_142_out, OP4);
  not not_143 (not_143_out, OP3);
  not not_144 (not_144_out, OP2);
  not not_145 (not_145_out, F14);
  not not_146 (not_146_out, F12);
  not not_147 (not_147_out, OP6);
  not not_148 (not_148_out, OP4);
  not not_149 (not_149_out, OP3);
  not not_150 (not_150_out, OP2);
  not not_151 (not_151_out, OP6);
  not not_152 (not_152_out, OP3);
  not not_153 (not_153_out, F12);
  not not_154 (not_154_out, OP6);
  not not_155 (not_155_out, OP3);
  not not_156 (not_156_out, OP2);
  not not_157 (not_157_out, F14);
  not not_158 (not_158_out, F12);
  not not_159 (not_159_out, OP6);
  not not_160 (not_160_out, OP3);
  not not_161 (not_161_out, OP2);
  not not_162 (not_162_out, F14);
  not not_163 (not_163_out, OP6);
  not not_164 (not_164_out, OP3);
  not not_165 (not_165_out, OP2);
  not not_166 (not_166_out, F12);
  not not_167 (not_167_out, OP6);
  not not_168 (not_168_out, OP5);
  not not_169 (not_169_out, OP3);
  not not_170 (not_170_out, OP2);
  not not_171 (not_171_out, F13);
  not not_172 (not_172_out, F12);
  not not_173 (not_173_out, OP6);
  not not_174 (not_174_out, OP5);
  not not_175 (not_175_out, OP3);
  not not_176 (not_176_out, OP2);
  not not_177 (not_177_out, F14);
  not not_178 (not_178_out, F12);
  not not_179 (not_179_out, OP6);
  not not_180 (not_180_out, OP5);
  not not_181 (not_181_out, OP3);
  not not_182 (not_182_out, OP2);
  not not_183 (not_183_out, OP6);
  not not_184 (not_184_out, OP3);
  not not_185 (not_185_out, F13);
  not not_186 (not_186_out, OP4);
  not not_187 (not_187_out, OP3);
  not not_188 (not_188_out, OP2);
  and and_1 (and_1_out, not_1_out, not_2_out, not_3_out, not_4_out, not_5_out, not_6_out, OP5, OP4, not_7_out, not_8_out);
  and and_2 (and_2_out, F14, F13, F12, not_9_out, OP5, OP4, not_10_out, not_11_out);
  and and_3 (and_3_out, not_12_out, F13, not_13_out, not_14_out, OP5, OP4, not_15_out, not_16_out);
  and and_4 (and_4_out, not_17_out, not_18_out, not_19_out, not_20_out, not_21_out, OP4, not_22_out, not_23_out);
  and and_5 (and_5_out, F14, F13, F12, not_24_out, not_25_out, OP4, not_26_out, not_27_out);
  and and_6 (and_6_out, F14, not_28_out, not_29_out, not_30_out, not_31_out, OP4, not_32_out, not_33_out);
  and and_7 (and_7_out, not_34_out, F13, not_35_out, not_36_out, not_37_out, OP4, not_38_out, not_39_out);
  and and_8 (and_8_out, F30, not_40_out, F14, not_41_out, F12, not_42_out, not_43_out, OP4, not_44_out, not_45_out);
  and and_9 (and_9_out, not_46_out, F13, not_47_out, not_48_out, not_49_out, not_50_out, not_51_out, not_52_out);
  and and_10 (and_10_out, not_53_out, F13, not_54_out, not_55_out, OP5, not_56_out, not_57_out, not_58_out);
  and and_11 (and_11_out, not_59_out, OP5, OP4, not_60_out, OP2);
  and and_12 (and_12_out, F14, not_61_out, F12, OP6, OP5, not_62_out, not_63_out, not_64_out);
  and and_13 (and_13_out, F30, not_65_out, not_66_out, not_67_out, not_68_out, not_69_out, OP5, OP4, not_70_out, not_71_out);
  and and_14 (and_14_out, F14, F13, F12, not_72_out, OP5, OP4, not_73_out, not_74_out);
  and and_15 (and_15_out, not_75_out, F13, not_76_out, not_77_out, OP5, OP4, not_78_out, not_79_out);
  and and_16 (and_16_out, F14, F13, F12, not_80_out, not_81_out, OP4, not_82_out, not_83_out);
  and and_17 (and_17_out, not_84_out, F13, not_85_out, not_86_out, not_87_out, OP4, not_88_out, not_89_out);
  and and_18 (and_18_out, not_90_out, not_91_out, F14, not_92_out, F12, not_93_out, not_94_out, OP4, not_95_out, not_96_out);
  and and_19 (and_19_out, F14, not_97_out, F12, not_98_out, OP5, OP4, not_99_out, not_100_out);
  and and_20 (and_20_out, F14, not_101_out, F12, OP6, OP5, not_102_out, not_103_out, not_104_out);
  and and_21 (and_21_out, not_105_out, not_106_out, not_107_out, not_108_out, not_109_out, not_110_out, OP5, OP4, not_111_out, not_112_out);
  and and_22 (and_22_out, F30, not_113_out, not_114_out, not_115_out, not_116_out, not_117_out, OP5, OP4, not_118_out, not_119_out);
  and and_23 (and_23_out, F14, F13, F12, not_120_out, OP5, OP4, not_121_out, not_122_out);
  and and_24 (and_24_out, not_123_out, F13, F12, not_124_out, OP5, OP4, not_125_out, not_126_out);
  and and_25 (and_25_out, not_127_out, not_128_out, not_129_out, not_130_out, not_131_out, OP4, not_132_out, not_133_out);
  and and_26 (and_26_out, F14, F13, F12, not_134_out, not_135_out, OP4, not_136_out, not_137_out);
  and and_27 (and_27_out, not_138_out, F13, not_139_out, not_140_out, not_141_out, not_142_out, not_143_out, not_144_out);
  and and_28 (and_28_out, not_145_out, F13, not_146_out, not_147_out, OP5, not_148_out, not_149_out, not_150_out);
  and and_29 (and_29_out, not_151_out, OP5, OP4, not_152_out, OP2);
  and and_30 (and_30_out, F14, F13, not_153_out, not_154_out, OP5, OP4, not_155_out, not_156_out);
  and and_31 (and_31_out, not_157_out, F13, not_158_out, not_159_out, OP5, OP4, not_160_out, not_161_out);
  and and_32 (and_32_out, not_162_out, F13, F12, not_163_out, OP5, OP4, not_164_out, not_165_out);
  and and_33 (and_33_out, F14, F13, not_166_out, not_167_out, not_168_out, OP4, not_169_out, not_170_out);
  and and_34 (and_34_out, F14, not_171_out, not_172_out, not_173_out, not_174_out, OP4, not_175_out, not_176_out);
  and and_35 (and_35_out, not_177_out, F13, not_178_out, not_179_out, not_180_out, OP4, not_181_out, not_182_out);
  and and_36 (and_36_out, not_183_out, OP5, OP4, not_184_out, OP2);
  and and_37 (and_37_out, F14, not_185_out, F12, OP6, OP5, not_186_out, not_187_out, not_188_out);
  or or_1 (S0, and_1_out, and_2_out, and_3_out, and_4_out, and_5_out, and_6_out, and_7_out, and_8_out, and_9_out, and_10_out, and_11_out, and_12_out);
  or or_2 (S1, and_13_out, and_14_out, and_15_out, and_16_out, and_17_out, and_18_out, and_19_out, and_20_out);
  or or_3 (S2, and_21_out, and_22_out, and_23_out, and_24_out, and_25_out, and_26_out, and_27_out, and_28_out, and_29_out);
  or or_4 (S3, and_30_out, and_31_out, and_32_out, and_33_out, and_34_out, and_35_out, and_36_out, and_37_out);
endmodule

// 控制信号生成
module \控制信号自动生成  (
  input  OP2,
  input  OP3,
  input  OP4,
  input  OP5,
  input  OP6,
  input  F12,
  input  F13,
  input  F14,
  input  F25,
  input  F30,
  output MemToReg,
  output MemWrite,
  output ALU_SRC,
  output RegWrite,
  output ecall,
  output S_Type,
  output BEQ,
  output BNE,
  output JAL,
  output JALR,
  output LUI,
  output LBU,
  output BGE
);

  wire and_1_out, and_2_out, and_4_out, and_5_out, and_6_out, and_7_out, and_8_out, and_9_out, and_10_out,
       and_11_out, and_12_out, and_13_out, and_14_out, and_15_out, and_16_out, and_17_out, and_18_out,
       and_19_out, and_20_out, and_21_out, not_1_out, not_2_out, not_3_out, not_4_out, not_5_out, not_6_out,
       not_7_out, not_8_out, not_9_out, not_10_out, not_11_out, not_12_out, not_13_out, not_14_out,
       not_15_out, not_16_out, not_17_out, not_18_out, not_19_out, not_20_out, not_21_out, not_22_out,
       not_23_out, not_24_out, not_25_out, not_26_out, not_27_out, not_28_out, not_29_out, not_30_out,
       not_31_out, not_32_out, not_33_out, not_34_out, not_35_out, not_36_out, not_37_out, not_38_out,
       not_39_out, not_40_out, not_41_out, not_42_out, not_43_out, not_44_out, not_45_out, not_46_out,
       not_47_out, not_48_out, not_49_out, not_50_out, not_51_out, not_52_out, not_53_out, not_54_out,
       not_55_out, not_56_out, not_57_out, not_58_out, not_59_out, not_60_out, not_61_out, not_62_out,
       not_63_out, not_64_out, not_65_out, not_66_out, not_67_out, not_68_out, not_69_out, not_70_out,
       not_71_out, not_72_out, not_73_out, not_74_out, not_75_out, not_76_out, not_77_out, not_78_out,
       not_79_out, not_80_out, not_81_out, not_82_out, not_83_out, not_84_out, not_85_out, not_86_out,
       not_87_out, not_88_out, not_89_out, not_90_out, not_91_out, not_92_out, not_93_out, not_94_out,
       not_95_out, not_96_out, not_97_out, not_98_out, not_99_out, not_100_out, not_101_out, not_102_out,
       not_103_out, not_104_out, not_105_out, not_106_out, not_107_out, not_108_out, not_109_out,
       not_110_out, not_111_out, not_112_out, not_113_out, not_114_out, not_115_out, not_116_out,
       not_117_out, not_118_out, not_119_out, not_120_out, not_121_out, not_122_out, not_123_out,
       not_124_out, not_125_out, not_126_out, not_127_out, not_128_out, not_129_out, not_130_out,
       not_131_out, not_132_out, not_133_out, not_134_out, not_135_out, not_136_out, not_137_out,
       not_138_out, not_139_out, not_140_out;

  not not_1 (not_1_out, OP2);
  not not_2 (not_2_out, OP3);
  not not_3 (not_3_out, OP4);
  not not_4 (not_4_out, OP5);
  not not_5 (not_5_out, OP6);
  not not_6 (not_6_out, F12);
  not not_7 (not_7_out, F13);
  not not_8 (not_8_out, OP2);
  not not_9 (not_9_out, OP3);
  not not_10 (not_10_out, OP4);
  not not_11 (not_11_out, OP5);
  not not_12 (not_12_out, OP6);
  not not_13 (not_13_out, F12);
  not not_14 (not_14_out, F14);
  not not_15 (not_15_out, OP2);
  not not_16 (not_16_out, OP3);
  not not_17 (not_17_out, OP4);
  not not_18 (not_18_out, OP6);
  not not_19 (not_19_out, F12);
  not not_20 (not_20_out, F14);
  not not_21 (not_21_out, OP2);
  not not_22 (not_22_out, OP3);
  not not_23 (not_23_out, OP5);
  not not_24 (not_24_out, OP6);
  not not_25 (not_25_out, F12);
  not not_26 (not_26_out, F13);
  not not_27 (not_27_out, OP2);
  not not_28 (not_28_out, OP3);
  not not_29 (not_29_out, OP4);
  not not_30 (not_30_out, OP6);
  not not_31 (not_31_out, F12);
  not not_32 (not_32_out, F14);
  not not_33 (not_33_out, OP2);
  not not_34 (not_34_out, OP3);
  not not_35 (not_35_out, OP5);
  not not_36 (not_36_out, OP6);
  not not_37 (not_37_out, F12);
  not not_38 (not_38_out, OP2);
  not not_39 (not_39_out, OP3);
  not not_40 (not_40_out, OP5);
  not not_41 (not_41_out, OP6);
  not not_42 (not_42_out, F13);
  not not_43 (not_43_out, F14);
  not not_44 (not_44_out, OP2);
  not not_45 (not_45_out, OP3);
  not not_46 (not_46_out, OP5);
  not not_47 (not_47_out, OP6);
  not not_48 (not_48_out, F13);
  not not_49 (not_49_out, F25);
  not not_50 (not_50_out, OP2);
  not not_51 (not_51_out, OP3);
  not not_52 (not_52_out, OP5);
  not not_53 (not_53_out, OP6);
  not not_54 (not_54_out, OP3);
  not not_55 (not_55_out, OP6);
  not not_56 (not_56_out, OP2);
  not not_57 (not_57_out, OP3);
  not not_58 (not_58_out, OP5);
  not not_59 (not_59_out, OP6);
  not not_60 (not_60_out, F12);
  not not_61 (not_61_out, F13);
  not not_62 (not_62_out, OP2);
  not not_63 (not_63_out, OP3);
  not not_64 (not_64_out, OP5);
  not not_65 (not_65_out, OP6);
  not not_66 (not_66_out, F12);
  not not_67 (not_67_out, F14);
  not not_68 (not_68_out, OP2);
  not not_69 (not_69_out, OP3);
  not not_70 (not_70_out, OP5);
  not not_71 (not_71_out, OP6);
  not not_72 (not_72_out, F13);
  not not_73 (not_73_out, F14);
  not not_74 (not_74_out, OP2);
  not not_75 (not_75_out, OP3);
  not not_76 (not_76_out, OP5);
  not not_77 (not_77_out, OP6);
  not not_78 (not_78_out, F13);
  not not_79 (not_79_out, F25);
  not not_80 (not_80_out, OP2);
  not not_81 (not_81_out, OP3);
  not not_82 (not_82_out, OP6);
  not not_83 (not_83_out, F12);
  not not_84 (not_84_out, F14);
  not not_85 (not_85_out, F25);
  not not_86 (not_86_out, OP2);
  not not_87 (not_87_out, OP3);
  not not_88 (not_88_out, OP6);
  not not_89 (not_89_out, OP3);
  not not_90 (not_90_out, OP6);
  not not_91 (not_91_out, OP3);
  not not_92 (not_92_out, OP6);
  not not_93 (not_93_out, OP4);
  not not_94 (not_94_out, F12);
  not not_95 (not_95_out, F13);
  not not_96 (not_96_out, F14);
  not not_97 (not_97_out, OP3);
  not not_98 (not_98_out, OP6);
  not not_99 (not_99_out, OP4);
  not not_100 (not_100_out, OP2);
  not not_101 (not_101_out, OP3);
  not not_102 (not_102_out, F12);
  not not_103 (not_103_out, F13);
  not not_104 (not_104_out, F14);
  not not_105 (not_105_out, OP2);
  not not_106 (not_106_out, OP3);
  not not_107 (not_107_out, OP4);
  not not_108 (not_108_out, OP6);
  not not_109 (not_109_out, F12);
  not not_110 (not_110_out, F14);
  not not_111 (not_111_out, OP2);
  not not_112 (not_112_out, OP3);
  not not_113 (not_113_out, OP4);
  not not_114 (not_114_out, F12);
  not not_115 (not_115_out, F13);
  not not_116 (not_116_out, F14);
  not not_117 (not_117_out, OP2);
  not not_118 (not_118_out, OP3);
  not not_119 (not_119_out, OP4);
  not not_120 (not_120_out, F13);
  not not_121 (not_121_out, F14);
  not not_122 (not_122_out, OP4);
  not not_123 (not_123_out, OP3);
  not not_124 (not_124_out, OP4);
  not not_125 (not_125_out, F12);
  not not_126 (not_126_out, F13);
  not not_127 (not_127_out, F14);
  not not_128 (not_128_out, OP3);
  not not_129 (not_129_out, OP6);
  not not_130 (not_130_out, OP2);
  not not_131 (not_131_out, OP3);
  not not_132 (not_132_out, OP4);
  not not_133 (not_133_out, OP5);
  not not_134 (not_134_out, OP6);
  not not_135 (not_135_out, F12);
  not not_136 (not_136_out, F13);
  not not_137 (not_137_out, OP2);
  not not_138 (not_138_out, OP3);
  not not_139 (not_139_out, OP4);
  not not_140 (not_140_out, F13);
  and and_1 (and_1_out, not_1_out, not_2_out, not_3_out, not_4_out, not_5_out, not_6_out, not_7_out, F14);
  and and_2 (and_2_out, not_8_out, not_9_out, not_10_out, not_11_out, not_12_out, not_13_out, F13, not_14_out);
  and and_3 (MemWrite, not_15_out, not_16_out, not_17_out, OP5, not_18_out, not_19_out, F13, not_20_out);
  and and_4 (and_4_out, not_21_out, not_22_out, not_23_out, not_24_out, not_25_out, not_26_out, F14);
  and and_5 (and_5_out, not_27_out, not_28_out, not_29_out, not_30_out, not_31_out, F13, not_32_out);
  and and_6 (and_6_out, not_33_out, not_34_out, OP4, not_35_out, not_36_out, not_37_out);
  and and_7 (and_7_out, not_38_out, not_39_out, OP4, not_40_out, not_41_out, not_42_out, not_43_out);
  and and_8 (and_8_out, not_44_out, not_45_out, OP4, not_46_out, not_47_out, not_48_out, not_49_out);
  and and_9 (and_9_out, not_50_out, not_51_out, OP4, not_52_out, not_53_out, F13, F14);
  and and_10 (and_10_out, OP2, not_54_out, OP4, OP5, not_55_out);
  and and_11 (and_11_out, not_56_out, not_57_out, not_58_out, not_59_out, not_60_out, not_61_out, F14);
  and and_12 (and_12_out, not_62_out, not_63_out, not_64_out, not_65_out, not_66_out, F13, not_67_out);
  and and_13 (and_13_out, not_68_out, not_69_out, OP4, not_70_out, not_71_out, not_72_out, not_73_out);
  and and_14 (and_14_out, not_74_out, not_75_out, OP4, not_76_out, not_77_out, not_78_out, not_79_out);
  and and_15 (and_15_out, not_80_out, not_81_out, OP4, not_82_out, not_83_out, not_84_out, not_85_out);
  and and_16 (and_16_out, not_86_out, not_87_out, OP4, not_88_out, F13, F14);
  and and_17 (and_17_out, not_89_out, OP4, OP5, not_90_out, F13);
  and and_18 (and_18_out, not_91_out, OP4, OP5, not_92_out, F12, F14);
  and and_19 (and_19_out, OP2, not_93_out, OP5, OP6, not_94_out, not_95_out, not_96_out);
  and and_20 (and_20_out, OP2, not_97_out, OP4, OP5, not_98_out);
  and and_21 (and_21_out, OP2, OP3, not_99_out, OP5, OP6);
  and and_22 (ecall, not_100_out, not_101_out, OP4, OP5, OP6, not_102_out, not_103_out, not_104_out);
  and and_23 (S_Type, not_105_out, not_106_out, not_107_out, OP5, not_108_out, not_109_out, F13, not_110_out);
  and and_24 (BEQ, not_111_out, not_112_out, not_113_out, OP5, OP6, not_114_out, not_115_out, not_116_out);
  and and_25 (BNE, not_117_out, not_118_out, not_119_out, OP5, OP6, F12, not_120_out, not_121_out);
  and and_26 (JAL, OP2, OP3, not_122_out, OP5, OP6);
  and and_27 (JALR, OP2, not_123_out, not_124_out, OP5, OP6, not_125_out, not_126_out, not_127_out);
  and and_28 (LUI, OP2, not_128_out, OP4, OP5, not_129_out);
  and and_29 (LBU, not_130_out, not_131_out, not_132_out, not_133_out, not_134_out, not_135_out, not_136_out, F14);
  and and_30 (BGE, not_137_out, not_138_out, not_139_out, OP5, OP6, F12, not_140_out, F14);
  or or_1 (MemToReg, and_1_out, and_2_out);
  or or_2 (ALU_SRC, and_4_out, and_5_out, and_6_out, and_7_out, and_8_out, and_9_out, and_10_out);
  or or_3 (RegWrite, and_11_out, and_12_out, and_13_out, and_14_out, and_15_out, and_16_out, and_17_out, and_18_out, and_19_out, and_20_out, and_21_out);
endmodule

module \中断信号自动生成  (
  input  OP2,
  input  OP3,
  input  OP4,
  input  OP5,
  input  OP6,
  input  F12,
  input  F13,
  input  F14,
  input  F25,
  input  F30,
  output csrrsi,
  output csrrci
);

  wire not_1_out, not_2_out, not_3_out, not_4_out, not_5_out;

  not not_1 (not_1_out, F12);
  not not_2 (not_2_out, OP3);
  not not_3 (not_3_out, OP2);
  not not_4 (not_4_out, OP3);
  not not_5 (not_5_out, OP2);
  and and_1 (csrrsi, F14, F13, not_1_out, OP6, OP5, OP4, not_2_out, not_3_out);
  and and_2 (csrrci, F14, F13, F12, OP6, OP5, OP4, not_4_out, not_5_out);
endmodule

// ALU
module ALU (
  input  [31:0] X,
  input  [31:0] Y,
  input  [3:0] AluOP,
  output out_4,
  output Equal,
  output out_6,
  output [31:0] Result,
  output [31:0] Result_2
);

  wire [0:0] comparator_1_lt, comparator_2_lt;
  wire [31:0] adder_1_out, AND_out, divider_1_out, divider_1_rem, multiplier_1_cout, multiplier_1_out,
       NOR_out, OR_out, shifter_1_out, shifter_2_out, shifter_3_out, shifter_4_out, subtractor_1_out, XOR_out;

  assign AND_out = X & Y;  // AND_Gate AND, 32 bits wide
  assign OR_out = X | Y;  // OR_Gate OR, 32 bits wide
  Shifter #(.width(32), .shift("ll")) shifter_1 (.in(X), .\dist (Y[4:0]), .out(shifter_1_out));
  Shifter #(.width(32), .shift("ar")) shifter_2 (.in(X), .\dist (Y[4:0]), .out(shifter_2_out));
  Shifter #(.width(32), .shift("lr")) shifter_3 (.in(X), .\dist (Y[4:0]), .out(shifter_3_out));
  Multiplier #(.width(32)) multiplier_1 (.a(X), .b(Y), .out(multiplier_1_out), .cout(multiplier_1_cout));  // open: cin
  Divider #(.width(32)) divider_1 (.a(X), .b(Y), .out(divider_1_out), .rem(divider_1_rem));  // open: upper
  Adder #(.width(32)) adder_1 (.a(X), .b(Y), .out(adder_1_out));  // open: cin, cout
  Subtractor #(.width(32)) subtractor_1 (.a(X), .b(Y), .out(subtractor_1_out));  // open: bin, bout
  assign XOR_out = X ^ Y;  // XOR_Gate XOR, 32 bits wide
  assign NOR_out = ~(X | Y);  // NOR_Gate NOR, 32 bits wide
  Comparator #(.width(32), .mode("twosComplement")) comparator_1 (
    .a(X), .b(Y), .eq(Equal), .lt(comparator_1_lt[0]));  // open: gt
  Comparator #(.width(32), .mode("unsigned")) comparator_2 (.a(X), .b(Y), .lt(comparator_2_lt[0]));  // open: gt, eq
  Shifter #(.width(32), .shift("ll")) shifter_4 (.in(Y), .\dist (5'b01100), .out(shifter_4_out));
  Multiplexer #(.select(4), .width(32), .disabled("Z"), .enable("false")) multiplexer_1 (
    .in0(shifter_1_out), .in1(shifter_2_out), .in2(shifter_3_out), .in3(multiplier_1_out),
    .in4(divider_1_out), .in5(adder_1_out), .in6(subtractor_1_out), .in7(AND_out), .in8(OR_out),
    .in9(XOR_out), .in10(NOR_out), .in11({{31{1'b0}}, comparator_1_lt[0]}),
    .in12({{31{1'b0}}, comparator_2_lt[0]}), .in13(shifter_4_out), .in14({32{1'b0}}), .in15({32{1'b0}}),
    .out(Result), .sel(AluOP));
  Multiplexer #(.select(4), .width(32), .disabled("Z"), .enable("false")) multiplexer_2 (
    .in0({32{1'b0}}), .in1({32{1'b0}}), .in2({32{1'b0}}), .in3(multiplier_1_cout), .in4(divider_1_rem),
    .in5({32{1'b0}}), .in6({32{1'b0}}), .in7({32{1'b0}}), .in8({32{1'b0}}), .in9({32{1'b0}}),
    .in10({32{1'b0}}), .in11({32{1'b0}}), .in12({32{1'b0}}), .in13({32{1'b0}}), .in14({32{1'b0}}),
    .in15({32{1'b0}}), .out(Result_2), .sel(AluOP));
  Multiplexer #(.select(4), .width(1), .disabled("Z"), .enable("false")) multiplexer_3 (
    .in0(1'b0), .in1(1'b0), .in2(1'b0), .in3(1'b0), .in4(1'b0), .in5(1'b0), .in6(1'b0), .in7(1'b0),
    .in8(1'b0), .in9(1'b0), .in10(1'b0), .in11(comparator_1_lt[0]), .in12(comparator_2_lt[0]), .in13(1'b0),
    .in14(1'b0), .in15(1'b0), .out(out_6), .sel(AluOP));
  not not_1 (out_4, out_6);

  // Other names for the same wires on the sheet: Result2[31:0] = Result_2; S[3:0] = AluOP; tunnel = out_6;
  //   tunnel_t = out_4

  // Notes on the sheet:
  //   不要改变此引脚区域内容，也不要改变ALU封装形式
  //   输入引脚
  //   输出引脚
endmodule

module Regifile (
  input  [31:0] Din,
  input  Clk,
  input  WE,
  input  [4:0] R1_num,
  input  [4:0] W_num,
  input  [4:0] R2_num,
  output [31:0] R1,
  output [31:0] R2
);

  // RegisterFile registerfile_1: pin names not known; wires that end beside it: Din, Clk, WE, W_num, R1_num, R2_num, R1, R2
endmodule

module \中断按键参考电路  (
  input  \中断 ,
  input  \同步清零信号 ,
  output \与中断屏蔽位与 
);

  wire and_1_out, clock_1_out, d_ff_1_q, or_1_out, or_2_out;

  Clock #(.highDuration(1), .lowDuration(1)) clock_1 (.out(clock_1_out));
  or or_1 (or_1_out, \与中断屏蔽位与 , d_ff_1_q);
  LED #(.active("true")) \_1号中断等待指示灯  (.in(or_1_out));
  D_Flip_Flop #(.trigger("rising"), .Pre_Clr_Positions("LEGACY"), .NegatePresetClear("false"), .enable("true"), .NewFFLayout("false")) d_ff_1 (
    .clk(\中断 ), .D(1'b1), .Q(d_ff_1_q), .reset(\与中断屏蔽位与 ));  // open: Qn, preset, en
  or or_2 (or_2_out, d_ff_1_q, \与中断屏蔽位与 );
  and and_1 (and_1_out, or_2_out, ~\同步清零信号 );  // AND_Gate
  D_Flip_Flop #(.trigger("rising"), .Pre_Clr_Positions("LEGACY"), .NegatePresetClear("false"), .enable("true"), .NewFFLayout("false")) IR1 (
    .clk(clock_1_out), .D(and_1_out), .Q(\与中断屏蔽位与 ));  // open: Qn, preset, en, reset

  // Notes on the sheet:
  //   中断信号采样参考电路
  //   Reset 
endmodule

module \单周期_多级中断  (
  input  IR1,
  input  IR2,
  input  IR3,
  output RegWrite,
  output MemWrite,
  output [31:0] PC,
  output [31:0] IR,
  output [31:0] RDin,
  output [31:0] MDin,
  output [31:0] LedData
);

  wire \_1号中断请求信号 , \_1号同步清零信号 , \_2号中断请求信号 , \_2号同步清零信号 , \_3号中断请求信号 , \_3号同步清零信号 , alu_1_equal,
       alu_1_out_4, and_1_out, and_2_out, and_3_out, and_4_out, and_5_out, and_6_out, and_7_out, and_8_out,
       and_10_out, B_type, CLK, clock_1_out, comparator_1_eq, comparator_2_eq, comparator_3_eq,
       comparator_4_eq, comparator_5_eq, comparator_6_gt, comparator_7_eq, comparator_8_eq, comparator_8_lt,
       d_ff_1_q, d_ff_2_q, d_ff_3_q, d_ff_4_q, d_ff_5_q, demultiplexer_1_out1, demultiplexer_1_out2,
       demultiplexer_1_out3, demultiplexer_2_out1, demultiplexer_2_out2, demultiplexer_2_out3, Go, I_type,
       IE_q, ini, IR1_t, IR2_t, IR3_t, IRA, IRB, IRC, ISR1_q, ISR2_q, ISR3_q, J_typpe, nand_1_out, nor_2_out,
       not_1_out, not_2_out, not_3_out, not_4_out, not_5_out, not_6_out, or_1_out, or_2_out, or_3_out,
       or_4_out, or_5_out, or_6_out, or_7_out, or_13_out, or_14_out, or_15_out, or_18_out, or_19_out,
       or_20_out, pull_resistor_1_node, pull_resistor_2_node, pull_resistor_3_node, S_type, stop, U_type, W1,
       W2, W3, \单周期硬布线控制器_封装2_1_alu_src , \单周期硬布线控制器_封装2_1_beq , \单周期硬布线控制器_封装2_1_bge ,
       \单周期硬布线控制器_封装2_1_bne , \单周期硬布线控制器_封装2_1_csrrci , \单周期硬布线控制器_封装2_1_csrrsi , \单周期硬布线控制器_封装2_1_ecall ,
       \单周期硬布线控制器_封装2_1_jalr , \单周期硬布线控制器_封装2_1_lbu , \单周期硬布线控制器_封装2_1_memtoreg , \单周期硬布线控制器_封装2_1_uret ;
  wire [1:0] priority_encoder_1_out, priority_encoder_2_out;
  wire [3:0] \单周期硬布线控制器_封装2_1_alu_op ;
  wire [4:0] multiplexer_8_out, multiplexer_9_out;
  wire [7:0] multiplexer_12_out, ram_1_data, ram_1_data_2, ram_1_data_3, ram_1_data_4;
  wire [12:0] CNT_num;
  wire [15:0] \总周期数 ;
  wire [31:0] adder_1_out, adder_2_out, adder_3_out, alu_1_result, and_9_out, bit_extender_1_out,
       bit_extender_2_out, bit_extender_3_out, bit_extender_4_out, bit_extender_5_out, bit_extender_6_out,
       controlled_buffer_1_out, mEPC_2_q, mEPC_3_q, mEPC_q, multiplexer_1_out, multiplexer_2_out,
       multiplexer_3_out, multiplexer_4_out, multiplexer_5_out, multiplexer_6_out, multiplexer_7_out,
       multiplexer_10_out, multiplexer_11_out, multiplexer_13_out, regifile_1_r1, shifter_1_out;

  Button \u_继续运行  (.out(Go));
  Button _1 (.out(IRA));
  Button _2 (.out(IRB));
  Button _3 (.out(IRC));
  LED #(.active("true")) led_1 (.in(W1));
  LED #(.active("true")) led_2 (.in(W2));
  LED #(.active("true")) led_3 (.in(W3));
  Multiplexer #(.select(1), .width(32), .disabled("Z"), .enable("false")) multiplexer_1 (
    .in0(adder_1_out), .in1(and_9_out), .out(multiplexer_1_out), .sel(or_19_out));
  Hex_Digit_Display hex_digit_display_1 (.value(LedData[31:28]));  // open: dp
  Priority_Encoder #(.select(2), .disabled("Z")) priority_encoder_1 (
    .in0(1'b1), .in1(\_1号中断请求信号 ), .in2(\_2号中断请求信号 ), .in3(\_3号中断请求信号 ), .out(priority_encoder_1_out));  // open: gs, en_out, en_in
  Comparator #(.width(16), .mode("twosComplement")) comparator_1 (
    .a(\总周期数 ), .b(16'h7), .eq(comparator_1_eq));  // open: gt, lt
  Comparator #(.width(16), .mode("twosComplement")) comparator_2 (
    .a(\总周期数 ), .b(16'h241), .eq(comparator_2_eq));  // open: gt, lt
  Hex_Digit_Display hex_digit_display_2 (.value(LedData[23:20]));  // open: dp
  Hex_Digit_Display hex_digit_display_3 (.value(LedData[27:24]));  // open: dp
  Demultiplexer #(.select(2), .width(1), .tristate("false"), .disabled(0), .enable("false")) demultiplexer_1 (
    .out1(demultiplexer_1_out1), .out2(demultiplexer_1_out2), .out3(demultiplexer_1_out3),
    .in(\单周期硬布线控制器_封装2_1_uret ), .sel(priority_encoder_2_out));  // open: out0
  Comparator #(.width(16), .mode("twosComplement")) comparator_3 (
    .a(16'h258), .b(\总周期数 ), .eq(comparator_3_eq));  // open: gt, lt
  or or_1 (or_1_out, comparator_3_eq, comparator_4_eq);
  Comparator #(.width(16), .mode("twosComplement")) comparator_4 (
    .a(\总周期数 ), .b(16'h1), .eq(comparator_4_eq));  // open: gt, lt
  Comparator #(.width(16), .mode("twosComplement")) comparator_5 (
    .a(\总周期数 ), .b(16'h4), .eq(comparator_5_eq));  // open: gt, lt
  or or_2 (or_2_out, comparator_1_eq, comparator_2_eq);
  Hex_Digit_Display hex_digit_display_4 (.value(LedData[19:16]));  // open: dp
  Hex_Digit_Display hex_digit_display_5 (.value(LedData[15:12]));  // open: dp
  Multiplexer #(.select(2), .width(32), .disabled("Z"), .enable("false")) multiplexer_2 (
    .in1(32'h30ac), .in2(32'h3158), .in3(32'h3204), .out(multiplexer_2_out), .sel(priority_encoder_1_out));  // open: in0
  Demultiplexer #(.select(2), .width(1), .tristate("false"), .disabled(0), .enable("false")) demultiplexer_2 (
    .out1(demultiplexer_2_out1), .out2(demultiplexer_2_out2), .out3(demultiplexer_2_out3), .in(and_1_out),
    .sel(priority_encoder_1_out));  // open: out0
  Pull_Resistor #(.pull(0)) pull_resistor_1 (.node(pull_resistor_1_node));
  assign pull_resistor_1_node = or_1_out ? ~CLK : 1'bz;  // Controlled_Inverter controlled_inverter_1
  Pull_Resistor #(.pull(0)) pull_resistor_2 (.node(pull_resistor_2_node));
  assign pull_resistor_2_node = comparator_5_eq ? ~CLK : 1'bz;  // Controlled_Inverter controlled_inverter_2
  Pull_Resistor #(.pull(0)) pull_resistor_3 (.node(pull_resistor_3_node));
  assign pull_resistor_3_node = or_2_out ? ~CLK : 1'bz;  // Controlled_Inverter controlled_inverter_3
  Hex_Digit_Display hex_digit_display_6 (.value(LedData[11:8]));  // open: dp
  Hex_Digit_Display hex_digit_display_7 (.value(LedData[7:4]));  // open: dp
  // Probe on \总周期数 
  Comparator #(.width(2), .mode("unsigned")) comparator_6 (
    .a(priority_encoder_1_out), .b(priority_encoder_2_out), .gt(comparator_6_gt));  // open: eq, lt
  not not_1 (not_1_out, ISR1_q);
  or or_3 (or_3_out, demultiplexer_2_out1, demultiplexer_1_out1);
  not not_2 (not_2_out, ISR2_q);
  or or_4 (or_4_out, demultiplexer_2_out2, demultiplexer_1_out2);
  not not_3 (not_3_out, ISR3_q);
  or or_5 (or_5_out, demultiplexer_1_out3, demultiplexer_2_out3);
  Hex_Digit_Display hex_digit_display_8 (.value(LedData[3:0]));  // open: dp
  Register #(.width(1), .trigger("rising"), .Select("low")) IE (
    .D(not_4_out), .en(or_6_out), .Q(IE_q), .clk(CLK), .preset(ini));  // open: clr, cs
  or or_6 (or_6_out, \单周期硬布线控制器_封装2_1_uret , \单周期硬布线控制器_封装2_1_csrrsi , \单周期硬布线控制器_封装2_1_csrrci , and_1_out);
  not not_4 (not_4_out, IE_q);
  or or_7 (or_7_out, \单周期硬布线控制器_封装2_1_uret , and_1_out);
  Register #(.width(1), .trigger("rising"), .Select("low")) ISR1 (
    .D(not_1_out), .en(or_3_out), .Q(ISR1_q), .clk(CLK));  // open: clr
  Register #(.width(1), .trigger("rising"), .Select("low")) ISR2 (
    .D(not_2_out), .en(or_4_out), .Q(ISR2_q), .clk(CLK));  // open: clr
  Register #(.width(1), .trigger("rising"), .Select("low")) ISR3 (
    .D(not_3_out), .en(or_5_out), .Q(ISR3_q), .clk(CLK));  // open: clr
  and and_1 (and_1_out, comparator_6_gt, IE_q);
  Priority_Encoder #(.select(2), .disabled("Z")) priority_encoder_2 (
    .in0(1'b1), .in1(ISR1_q), .in2(ISR2_q), .in3(ISR3_q), .out(priority_encoder_2_out));  // open: gs, en_out, en_in
  LED #(.active("true")) \_1号中断等待指示灯  (.in(W1));
  LED #(.active("true")) \_2号中断等待指示灯  (.in(W2));
  LED #(.active("true")) \_3号中断等待指示灯  (.in(W3));
  or or_8 (IR1_t, IR1, IRA);
  Multiplexer #(.select(1), .width(32), .disabled("Z"), .enable("false")) multiplexer_3 (
    .in0(multiplexer_1_out), .in1(mEPC_2_q), .out(multiplexer_3_out), .sel(\单周期硬布线控制器_封装2_1_uret ));
  Multiplexer #(.select(1), .width(32), .disabled("Z"), .enable("false")) multiplexer_4 (
    .in0(mEPC_q), .in1(mEPC_3_q), .out(multiplexer_4_out), .sel(\单周期硬布线控制器_封装2_1_uret ));
  Multiplexer #(.select(1), .width(32), .disabled("Z"), .enable("false")) multiplexer_5 (
    .in0(mEPC_2_q), .in1({32{1'b1}}), .out(multiplexer_5_out), .sel(\单周期硬布线控制器_封装2_1_uret ));
  or or_9 (W1, \_1号中断请求信号 , d_ff_1_q);
  or or_10 (W2, \_2号中断请求信号 , d_ff_2_q);
  or or_11 (W3, \_3号中断请求信号 , d_ff_3_q);
  or or_12 (IR2_t, IR2, IRB);
  Multiplexer #(.select(1), .width(32), .disabled("Z"), .enable("false")) multiplexer_6 (
    .in0(multiplexer_1_out), .in1(multiplexer_2_out), .out(multiplexer_6_out), .sel(and_1_out));
  Multiplexer #(.select(1), .width(32), .disabled("Z"), .enable("false")) multiplexer_7 (
    .in0(multiplexer_6_out), .in1(mEPC_q), .out(multiplexer_7_out), .sel(\单周期硬布线控制器_封装2_1_uret ));
  Register #(.width(32), .trigger("rising"), .Select("low")) mEPC (
    .D(multiplexer_3_out), .en(or_7_out), .Q(mEPC_q), .clk(CLK));  // open: clr
  Register #(.width(32), .trigger("rising"), .Select("low")) mEPC_2 (
    .D(multiplexer_4_out), .en(or_7_out), .Q(mEPC_2_q), .clk(CLK));  // open: clr
  Register #(.width(32), .trigger("rising"), .Select("low")) mEPC_3 (
    .D(multiplexer_5_out), .en(or_7_out), .Q(mEPC_3_q), .clk(CLK));  // open: clr
  D_Flip_Flop #(.trigger("rising"), .Pre_Clr_Positions("LEGACY"), .NegatePresetClear("false"), .enable("true"), .NewFFLayout("false")) d_ff_1 (
    .clk(IR1_t), .D(1'b1), .Q(d_ff_1_q), .reset(\_1号中断请求信号 ));  // open: Qn, preset, en
  D_Flip_Flop #(.trigger("rising"), .Pre_Clr_Positions("LEGACY"), .NegatePresetClear("false"), .enable("true"), .NewFFLayout("false")) d_ff_2 (
    .clk(IR2_t), .D(1'b1), .Q(d_ff_2_q), .reset(\_2号中断请求信号 ));  // open: Qn, preset, en
  D_Flip_Flop #(.trigger("rising"), .Pre_Clr_Positions("LEGACY"), .NegatePresetClear("false"), .enable("true"), .NewFFLayout("false")) d_ff_3 (
    .clk(IR3_t), .D(1'b1), .Q(d_ff_3_q), .reset(\_3号中断请求信号 ));  // open: Qn, preset, en
  Register #(.width(32), .trigger("rising"), .Select("low")) u_PC (
    .D(multiplexer_7_out), .en(stop), .Q(PC), .clk(CLK));  // open: clr
  or or_13 (or_13_out, d_ff_1_q, \_1号中断请求信号 );
  or or_14 (or_14_out, d_ff_2_q, \_2号中断请求信号 );
  or or_15 (or_15_out, d_ff_3_q, \_3号中断请求信号 );
  or or_16 (IR3_t, IR3, IRC);
  and and_2 (and_2_out, or_13_out, ~\_1号同步清零信号 );  // AND_Gate
  and and_3 (and_3_out, or_14_out, ~\_2号同步清零信号 );  // AND_Gate
  and and_4 (and_4_out, or_15_out, ~\_3号同步清零信号 );  // AND_Gate
  Demultiplexer #(.select(2), .width(1), .tristate("false"), .disabled(0), .enable("false")) demultiplexer_3 (
    .out1(\_1号同步清零信号 ), .out2(\_2号同步清零信号 ), .out3(\_3号同步清零信号 ), .in(\单周期硬布线控制器_封装2_1_uret ),
    .sel(priority_encoder_2_out));  // open: out0
  Adder #(.width(32)) adder_1 (.a(PC), .b(32'h4), .out(adder_1_out));  // open: cin, cout
  D_Flip_Flop #(.trigger("rising"), .Pre_Clr_Positions("LEGACY"), .NegatePresetClear("false"), .enable("true"), .NewFFLayout("false")) u_IR1 (
    .clk(CLK), .D(and_2_out), .Q(\_1号中断请求信号 ));  // open: Qn, preset, en, reset
  D_Flip_Flop #(.trigger("rising"), .Pre_Clr_Positions("LEGACY"), .NegatePresetClear("false"), .enable("true"), .NewFFLayout("false")) u_IR2 (
    .clk(CLK), .D(and_3_out), .Q(\_2号中断请求信号 ));  // open: Qn, preset, en, reset
  D_Flip_Flop #(.trigger("rising"), .Pre_Clr_Positions("LEGACY"), .NegatePresetClear("false"), .enable("true"), .NewFFLayout("false")) u_IR3 (
    .clk(CLK), .D(and_4_out), .Q(\_3号中断请求信号 ));  // open: Qn, preset, en, reset
  // RiscV_Probe riscv_probe_1: pin names not known; wires that end beside it: IR, RegWrite
  ROM #(.addrWidth(10), .dataWidth(32), .Select("high")) rom_1 (.addr(PC[11:2]), .data(IR));
  \单周期硬布线控制器_封装2  \u_单周期硬布线控制器_封装2_1  (
    .OP(IR[6:2]), .Funct({IR[30], IR[25], IR[14:12]}), .in_3(IR[21]), .ALU_OP(\单周期硬布线控制器_封装2_1_alu_op ),
    .uret(\单周期硬布线控制器_封装2_1_uret ), .MemToReg(\单周期硬布线控制器_封装2_1_memtoreg ), .ecall(\单周期硬布线控制器_封装2_1_ecall ),
    .MemWrite(MemWrite), .ALU_SRC(\单周期硬布线控制器_封装2_1_alu_src ), .RegWrite(RegWrite), .S_type(S_type),
    .Beq(\单周期硬布线控制器_封装2_1_beq ), .Bne(\单周期硬布线控制器_封装2_1_bne ), .Jalr(\单周期硬布线控制器_封装2_1_jalr ), .JAL(J_typpe),
    .LUI(U_type), .LBU(\单周期硬布线控制器_封装2_1_lbu ), .BGE(\单周期硬布线控制器_封装2_1_bge ),
    .csrrsi(\单周期硬布线控制器_封装2_1_csrrsi ), .csrrci(\单周期硬布线控制器_封装2_1_csrrci ));
  Multiplexer #(.select(1), .width(5), .disabled("Z"), .enable("false")) multiplexer_8 (
    .in0(IR[19:15]), .in1(5'b10001), .out(multiplexer_8_out), .sel(\单周期硬布线控制器_封装2_1_ecall ));
  Multiplexer #(.select(1), .width(5), .disabled("Z"), .enable("false")) multiplexer_9 (
    .in0(IR[24:20]), .in1(5'b01010), .out(multiplexer_9_out), .sel(\单周期硬布线控制器_封装2_1_ecall ));
  assign bit_extender_1_out = {{20{IR[31]}}, IR[31:20]};  // Bit_Extender bit_extender_1
  assign bit_extender_2_out = {{20{IR[31]}}, {IR[31:25], IR[11:7]}};  // Bit_Extender bit_extender_2
  assign bit_extender_3_out = {{20{IR[31]}}, {IR[31], IR[7], IR[30:25], IR[11:8]}};  // Bit_Extender bit_extender_3
  assign bit_extender_4_out = {{12{IR[31]}}, {IR[31], IR[19:12], IR[20], IR[30:21]}};  // Bit_Extender bit_extender_4
  assign bit_extender_5_out = {{12{IR[31]}}, IR[31:12]};  // Bit_Extender bit_extender_5
  assign controlled_buffer_1_out = I_type ? bit_extender_1_out : 32'bz;  // Controlled_Buffer controlled_buffer_1
  assign controlled_buffer_1_out = S_type ? bit_extender_2_out : 32'bz;  // Controlled_Buffer controlled_buffer_2
  assign controlled_buffer_1_out = B_type ? bit_extender_3_out : 32'bz;  // Controlled_Buffer controlled_buffer_3
  assign controlled_buffer_1_out = J_typpe ? bit_extender_4_out : 32'bz;  // Controlled_Buffer controlled_buffer_4
  assign controlled_buffer_1_out = U_type ? bit_extender_5_out : 32'bz;  // Controlled_Buffer controlled_buffer_5
  or or_17 (B_type, \单周期硬布线控制器_封装2_1_beq , \单周期硬布线控制器_封装2_1_bne , \单周期硬布线控制器_封装2_1_bge );
  Regifile regifile_1 (
    .Din(RDin), .Clk(CLK), .R1(regifile_1_r1), .R2(MDin), .WE(RegWrite), .W_num(IR[11:7]),
    .R1_num(multiplexer_8_out), .R2_num(multiplexer_9_out));
  nor nor_1 (I_type, S_type, B_type, J_typpe, U_type);
  D_Flip_Flop #(.trigger("high"), .Pre_Clr_Positions("LEGACY"), .NegatePresetClear("false"), .enable("true"), .NewFFLayout("false")) d_ff_4 (.Q(d_ff_4_q));  // open: clk, D, Qn, preset, en, reset
  // Probe on 13'hc
  Comparator #(.width(32), .mode("twosComplement")) comparator_7 (
    .a(regifile_1_r1), .b(32'h22), .eq(comparator_7_eq));  // open: gt, lt
  Comparator #(.width(13), .mode("twosComplement")) comparator_8 (
    .a(CNT_num), .b(13'hc), .eq(comparator_8_eq), .lt(comparator_8_lt));  // open: gt
  Clock #(.highDuration(1), .lowDuration(1)) clock_1 (.out(clock_1_out));
  Multiplexer #(.select(1), .width(32), .disabled("Z"), .enable("false")) multiplexer_10 (
    .in0(MDin), .in1(controlled_buffer_1_out), .out(multiplexer_10_out), .sel(\单周期硬布线控制器_封装2_1_alu_src ));
  Shifter #(.width(32), .shift("ll")) shifter_1 (.in(controlled_buffer_1_out), .\dist (5'b00001), .out(shifter_1_out));
  Multiplexer #(.select(1), .width(32), .disabled("Z"), .enable("false")) multiplexer_11 (
    .in0(PC), .in1(regifile_1_r1), .out(multiplexer_11_out), .sel(\单周期硬布线控制器_封装2_1_jalr ));
  not not_5 (not_5_out, comparator_7_eq);
  Counter #(.width(13), .max('h1fff), .ongoal("stay"), .trigger("rising"), .behavior("old")) counter_1 (
    .count(comparator_8_lt), .Q(CNT_num), .clk(clock_1_out));  // open: load, D, carry, clr, preset
  ALU alu_1 (
    .X(regifile_1_r1), .Y(multiplexer_10_out), .AluOP(\单周期硬布线控制器_封装2_1_alu_op ), .Equal(alu_1_equal),
    .Result(alu_1_result), .out_4(alu_1_out_4));  // open: Result_2, out_6
  Adder #(.width(32)) adder_2 (.a(shifter_1_out), .b(multiplexer_11_out), .out(adder_2_out));  // open: cin, cout
  Register #(.width(32), .trigger("rising"), .Select("low")) \Led寄存器  (
    .D(MDin), .en(and_5_out), .Q(LedData), .clk(CLK));  // open: clr
  and and_5 (and_5_out, comparator_7_eq, \单周期硬布线控制器_封装2_1_ecall );
  and and_6 (and_6_out, \单周期硬布线控制器_封装2_1_ecall , not_5_out);
  nand nand_1 (nand_1_out, d_ff_4_q, comparator_8_eq);
  not not_6 (not_6_out, alu_1_equal);
  and and_7 (and_7_out, alu_1_out_4, \单周期硬布线控制器_封装2_1_bge );
  and and_8 (and_8_out, not_6_out, \单周期硬布线控制器_封装2_1_bne );
  assign and_9_out = adder_2_out & 32'hfffffffe;  // AND_Gate and_9, 32 bits wide
  assign CLK = nand_1_out ? clock_1_out : 1'bz;  // Controlled_Buffer controlled_buffer_6
  Pull_Resistor #(.pull(1)) pull_resistor_4 (.node(CLK));
  and and_10 (and_10_out, alu_1_equal, \单周期硬布线控制器_封装2_1_beq );
  or or_18 (or_18_out, d_ff_5_q, and_6_out);
  or or_19 (or_19_out, J_typpe, \单周期硬布线控制器_封装2_1_jalr , and_10_out, and_8_out, and_7_out);
  Adder #(.width(32)) adder_3 (.a(32'h4), .b(PC), .out(adder_3_out));  // open: cin, cout
  D_Flip_Flop #(.trigger("falling"), .Pre_Clr_Positions("ABOVE_BELOW"), .NegatePresetClear("false"), .enable("false"), .NewFFLayout("true")) d_ff_5 (
    .clk(CLK), .D(or_18_out), .Q(d_ff_5_q), .reset(Go));  // open: Qn, preset
  not not_7 (stop, d_ff_5_q);
  RAM #(.addrWidth(10), .dataWidth(32), .bus("separate"), .Select("high")) ram_1 (
    .addr(alu_1_result[11:2]), .din(MDin), .data({ram_1_data_4, ram_1_data_3, ram_1_data_2, ram_1_data}),
    .str(MemWrite), .sel(stop), .clk(CLK));  // open: ld, clr
  Multiplexer #(.select(2), .width(8), .disabled("Z"), .enable("false")) multiplexer_12 (
    .in0(ram_1_data), .in1(ram_1_data_2), .in2(ram_1_data_3), .in3(ram_1_data_4), .out(multiplexer_12_out),
    .sel(alu_1_result[1:0]));
  assign bit_extender_6_out = {{24{1'b0}}, multiplexer_12_out};  // Bit_Extender bit_extender_6
  Counter #(.width(16), .max('hffff), .ongoal("stay"), .trigger("rising"), .behavior("new")) counter_2 (
    .count(stop), .Q(\总周期数 ), .clk(CLK));  // open: load, D, carry, clr, preset, down
  Multiplexer #(.select(1), .width(32), .disabled("Z"), .enable("false")) multiplexer_13 (
    .in0({ram_1_data_4, ram_1_data_3, ram_1_data_2, ram_1_data}), .in1(bit_extender_6_out),
    .out(multiplexer_13_out), .sel(\单周期硬布线控制器_封装2_1_lbu ));
  Comparator #(.width(16), .mode("twosComplement")) comparator_9 (
    .a({16{1'b0}}), .b(\总周期数 ), .eq(ini));  // open: gt, lt
  or or_20 (or_20_out, \单周期硬布线控制器_封装2_1_jalr , J_typpe);
  nor nor_2 (nor_2_out, \单周期硬布线控制器_封装2_1_memtoreg , or_20_out);
  assign RDin = nor_2_out ? alu_1_result : 32'bz;  // Controlled_Buffer controlled_buffer_7
  assign RDin = \单周期硬布线控制器_封装2_1_memtoreg  ? multiplexer_13_out : 32'bz;  // Controlled_Buffer controlled_buffer_8
  assign RDin = or_20_out ? adder_3_out : 32'bz;  // Controlled_Buffer controlled_buffer_9

  // Notes on the sheet:
  //   中断源
  //   中断等待指示
  //   总复位信号应将除ROM以外所有存储组件全部清零
  //   中断优先级 1 < 2 < 3，
  //   多级中断测试信号模拟器
  //   中断编号
  //   IntR&IE
  //   uret
  //   数码管输出
  //   2位无符号
  //   中断编号
  //   数码管输出应该用寄存器锁存，否则显示数据只能一闪而过
  //   csrrsi
  //   csrrci
  //   中断请求
  //   IntR&IE
  //   IE 用于开关中断，1 表示开中断，0 表是关中断
  //   IE寄存器建议采用同步置位和复位方式
  //   IntR&IE
  //   uret
  //   中断编号
  //   指令存储器
  //   Reset 
  //   Reset 
  //   Reset 
  //   pc+4
  //   $a7
  //   contents of rom_1 (hex, n*v repeats v):
  //   7d000113 100413 1f41993 41f9d993 433 c00913 800b13 140413 f47413 800293 100313 499993 89e9b3 1300533
  //   2200893 73 406282b3 fe0294e3 140413 f00f93 1f47433 1c41413 800293 100313 49d993 89e9b3 1300533
  //   2200893 73 406282b3 fe0294e3 1c45413 406b0b33 b0463 f95ff06f 2b3 fff2c293 1029293 fff2e293 500533
  //   2200893 73 f5dff06f 1112023 410113 a12023 410113 812023 410113 1312023 410113 1412023 410113 1512023
  //   410113 1612023 410113 40e073 100b13 300a13 100a93 1600433 441413 14469b3 1300533 2200893 73 fe0416e3
  //   415a0a33 fe0a10e3 40f073 ffc10113 12b03 ffc10113 12a83 ffc10113 12a03 ffc10113 12983 ffc10113 12403
  //   ffc10113 12503 ffc10113 12883 200073 1112023 410113 a12023 410113 812023 410113 1312023 410113
  //   1412023 410113 1512023 410113 1612023 410113 40e073 200b13 300a13 100a93 1600433 441413 14469b3
  //   1300533 2200893 73 fe0416e3 415a0a33 fe0a10e3 40f073 ffc10113 12b03 ffc10113 12a83 ffc10113 12a03
  //   ffc10113 12983 ffc10113 12403 ffc10113 12503 ffc10113 12883 200073 1112023 410113 a12023 410113
  //   812023 410113 1312023 410113 1412023 410113 1512023 410113 1612023 410113 40e073 300b13 300a13
  //   100a93 1600433 441413 14469b3 1300533 2200893 73 fe0416e3 415a0a33 fe0a10e3 40f073 ffc10113 12b03
  //   ffc10113 12a83 ffc10113 12a03 ffc10113 12983 ffc10113 12403 ffc10113 12503 ffc10113 12883 200073
  //   $a0
  //   I型指令
  //   S型指令
  //   B型指令
  //   J型指令
  //   U型指令
  //   为方便自动评测，需要输出PC，IR，寄存器堆写如数据RDin
  //   RAM写使能MemWrite、RAM写入数据MDin等信号
  //   控制位
  //   暂停节拍，不能为0
  //   戳工具置1进入计数暂停模式，ctrl+k时钟自动运行到对应节拍暂停
  //   ctrl+k关闭时钟连续运行，将控制位置零，进入单步调试模式调试
  //   上升沿
  //   可计数暂停的时钟源
  //   下降沿
  //   数据存储器
  //   halt
  //   IE寄存器初始值异步置1
endmodule
module \地图备份寄存器堆  (
  input  \全体位移 ,
  input  \写使能 ,
  input  [9:0] Addr,
  input  CLK,
  input  RST,
  input  [31:0] Data,
  output [31:0] \行9 ,
  output [31:0] \行25 ,
  output [31:0] \行1 ,
  output [31:0] \行17 ,
  output [31:0] \行10 ,
  output [31:0] \行26 ,
  output [31:0] \行2 ,
  output [31:0] \行18 ,
  output [31:0] \行11 ,
  output [31:0] \行27 ,
  output [31:0] \行3 ,
  output [31:0] \行19 ,
  output [31:0] \行4 ,
  output [31:0] \行12 ,
  output [31:0] \行28 ,
  output [31:0] \行20 ,
  output [31:0] Mem,
  output [31:0] \行5 ,
  output [31:0] \行13 ,
  output [31:0] \行29 ,
  output [31:0] \行21 ,
  output [31:0] \行6 ,
  output [31:0] \行14 ,
  output [31:0] \行30 ,
  output [31:0] \行22 ,
  output [31:0] \行7 ,
  output [31:0] \行15 ,
  output [31:0] \行31 ,
  output [31:0] \行23 ,
  output [31:0] \行8 ,
  output [31:0] \行16 ,
  output [31:0] \行32 ,
  output [31:0] \行24 
);

  wire and_1_out, and_2_out, and_3_out, and_4_out, and_5_out, and_6_out, and_7_out, and_8_out, and_9_out,
       and_10_out, and_11_out, and_12_out, and_13_out, and_14_out, and_15_out, and_16_out, and_17_out,
       and_18_out, and_19_out, and_20_out, and_21_out, and_22_out, and_23_out, and_24_out, and_25_out,
       and_26_out, and_27_out, and_28_out, and_29_out, and_30_out, and_31_out, and_32_out, or_1_out,
       or_2_out, or_3_out, or_4_out, or_5_out, or_6_out, or_7_out, or_8_out, or_9_out, or_10_out, or_11_out,
       or_12_out, or_13_out, or_14_out, or_15_out, or_16_out, or_17_out, or_18_out, or_19_out, or_20_out,
       or_21_out, or_22_out, or_23_out, or_24_out, or_25_out, or_26_out, or_27_out, or_28_out, or_29_out,
       or_30_out, or_31_out, or_32_out, \行1_t , \行2_t , \行3_t , \行4_t , \行5_t , \行6_t , \行7_t , \行8_t ,
       \行9_t , \行10_t , \行11_t , \行12_t , \行13_t , \行14_t , \行15_t , \行16_t , \行17_t , \行18_t , \行19_t ,
       \行20_t , \行21_t , \行22_t , \行23_t , \行24_t , \行25_t , \行26_t , \行27_t , \行28_t , \行29_t , \行30_t ,
       \行31_t , \行32_t ;
  wire [31:0] multiplexer_1_out, multiplexer_2_out, multiplexer_3_out, multiplexer_4_out, multiplexer_5_out,
       multiplexer_6_out, multiplexer_7_out, multiplexer_8_out, multiplexer_9_out, multiplexer_10_out,
       multiplexer_11_out, multiplexer_12_out, multiplexer_13_out, multiplexer_14_out, multiplexer_15_out,
       multiplexer_16_out, multiplexer_17_out, multiplexer_18_out, multiplexer_19_out, multiplexer_20_out,
       multiplexer_21_out, multiplexer_22_out, multiplexer_23_out, multiplexer_24_out, multiplexer_25_out,
       multiplexer_26_out, multiplexer_27_out, multiplexer_28_out, multiplexer_29_out, multiplexer_30_out,
       multiplexer_31_out, multiplexer_32_out, shifter_1_out, shifter_2_out, shifter_3_out, shifter_4_out,
       shifter_5_out, shifter_6_out, shifter_7_out, shifter_8_out, shifter_9_out, shifter_10_out,
       shifter_11_out, shifter_12_out, shifter_13_out, shifter_14_out, shifter_15_out, shifter_16_out,
       shifter_17_out, shifter_18_out, shifter_19_out, shifter_20_out, shifter_21_out, shifter_22_out,
       shifter_23_out, shifter_24_out, shifter_25_out, shifter_26_out, shifter_27_out, shifter_28_out,
       shifter_29_out, shifter_30_out, shifter_31_out, shifter_32_out;

  and and_1 (and_1_out, \写使能 , \行1_t );
  and and_2 (and_2_out, \写使能 , \行2_t );
  and and_3 (and_3_out, \写使能 , \行3_t );
  and and_4 (and_4_out, \写使能 , \行4_t );
  and and_5 (and_5_out, \写使能 , \行5_t );
  and and_6 (and_6_out, \写使能 , \行6_t );
  and and_7 (and_7_out, \写使能 , \行7_t );
  and and_8 (and_8_out, \写使能 , \行8_t );
  Shifter #(.width(32), .shift("ll")) shifter_1 (.in(\行1 ), .\dist (5'b00001), .out(shifter_1_out));
  or or_1 (or_1_out, and_1_out, \全体位移 );
  Shifter #(.width(32), .shift("ll")) shifter_2 (.in(\行2 ), .\dist (5'b00001), .out(shifter_2_out));
  or or_2 (or_2_out, and_2_out, \全体位移 );
  Shifter #(.width(32), .shift("ll")) shifter_3 (.in(\行3 ), .\dist (5'b00001), .out(shifter_3_out));
  or or_3 (or_3_out, and_3_out, \全体位移 );
  Shifter #(.width(32), .shift("ll")) shifter_4 (.in(\行4 ), .\dist (5'b00001), .out(shifter_4_out));
  or or_4 (or_4_out, and_4_out, \全体位移 );
  Shifter #(.width(32), .shift("ll")) shifter_5 (.in(\行5 ), .\dist (5'b00001), .out(shifter_5_out));
  or or_5 (or_5_out, and_5_out, \全体位移 );
  Shifter #(.width(32), .shift("ll")) shifter_6 (.in(\行6 ), .\dist (5'b00001), .out(shifter_6_out));
  or or_6 (or_6_out, and_6_out, \全体位移 );
  Shifter #(.width(32), .shift("ll")) shifter_7 (.in(\行7 ), .\dist (5'b00001), .out(shifter_7_out));
  or or_7 (or_7_out, and_7_out, \全体位移 );
  Shifter #(.width(32), .shift("ll")) shifter_8 (.in(\行8 ), .\dist (5'b00001), .out(shifter_8_out));
  or or_8 (or_8_out, and_8_out, \全体位移 );
  Multiplexer #(.select(1), .width(32), .disabled("Z"), .enable("false")) multiplexer_1 (
    .in0(Data), .in1(shifter_1_out), .out(multiplexer_1_out), .sel(\全体位移 ));
  Multiplexer #(.select(1), .width(32), .disabled("Z"), .enable("false")) multiplexer_2 (
    .in0(Data), .in1(shifter_2_out), .out(multiplexer_2_out), .sel(\全体位移 ));
  Multiplexer #(.select(1), .width(32), .disabled("Z"), .enable("false")) multiplexer_3 (
    .in0(Data), .in1(shifter_3_out), .out(multiplexer_3_out), .sel(\全体位移 ));
  Multiplexer #(.select(1), .width(32), .disabled("Z"), .enable("false")) multiplexer_4 (
    .in0(Data), .in1(shifter_4_out), .out(multiplexer_4_out), .sel(\全体位移 ));
  Multiplexer #(.select(1), .width(32), .disabled("Z"), .enable("false")) multiplexer_5 (
    .in0(Data), .in1(shifter_5_out), .out(multiplexer_5_out), .sel(\全体位移 ));
  Multiplexer #(.select(1), .width(32), .disabled("Z"), .enable("false")) multiplexer_6 (
    .in0(Data), .in1(shifter_6_out), .out(multiplexer_6_out), .sel(\全体位移 ));
  Multiplexer #(.select(1), .width(32), .disabled("Z"), .enable("false")) multiplexer_7 (
    .in0(Data), .in1(shifter_7_out), .out(multiplexer_7_out), .sel(\全体位移 ));
  Multiplexer #(.select(1), .width(32), .disabled("Z"), .enable("false")) multiplexer_8 (
    .in0(Data), .in1(shifter_8_out), .out(multiplexer_8_out), .sel(\全体位移 ));
  Register #(.width(32), .trigger("rising"), .Select("low")) register_1 (
    .D(multiplexer_1_out), .en(or_1_out), .Q(\行1 ), .clk(CLK), .clr(RST));
  Register #(.width(32), .trigger("rising"), .Select("low")) register_2 (
    .D(multiplexer_2_out), .en(or_2_out), .Q(\行2 ), .clk(CLK), .clr(RST));
  Register #(.width(32), .trigger("rising"), .Select("low")) register_3 (
    .D(multiplexer_3_out), .en(or_3_out), .Q(\行3 ), .clk(CLK), .clr(RST));
  Register #(.width(32), .trigger("rising"), .Select("low")) register_4 (
    .D(multiplexer_4_out), .en(or_4_out), .Q(\行4 ), .clk(CLK), .clr(RST));
  Register #(.width(32), .trigger("rising"), .Select("low")) register_5 (
    .D(multiplexer_5_out), .en(or_5_out), .Q(\行5 ), .clk(CLK), .clr(RST));
  Register #(.width(32), .trigger("rising"), .Select("low")) register_6 (
    .D(multiplexer_6_out), .en(or_6_out), .Q(\行6 ), .clk(CLK), .clr(RST));
  Register #(.width(32), .trigger("rising"), .Select("low")) register_7 (
    .D(multiplexer_7_out), .en(or_7_out), .Q(\行7 ), .clk(CLK), .clr(RST));
  Register #(.width(32), .trigger("rising"), .Select("low")) register_8 (
    .D(multiplexer_8_out), .en(or_8_out), .Q(\行8 ), .clk(CLK), .clr(RST));
  and and_9 (and_9_out, \写使能 , \行9_t );
  and and_10 (and_10_out, \写使能 , \行10_t );
  and and_11 (and_11_out, \写使能 , \行11_t );
  and and_12 (and_12_out, \写使能 , \行12_t );
  and and_13 (and_13_out, \写使能 , \行13_t );
  and and_14 (and_14_out, \写使能 , \行14_t );
  and and_15 (and_15_out, \写使能 , \行15_t );
  and and_16 (and_16_out, \写使能 , \行16_t );
  Shifter #(.width(32), .shift("ll")) shifter_9 (.in(\行9 ), .\dist (5'b00001), .out(shifter_9_out));
  or or_9 (or_9_out, and_9_out, \全体位移 );
  Shifter #(.width(32), .shift("ll")) shifter_10 (.in(\行10 ), .\dist (5'b00001), .out(shifter_10_out));
  or or_10 (or_10_out, and_10_out, \全体位移 );
  Shifter #(.width(32), .shift("ll")) shifter_11 (.in(\行11 ), .\dist (5'b00001), .out(shifter_11_out));
  or or_11 (or_11_out, and_11_out, \全体位移 );
  Shifter #(.width(32), .shift("ll")) shifter_12 (.in(\行12 ), .\dist (5'b00001), .out(shifter_12_out));
  or or_12 (or_12_out, and_12_out, \全体位移 );
  Shifter #(.width(32), .shift("ll")) shifter_13 (.in(\行13 ), .\dist (5'b00001), .out(shifter_13_out));
  or or_13 (or_13_out, and_13_out, \全体位移 );
  Shifter #(.width(32), .shift("ll")) shifter_14 (.in(\行14 ), .\dist (5'b00001), .out(shifter_14_out));
  or or_14 (or_14_out, and_14_out, \全体位移 );
  Shifter #(.width(32), .shift("ll")) shifter_15 (.in(\行15 ), .\dist (5'b00001), .out(shifter_15_out));
  or or_15 (or_15_out, and_15_out, \全体位移 );
  Shifter #(.width(32), .shift("ll")) shifter_16 (.in(\行16 ), .\dist (5'b00001), .out(shifter_16_out));
  or or_16 (or_16_out, and_16_out, \全体位移 );
  Multiplexer #(.select(1), .width(32), .disabled("Z"), .enable("false")) multiplexer_9 (
    .in0(Data), .in1(shifter_9_out), .out(multiplexer_9_out), .sel(\全体位移 ));
  Multiplexer #(.select(1), .width(32), .disabled("Z"), .enable("false")) multiplexer_10 (
    .in0(Data), .in1(shifter_10_out), .out(multiplexer_10_out), .sel(\全体位移 ));
  Multiplexer #(.select(1), .width(32), .disabled("Z"), .enable("false")) multiplexer_11 (
    .in0(Data), .in1(shifter_11_out), .out(multiplexer_11_out), .sel(\全体位移 ));
  Multiplexer #(.select(1), .width(32), .disabled("Z"), .enable("false")) multiplexer_12 (
    .in0(Data), .in1(shifter_12_out), .out(multiplexer_12_out), .sel(\全体位移 ));
  Multiplexer #(.select(1), .width(32), .disabled("Z"), .enable("false")) multiplexer_13 (
    .in0(Data), .in1(shifter_13_out), .out(multiplexer_13_out), .sel(\全体位移 ));
  Multiplexer #(.select(1), .width(32), .disabled("Z"), .enable("false")) multiplexer_14 (
    .in0(Data), .in1(shifter_14_out), .out(multiplexer_14_out), .sel(\全体位移 ));
  Multiplexer #(.select(1), .width(32), .disabled("Z"), .enable("false")) multiplexer_15 (
    .in0(Data), .in1(shifter_15_out), .out(multiplexer_15_out), .sel(\全体位移 ));
  Multiplexer #(.select(1), .width(32), .disabled("Z"), .enable("false")) multiplexer_16 (
    .in0(Data), .in1(shifter_16_out), .out(multiplexer_16_out), .sel(\全体位移 ));
  Register #(.width(32), .trigger("rising"), .Select("low")) register_9 (
    .D(multiplexer_9_out), .en(or_9_out), .Q(\行9 ), .clk(CLK), .clr(RST));
  Register #(.width(32), .trigger("rising"), .Select("low")) register_10 (
    .D(multiplexer_10_out), .en(or_10_out), .Q(\行10 ), .clk(CLK), .clr(RST));
  Register #(.width(32), .trigger("rising"), .Select("low")) register_11 (
    .D(multiplexer_11_out), .en(or_11_out), .Q(\行11 ), .clk(CLK), .clr(RST));
  Register #(.width(32), .trigger("rising"), .Select("low")) register_12 (
    .D(multiplexer_12_out), .en(or_12_out), .Q(\行12 ), .clk(CLK), .clr(RST));
  Register #(.width(32), .trigger("rising"), .Select("low")) register_13 (
    .D(multiplexer_13_out), .en(or_13_out), .Q(\行13 ), .clk(CLK), .clr(RST));
  Register #(.width(32), .trigger("rising"), .Select("low")) register_14 (
    .D(multiplexer_14_out), .en(or_14_out), .Q(\行14 ), .clk(CLK), .clr(RST));
  Register #(.width(32), .trigger("rising"), .Select("low")) register_15 (
    .D(multiplexer_15_out), .en(or_15_out), .Q(\行15 ), .clk(CLK), .clr(RST));
  Register #(.width(32), .trigger("rising"), .Select("low")) register_16 (
    .D(multiplexer_16_out), .en(or_16_out), .Q(\行16 ), .clk(CLK), .clr(RST));
  and and_17 (and_17_out, \写使能 , \行17_t );
  and and_18 (and_18_out, \写使能 , \行18_t );
  and and_19 (and_19_out, \写使能 , \行19_t );
  and and_20 (and_20_out, \写使能 , \行20_t );
  and and_21 (and_21_out, \写使能 , \行21_t );
  and and_22 (and_22_out, \写使能 , \行22_t );
  and and_23 (and_23_out, \写使能 , \行23_t );
  and and_24 (and_24_out, \写使能 , \行24_t );
  Shifter #(.width(32), .shift("ll")) shifter_17 (.in(\行17 ), .\dist (5'b00001), .out(shifter_17_out));
  or or_17 (or_17_out, and_17_out, \全体位移 );
  Shifter #(.width(32), .shift("ll")) shifter_18 (.in(\行18 ), .\dist (5'b00001), .out(shifter_18_out));
  or or_18 (or_18_out, and_18_out, \全体位移 );
  Shifter #(.width(32), .shift("ll")) shifter_19 (.in(\行19 ), .\dist (5'b00001), .out(shifter_19_out));
  or or_19 (or_19_out, and_19_out, \全体位移 );
  Shifter #(.width(32), .shift("ll")) shifter_20 (.in(\行20 ), .\dist (5'b00001), .out(shifter_20_out));
  or or_20 (or_20_out, and_20_out, \全体位移 );
  Shifter #(.width(32), .shift("ll")) shifter_21 (.in(\行21 ), .\dist (5'b00001), .out(shifter_21_out));
  or or_21 (or_21_out, and_21_out, \全体位移 );
  Shifter #(.width(32), .shift("ll")) shifter_22 (.in(\行22 ), .\dist (5'b00001), .out(shifter_22_out));
  or or_22 (or_22_out, and_22_out, \全体位移 );
  Shifter #(.width(32), .shift("ll")) shifter_23 (.in(\行23 ), .\dist (5'b00001), .out(shifter_23_out));
  or or_23 (or_23_out, and_23_out, \全体位移 );
  Shifter #(.width(32), .shift("ll")) shifter_24 (.in(\行24 ), .\dist (5'b00001), .out(shifter_24_out));
  or or_24 (or_24_out, and_24_out, \全体位移 );
  Multiplexer #(.select(1), .width(32), .disabled("Z"), .enable("false")) multiplexer_17 (
    .in0(Data), .in1(shifter_17_out), .out(multiplexer_17_out), .sel(\全体位移 ));
  Multiplexer #(.select(1), .width(32), .disabled("Z"), .enable("false")) multiplexer_18 (
    .in0(Data), .in1(shifter_18_out), .out(multiplexer_18_out), .sel(\全体位移 ));
  Multiplexer #(.select(1), .width(32), .disabled("Z"), .enable("false")) multiplexer_19 (
    .in0(Data), .in1(shifter_19_out), .out(multiplexer_19_out), .sel(\全体位移 ));
  Multiplexer #(.select(1), .width(32), .disabled("Z"), .enable("false")) multiplexer_20 (
    .in0(Data), .in1(shifter_20_out), .out(multiplexer_20_out), .sel(\全体位移 ));
  Multiplexer #(.select(1), .width(32), .disabled("Z"), .enable("false")) multiplexer_21 (
    .in0(Data), .in1(shifter_21_out), .out(multiplexer_21_out), .sel(\全体位移 ));
  Multiplexer #(.select(1), .width(32), .disabled("Z"), .enable("false")) multiplexer_22 (
    .in0(Data), .in1(shifter_22_out), .out(multiplexer_22_out), .sel(\全体位移 ));
  Multiplexer #(.select(1), .width(32), .disabled("Z"), .enable("false")) multiplexer_23 (
    .in0(Data), .in1(shifter_23_out), .out(multiplexer_23_out), .sel(\全体位移 ));
  Multiplexer #(.select(1), .width(32), .disabled("Z"), .enable("false")) multiplexer_24 (
    .in0(Data), .in1(shifter_24_out), .out(multiplexer_24_out), .sel(\全体位移 ));
  Register #(.width(32), .trigger("rising"), .Select("low")) register_17 (
    .D(multiplexer_17_out), .en(or_17_out), .Q(\行17 ), .clk(CLK), .clr(RST));
  Register #(.width(32), .trigger("rising"), .Select("low")) register_18 (
    .D(multiplexer_18_out), .en(or_18_out), .Q(\行18 ), .clk(CLK), .clr(RST));
  Register #(.width(32), .trigger("rising"), .Select("low")) register_19 (
    .D(multiplexer_19_out), .en(or_19_out), .Q(\行19 ), .clk(CLK), .clr(RST));
  Register #(.width(32), .trigger("rising"), .Select("low")) register_20 (
    .D(multiplexer_20_out), .en(or_20_out), .Q(\行20 ), .clk(CLK), .clr(RST));
  Register #(.width(32), .trigger("rising"), .Select("low")) register_21 (
    .D(multiplexer_21_out), .en(or_21_out), .Q(\行21 ), .clk(CLK), .clr(RST));
  Register #(.width(32), .trigger("rising"), .Select("low")) register_22 (
    .D(multiplexer_22_out), .en(or_22_out), .Q(\行22 ), .clk(CLK), .clr(RST));
  Register #(.width(32), .trigger("rising"), .Select("low")) register_23 (
    .D(multiplexer_23_out), .en(or_23_out), .Q(\行23 ), .clk(CLK), .clr(RST));
  Register #(.width(32), .trigger("rising"), .Select("low")) register_24 (
    .D(multiplexer_24_out), .en(or_24_out), .Q(\行24 ), .clk(CLK), .clr(RST));
  and and_25 (and_25_out, \写使能 , \行25_t );
  and and_26 (and_26_out, \写使能 , \行26_t );
  and and_27 (and_27_out, \写使能 , \行27_t );
  and and_28 (and_28_out, \写使能 , \行28_t );
  and and_29 (and_29_out, \写使能 , \行29_t );
  and and_30 (and_30_out, \写使能 , \行30_t );
  and and_31 (and_31_out, \写使能 , \行31_t );
  and and_32 (and_32_out, \写使能 , \行32_t );
  Shifter #(.width(32), .shift("ll")) shifter_25 (.in(\行25 ), .\dist (5'b00001), .out(shifter_25_out));
  Shifter #(.width(32), .shift("ll")) shifter_26 (.in(\行26 ), .\dist (5'b00001), .out(shifter_26_out));
  Shifter #(.width(32), .shift("ll")) shifter_27 (.in(\行27 ), .\dist (5'b00001), .out(shifter_27_out));
  Shifter #(.width(32), .shift("ll")) shifter_28 (.in(\行28 ), .\dist (5'b00001), .out(shifter_28_out));
  Shifter #(.width(32), .shift("ll")) shifter_29 (.in(\行29 ), .\dist (5'b00001), .out(shifter_29_out));
  Shifter #(.width(32), .shift("ll")) shifter_30 (.in(\行30 ), .\dist (5'b00001), .out(shifter_30_out));
  Shifter #(.width(32), .shift("ll")) shifter_31 (.in(\行31 ), .\dist (5'b00001), .out(shifter_31_out));
  Shifter #(.width(32), .shift("ll")) shifter_32 (.in(\行32 ), .\dist (5'b00001), .out(shifter_32_out));
  Multiplexer #(.select(1), .width(32), .disabled("Z"), .enable("false")) multiplexer_25 (
    .in0(Data), .in1(shifter_25_out), .out(multiplexer_25_out), .sel(\全体位移 ));
  or or_25 (or_25_out, and_25_out, \全体位移 );
  Multiplexer #(.select(1), .width(32), .disabled("Z"), .enable("false")) multiplexer_26 (
    .in0(Data), .in1(shifter_26_out), .out(multiplexer_26_out), .sel(\全体位移 ));
  or or_26 (or_26_out, and_26_out, \全体位移 );
  Multiplexer #(.select(1), .width(32), .disabled("Z"), .enable("false")) multiplexer_27 (
    .in0(Data), .in1(shifter_27_out), .out(multiplexer_27_out), .sel(\全体位移 ));
  or or_27 (or_27_out, and_27_out, \全体位移 );
  Multiplexer #(.select(1), .width(32), .disabled("Z"), .enable("false")) multiplexer_28 (
    .in0(Data), .in1(shifter_28_out), .out(multiplexer_28_out), .sel(\全体位移 ));
  or or_28 (or_28_out, and_28_out, \全体位移 );
  Multiplexer #(.select(1), .width(32), .disabled("Z"), .enable("false")) multiplexer_29 (
    .in0(Data), .in1(shifter_29_out), .out(multiplexer_29_out), .sel(\全体位移 ));
  or or_29 (or_29_out, and_29_out, \全体位移 );
  Multiplexer #(.select(1), .width(32), .disabled("Z"), .enable("false")) multiplexer_30 (
    .in0(Data), .in1(shifter_30_out), .out(multiplexer_30_out), .sel(\全体位移 ));
  or or_30 (or_30_out, and_30_out, \全体位移 );
  Multiplexer #(.select(1), .width(32), .disabled("Z"), .enable("false")) multiplexer_31 (
    .in0(Data), .in1(shifter_31_out), .out(multiplexer_31_out), .sel(\全体位移 ));
  or or_31 (or_31_out, and_31_out, \全体位移 );
  Multiplexer #(.select(1), .width(32), .disabled("Z"), .enable("false")) multiplexer_32 (
    .in0(Data), .in1(shifter_32_out), .out(multiplexer_32_out), .sel(\全体位移 ));
  or or_32 (or_32_out, and_32_out, \全体位移 );
  Register #(.width(32), .trigger("rising"), .Select("low")) register_25 (
    .D(multiplexer_25_out), .en(or_25_out), .Q(\行25 ), .clk(CLK), .clr(RST));
  Register #(.width(32), .trigger("rising"), .Select("low")) register_26 (
    .D(multiplexer_26_out), .en(or_26_out), .Q(\行26 ), .clk(CLK), .clr(RST));
  Register #(.width(32), .trigger("rising"), .Select("low")) register_27 (
    .D(multiplexer_27_out), .en(or_27_out), .Q(\行27 ), .clk(CLK), .clr(RST));
  Register #(.width(32), .trigger("rising"), .Select("low")) register_28 (
    .D(multiplexer_28_out), .en(or_28_out), .Q(\行28 ), .clk(CLK), .clr(RST));
  Register #(.width(32), .trigger("rising"), .Select("low")) register_29 (
    .D(multiplexer_29_out), .en(or_29_out), .Q(\行29 ), .clk(CLK), .clr(RST));
  Register #(.width(32), .trigger("rising"), .Select("low")) register_30 (
    .D(multiplexer_30_out), .en(or_30_out), .Q(\行30 ), .clk(CLK), .clr(RST));
  Register #(.width(32), .trigger("rising"), .Select("low")) register_31 (
    .D(multiplexer_31_out), .en(or_31_out), .Q(\行31 ), .clk(CLK), .clr(RST));
  Register #(.width(32), .trigger("rising"), .Select("low")) register_32 (
    .D(multiplexer_32_out), .en(or_32_out), .Q(\行32 ), .clk(CLK), .clr(RST));
  Demultiplexer #(.select(5), .width(1), .tristate("false"), .disabled("Z"), .enable("false")) demultiplexer_1 (
    .out0(\行1_t ), .out1(\行2_t ), .out2(\行3_t ), .out3(\行4_t ), .out4(\行5_t ), .out5(\行6_t ), .out6(\行7_t ),
    .out7(\行8_t ), .out8(\行9_t ), .out9(\行10_t ), .out10(\行11_t ), .out11(\行12_t ), .out12(\行13_t ),
    .out13(\行14_t ), .out14(\行15_t ), .out15(\行16_t ), .out16(\行17_t ), .out17(\行18_t ), .out18(\行19_t ),
    .out19(\行20_t ), .out20(\行21_t ), .out21(\行22_t ), .out22(\行23_t ), .out23(\行24_t ), .out24(\行25_t ),
    .out25(\行26_t ), .out26(\行27_t ), .out27(\行28_t ), .out28(\行29_t ), .out29(\行30_t ), .out30(\行31_t ),
    .out31(\行32_t ), .in(1'b1), .sel(Addr[4:0]));
  Multiplexer #(.select(5), .width(32), .disabled("Z"), .enable("false")) multiplexer_33 (
    .in0(\行1 ), .in1(\行2 ), .in2(\行3 ), .in3(\行4 ), .in4(\行5 ), .in5(\行6 ), .in6(\行7 ), .in7(\行8 ),
    .in8(\行9 ), .in9(\行10 ), .in10(\行11 ), .in11(\行12 ), .in12(\行13 ), .in13(\行14 ), .in14(\行15 ),
    .in15(\行16 ), .in16(\行17 ), .in17(\行18 ), .in18(\行19 ), .in19(\行20 ), .in20(\行21 ), .in21(\行22 ),
    .in22(\行23 ), .in23(\行24 ), .in24(\行25 ), .in25(\行26 ), .in26(\行27 ), .in27(\行28 ), .in28(\行29 ),
    .in29(\行30 ), .in30(\行31 ), .in31(\行32 ), .out(Mem), .sel(Addr[4:0]));

  // Other names for the same wires on the sheet: S1[31:0] = \行1 ; S2[31:0] = \行2 ; S3[31:0] = \行3 ; S4[31:0] = \行4 ;
  //   S5[31:0] = \行5 ; S6[31:0] = \行6 ; S7[31:0] = \行7 ; S8[31:0] = \行8 ; S9[31:0] = \行9 ; S10[31:0] = \行10 ;
  //   S11[31:0] = \行11 ; S12[31:0] = \行12 ; S13[31:0] = \行13 ; S14[31:0] = \行14 ; S15[31:0] = \行15 ;
  //   S16[31:0] = \行16 ; S17[31:0] = \行17 ; S18[31:0] = \行18 ; S19[31:0] = \行19 ; S20[31:0] = \行20 ;
  //   S21[31:0] = \行21 ; S22[31:0] = \行22 ; S23[31:0] = \行23 ; S24[31:0] = \行24 ; S25[31:0] = \行25 ;
  //   S26[31:0] = \行26 ; S27[31:0] = \行27 ; S28[31:0] = \行28 ; S29[31:0] = \行29 ; S30[31:0] = \行30 ;
  //   S31[31:0] = \行31 ; S32[31:0] = \行32 
endmodule

module \点阵显示寄存器堆  (
  input  \写使能 ,
  input  [31:0] _1,
  input  [31:0] _2,
  input  [31:0] _3,
  input  [31:0] _4,
  input  [31:0] _5,
  input  [31:0] _6,
  input  [31:0] _7,
  input  [31:0] _8,
  input  [31:0] _9,
  input  [31:0] _10,
  input  [31:0] _11,
  input  [31:0] _12,
  input  [31:0] _13,
  input  [31:0] _14,
  input  [31:0] _15,
  input  [31:0] _16,
  input  [31:0] _17,
  input  [31:0] _18,
  input  [31:0] _19,
  input  [31:0] _20,
  input  [31:0] _21,
  input  [31:0] _22,
  input  [31:0] _23,
  input  [31:0] _24,
  input  [31:0] _25,
  input  [31:0] _26,
  input  [31:0] _27,
  input  [31:0] _28,
  input  [31:0] _29,
  input  [31:0] _30,
  input  [31:0] _31,
  input  [31:0] _32,
  input  CLK,
  input  RST,
  output [31:0] _1_2,
  output [31:0] _2_2,
  output [31:0] _3_2,
  output [31:0] _4_2,
  output [31:0] _5_2,
  output [31:0] _6_2,
  output [31:0] _7_2,
  output [31:0] _8_2,
  output [31:0] _9_2,
  output [31:0] _10_2,
  output [31:0] _11_2,
  output [31:0] _12_2,
  output [31:0] _13_2,
  output [31:0] _14_2,
  output [31:0] _15_2,
  output [31:0] _16_2,
  output [31:0] _17_2,
  output [31:0] _18_2,
  output [31:0] _19_2,
  output [31:0] _20_2,
  output [31:0] _21_2,
  output [31:0] _22_2,
  output [31:0] _23_2,
  output [31:0] _24_2,
  output [31:0] _25_2,
  output [31:0] _26_2,
  output [31:0] _27_2,
  output [31:0] _28_2,
  output [31:0] _29_2,
  output [31:0] _30_2,
  output [31:0] _31_2,
  output [31:0] _32_2
);

  Register #(.width(32), .trigger("rising"), .Select("low")) register_1 (
    .D(_1), .en(\写使能 ), .Q(_1_2), .clk(CLK), .clr(RST));
  Register #(.width(32), .trigger("rising"), .Select("low")) register_2 (
    .D(_5), .en(\写使能 ), .Q(_5_2), .clk(CLK), .clr(RST));
  Register #(.width(32), .trigger("rising"), .Select("low")) register_3 (
    .D(_9), .en(\写使能 ), .Q(_9_2), .clk(CLK), .clr(RST));
  Register #(.width(32), .trigger("rising"), .Select("low")) register_4 (
    .D(_13), .en(\写使能 ), .Q(_13_2), .clk(CLK), .clr(RST));
  Register #(.width(32), .trigger("rising"), .Select("low")) register_5 (
    .D(_17), .en(\写使能 ), .Q(_17_2), .clk(CLK), .clr(RST));
  Register #(.width(32), .trigger("rising"), .Select("low")) register_6 (
    .D(_21), .en(\写使能 ), .Q(_21_2), .clk(CLK), .clr(RST));
  Register #(.width(32), .trigger("rising"), .Select("low")) register_7 (
    .D(_25), .en(\写使能 ), .Q(_25_2), .clk(CLK), .clr(RST));
  Register #(.width(32), .trigger("rising"), .Select("low")) register_8 (
    .D(_29), .en(\写使能 ), .Q(_29_2), .clk(CLK), .clr(RST));
  Register #(.width(32), .trigger("rising"), .Select("low")) register_9 (
    .D(_2), .en(\写使能 ), .Q(_2_2), .clk(CLK), .clr(RST));
  Register #(.width(32), .trigger("rising"), .Select("low")) register_10 (
    .D(_6), .en(\写使能 ), .Q(_6_2), .clk(CLK), .clr(RST));
  Register #(.width(32), .trigger("rising"), .Select("low")) register_11 (
    .D(_10), .en(\写使能 ), .Q(_10_2), .clk(CLK), .clr(RST));
  Register #(.width(32), .trigger("rising"), .Select("low")) register_12 (
    .D(_14), .en(\写使能 ), .Q(_14_2), .clk(CLK), .clr(RST));
  Register #(.width(32), .trigger("rising"), .Select("low")) register_13 (
    .D(_18), .en(\写使能 ), .Q(_18_2), .clk(CLK), .clr(RST));
  Register #(.width(32), .trigger("rising"), .Select("low")) register_14 (
    .D(_22), .en(\写使能 ), .Q(_22_2), .clk(CLK), .clr(RST));
  Register #(.width(32), .trigger("rising"), .Select("low")) register_15 (
    .D(_26), .en(\写使能 ), .Q(_26_2), .clk(CLK), .clr(RST));
  Register #(.width(32), .trigger("rising"), .Select("low")) register_16 (
    .D(_30), .en(\写使能 ), .Q(_30_2), .clk(CLK), .clr(RST));
  Register #(.width(32), .trigger("rising"), .Select("low")) register_17 (
    .D(_3), .en(\写使能 ), .Q(_3_2), .clk(CLK), .clr(RST));
  Register #(.width(32), .trigger("rising"), .Select("low")) register_18 (
    .D(_7), .en(\写使能 ), .Q(_7_2), .clk(CLK), .clr(RST));
  Register #(.width(32), .trigger("rising"), .Select("low")) register_19 (
    .D(_11), .en(\写使能 ), .Q(_11_2), .clk(CLK), .clr(RST));
  Register #(.width(32), .trigger("rising"), .Select("low")) register_20 (
    .D(_15), .en(\写使能 ), .Q(_15_2), .clk(CLK), .clr(RST));
  Register #(.width(32), .trigger("rising"), .Select("low")) register_21 (
    .D(_19), .en(\写使能 ), .Q(_19_2), .clk(CLK), .clr(RST));
  Register #(.width(32), .trigger("rising"), .Select("low")) register_22 (
    .D(_23), .en(\写使能 ), .Q(_23_2), .clk(CLK), .clr(RST));
  Register #(.width(32), .trigger("rising"), .Select("low")) register_23 (
    .D(_27), .en(\写使能 ), .Q(_27_2), .clk(CLK), .clr(RST));
  Register #(.width(32), .trigger("rising"), .Select("low")) register_24 (
    .D(_31), .en(\写使能 ), .Q(_31_2), .clk(CLK), .clr(RST));
  Register #(.width(32), .trigger("rising"), .Select("low")) register_25 (
    .D(_4), .en(\写使能 ), .Q(_4_2), .clk(CLK), .clr(RST));
  Register #(.width(32), .trigger("rising"), .Select("low")) register_26 (
    .D(_8), .en(\写使能 ), .Q(_8_2), .clk(CLK), .clr(RST));
  Register #(.width(32), .trigger("rising"), .Select("low")) register_27 (
    .D(_12), .en(\写使能 ), .Q(_12_2), .clk(CLK), .clr(RST));
  Register #(.width(32), .trigger("rising"), .Select("low")) register_28 (
    .D(_16), .en(\写使能 ), .Q(_16_2), .clk(CLK), .clr(RST));
  Register #(.width(32), .trigger("rising"), .Select("low")) register_29 (
    .D(_20), .en(\写使能 ), .Q(_20_2), .clk(CLK), .clr(RST));
  Register #(.width(32), .trigger("rising"), .Select("low")) register_30 (
    .D(_24), .en(\写使能 ), .Q(_24_2), .clk(CLK), .clr(RST));
  Register #(.width(32), .trigger("rising"), .Select("low")) register_31 (
    .D(_28), .en(\写使能 ), .Q(_28_2), .clk(CLK), .clr(RST));
  Register #(.width(32), .trigger("rising"), .Select("low")) register_32 (
    .D(_32), .en(\写使能 ), .Q(_32_2), .clk(CLK), .clr(RST));
endmodule

module \选择电路  (
  input  \碰撞 ,
  input  END,
  input  [31:0] in_3,
  input  [31:0] in_4,
  input  [31:0] in_5,
  input  [31:0] in_6,
  input  [31:0] in_7,
  input  [31:0] in_8,
  input  [31:0] in_9,
  input  [31:0] in_10,
  input  [31:0] in_11,
  input  [31:0] in_12,
  input  [31:0] in_13,
  input  [31:0] in_14,
  input  [31:0] in_15,
  input  [31:0] in_16,
  input  [31:0] in_17,
  input  [31:0] in_18,
  input  [31:0] in_19,
  input  [31:0] in_20,
  input  [31:0] in_21,
  input  [31:0] in_22,
  input  [31:0] in_23,
  input  [31:0] in_24,
  input  [31:0] in_25,
  input  [31:0] in_26,
  input  [31:0] in_27,
  input  [31:0] in_28,
  input  [31:0] in_29,
  input  [31:0] in_30,
  input  [31:0] in_31,
  input  [31:0] in_32,
  input  [31:0] in_33,
  input  [31:0] in_34,
  output [31:0] _1,
  output [31:0] _2,
  output [31:0] _3,
  output [31:0] _4,
  output [31:0] _5,
  output [31:0] _6,
  output [31:0] _7,
  output [31:0] _8,
  output [31:0] _1_2,
  output [31:0] _2_2,
  output [31:0] _3_2,
  output [31:0] _4_2,
  output [31:0] _5_2,
  output [31:0] _6_2,
  output [31:0] _7_2,
  output [31:0] _8_2,
  output [31:0] _1_3,
  output [31:0] _2_3,
  output [31:0] _3_3,
  output [31:0] _4_3,
  output [31:0] _5_3,
  output [31:0] _6_3,
  output [31:0] _7_3,
  output [31:0] _8_3,
  output [31:0] _1_4,
  output [31:0] _2_4,
  output [31:0] _3_4,
  output [31:0] _4_4,
  output [31:0] _5_4,
  output [31:0] _6_4,
  output [31:0] _7_4,
  output [31:0] _8_4
);

  \多路选择封装_单个  \u_多路选择封装_单个_1  (
    .in_2(in_3), .in_3({32{1'b0}}), .in_4({32{1'b1}}), .in_5({32{1'b0}}), .out_6(_1), .in_1({\碰撞 , END}));
  \多路选择封装_单个  \u_多路选择封装_单个_2  (
    .in_2(in_11), .in_3(32'h7c000), .in_4({32{1'b0}}), .in_5({32{1'b0}}), .out_6(_1_2), .in_1({\碰撞 , END}));
  \多路选择封装_单个  \u_多路选择封装_单个_3  (
    .in_2(in_19), .in_3(32'h10000), .in_4({32{1'b0}}), .in_5({32{1'b0}}), .out_6(_1_3), .in_1({\碰撞 , END}));
  \多路选择封装_单个  \u_多路选择封装_单个_4  (
    .in_2(in_27), .in_3({32{1'b0}}), .in_4({32{1'b0}}), .in_5({32{1'b0}}), .out_6(_1_4), .in_1({\碰撞 , END}));
  \多路选择封装_单个  \u_多路选择封装_单个_5  (
    .in_2(in_4), .in_3({32{1'b0}}), .in_4({32{1'b1}}), .in_5({32{1'b0}}), .out_6(_2), .in_1({\碰撞 , END}));
  \多路选择封装_单个  \u_多路选择封装_单个_6  (
    .in_2(in_12), .in_3(32'h54000), .in_4({32{1'b0}}), .in_5({32{1'b0}}), .out_6(_2_2), .in_1({\碰撞 , END}));
  \多路选择封装_单个  \u_多路选择封装_单个_7  (
    .in_2(in_20), .in_3(32'h7c000), .in_4({32{1'b0}}), .in_5({32{1'b0}}), .out_6(_2_3), .in_1({\碰撞 , END}));
  \多路选择封装_单个  \u_多路选择封装_单个_8  (
    .in_2(in_28), .in_3({32{1'b0}}), .in_4({32{1'b0}}), .in_5({32{1'b0}}), .out_6(_2_4), .in_1({\碰撞 , END}));
  \多路选择封装_单个  \u_多路选择封装_单个_9  (
    .in_2(in_5), .in_3({32{1'b0}}), .in_4({32{1'b0}}), .in_5({32{1'b0}}), .out_6(_3), .in_1({\碰撞 , END}));
  \多路选择封装_单个  \u_多路选择封装_单个_10  (
    .in_2(in_6), .in_3({32{1'b0}}), .in_4({32{1'b0}}), .in_5({32{1'b0}}), .out_6(_4), .in_1({\碰撞 , END}));
  \多路选择封装_单个  \u_多路选择封装_单个_11  (
    .in_2(in_13), .in_3(32'h54000), .in_4({32{1'b0}}), .in_5({32{1'b0}}), .out_6(_3_2), .in_1({\碰撞 , END}));
  \多路选择封装_单个  \u_多路选择封装_单个_12  (
    .in_2(in_14), .in_3(32'h54000), .in_4({32{1'b0}}), .in_5({32{1'b0}}), .out_6(_4_2), .in_1({\碰撞 , END}));
  \多路选择封装_单个  \u_多路选择封装_单个_13  (
    .in_2(in_21), .in_3({32{1'b0}}), .in_4({32{1'b0}}), .in_5({32{1'b0}}), .out_6(_3_3), .in_1({\碰撞 , END}));
  \多路选择封装_单个  \u_多路选择封装_单个_14  (
    .in_2(in_22), .in_3({32{1'b0}}), .in_4({32{1'b0}}), .in_5({32{1'b0}}), .out_6(_4_3), .in_1({\碰撞 , END}));
  \多路选择封装_单个  \u_多路选择封装_单个_15  (
    .in_2(in_29), .in_3({32{1'b0}}), .in_4({32{1'b0}}), .in_5({32{1'b0}}), .out_6(_3_4), .in_1({\碰撞 , END}));
  \多路选择封装_单个  \u_多路选择封装_单个_16  (
    .in_2(in_30), .in_3({32{1'b0}}), .in_4({32{1'b0}}), .in_5({32{1'b0}}), .out_6(_4_4), .in_1({\碰撞 , END}));
  \多路选择封装_单个  \u_多路选择封装_单个_17  (
    .in_2(in_7), .in_3({32{1'b0}}), .in_4({32{1'b0}}), .in_5({32{1'b0}}), .out_6(_5), .in_1({\碰撞 , END}));
  \多路选择封装_单个  \u_多路选择封装_单个_18  (
    .in_2(in_15), .in_3({32{1'b0}}), .in_4({32{1'b0}}), .in_5({32{1'b0}}), .out_6(_5_2), .in_1({\碰撞 , END}));
  \多路选择封装_单个  \u_多路选择封装_单个_19  (
    .in_2(in_23), .in_3(32'h7c000), .in_4({32{1'b0}}), .in_5({32{1'b0}}), .out_6(_5_3), .in_1({\碰撞 , END}));
  \多路选择封装_单个  \u_多路选择封装_单个_20  (
    .in_2(in_31), .in_3({32{1'b0}}), .in_4({32{1'b0}}), .in_5({32{1'b0}}), .out_6(_5_4), .in_1({\碰撞 , END}));
  \多路选择封装_单个  \u_多路选择封装_单个_21  (
    .in_2(in_8), .in_3({32{1'b0}}), .in_4({32{1'b0}}), .in_5({32{1'b0}}), .out_6(_6), .in_1({\碰撞 , END}));
  \多路选择封装_单个  \u_多路选择封装_单个_22  (
    .in_2(in_16), .in_3({32{1'b0}}), .in_4({32{1'b0}}), .in_5({32{1'b0}}), .out_6(_6_2), .in_1({\碰撞 , END}));
  \多路选择封装_单个  \u_多路选择封装_单个_23  (
    .in_2(in_24), .in_3(32'h44000), .in_4({32{1'b0}}), .in_5({32{1'b0}}), .out_6(_6_3), .in_1({\碰撞 , END}));
  \多路选择封装_单个  \u_多路选择封装_单个_24  (
    .in_2(in_32), .in_3({32{1'b0}}), .in_4({32{1'b0}}), .in_5({32{1'b0}}), .out_6(_6_4), .in_1({\碰撞 , END}));
  \多路选择封装_单个  \u_多路选择封装_单个_25  (
    .in_2(in_9), .in_3({32{1'b0}}), .in_4({32{1'b0}}), .in_5({32{1'b0}}), .out_6(_7), .in_1({\碰撞 , END}));
  \多路选择封装_单个  \u_多路选择封装_单个_26  (
    .in_2(in_10), .in_3({32{1'b0}}), .in_4({32{1'b0}}), .in_5({32{1'b0}}), .out_6(_8), .in_1({\碰撞 , END}));
  \多路选择封装_单个  \u_多路选择封装_单个_27  (
    .in_2(in_17), .in_3(32'h7c000), .in_4({32{1'b0}}), .in_5({32{1'b0}}), .out_6(_7_2), .in_1({\碰撞 , END}));
  \多路选择封装_单个  \u_多路选择封装_单个_28  (
    .in_2(in_18), .in_3(32'h20000), .in_4({32{1'b0}}), .in_5({32{1'b0}}), .out_6(_8_2), .in_1({\碰撞 , END}));
  \多路选择封装_单个  \u_多路选择封装_单个_29  (
    .in_2(in_25), .in_3(32'h44000), .in_4({32{1'b0}}), .in_5({32{1'b0}}), .out_6(_7_3), .in_1({\碰撞 , END}));
  \多路选择封装_单个  \u_多路选择封装_单个_30  (
    .in_2(in_26), .in_3(32'h38000), .in_4({32{1'b0}}), .in_5({32{1'b0}}), .out_6(_8_3), .in_1({\碰撞 , END}));
  \多路选择封装_单个  \u_多路选择封装_单个_31  (
    .in_2(in_33), .in_3({32{1'b0}}), .in_4({32{1'b1}}), .in_5({32{1'b0}}), .out_6(_7_4), .in_1({\碰撞 , END}));
  \多路选择封装_单个  \u_多路选择封装_单个_32  (
    .in_2(in_34), .in_3({32{1'b0}}), .in_4({32{1'b1}}), .in_5({32{1'b0}}), .out_6(_8_4), .in_1({\碰撞 , END}));

  // Other names for the same wires on the sheet: OP[1:0] = {\碰撞 , END}
endmodule

module \多路选择封装_单个  (
  input  [1:0] in_1,
  input  [31:0] in_2,
  input  [31:0] in_3,
  input  [31:0] in_4,
  input  [31:0] in_5,
  output [31:0] out_6
);

  Multiplexer #(.select(2), .width(32), .disabled(0), .enable("false")) multiplexer_1 (
    .in0(in_2), .in1(in_3), .in2(in_4), .in3(in_5), .out(out_6), .sel(in_1));
endmodule
