// Logisim project main.circ as structural Verilog: 8 circuits, main circuit 团队任务-交互电路
module \团队任务_交互电路  (
);

  wire and_1_out, and_3_out, and_7_out, and_8_out, and_9_out, and_10_out, CLK, comparator_1_lt,
       comparator_2_eq, comparator_2_gt, comparator_2_lt, comparator_3_gt, comparator_3_lt, comparator_4_gt,
       comparator_4_lt, comparator_5_eq, END, IS_START, or_5_out, or_6_out, RST, SHOW, START, START_t, \上 ,
       \下 , \单周期_单级中断_1_碰撞信号 , \单周期_单级中断_1_边界警告 , \右 , \团队任务_音频_1_en_2 , \左 , \扣除生命值 , \按钮_上 , \按钮_下 ,
       \按钮_右 , \按钮_左 , \摇杆_上 , \摇杆_下 , \摇杆_右 , \摇杆_左 , \触碰边界警告 , \键盘_上 , \键盘_下 , \键盘_右 , \键盘_左 ;
  wire [3:0] \init_个 , \init_十 , \init_百 , joystick_1_x, joystick_1_y, \个 , \十 , \百 , \音量 ;
  wire [6:0] keyboard_1_data;
  wire [7:0] counter_2_q;
  wire [13:0] \团队任务_音频_1_频率 ;
  wire [15:0] counter_1_q;
  wire [31:0] \单周期_单级中断_1_行1 , \单周期_单级中断_1_行2 , \单周期_单级中断_1_行3 , \单周期_单级中断_1_行4 , \单周期_单级中断_1_行5 ,
       \单周期_单级中断_1_行6 , \单周期_单级中断_1_行7 , \单周期_单级中断_1_行8 , \单周期_单级中断_1_行9 , \单周期_单级中断_1_行10 ,
       \单周期_单级中断_1_行11 , \单周期_单级中断_1_行12 , \单周期_单级中断_1_行13 , \单周期_单级中断_1_行14 , \单周期_单级中断_1_行15 ,
       \单周期_单级中断_1_行16 , \单周期_单级中断_1_行17 , \单周期_单级中断_1_行18 , \单周期_单级中断_1_行19 , \单周期_单级中断_1_行20 ,
       \单周期_单级中断_1_行21 , \单周期_单级中断_1_行22 , \单周期_单级中断_1_行23 , \单周期_单级中断_1_行24 , \单周期_单级中断_1_行25 ,
       \单周期_单级中断_1_行26 , \单周期_单级中断_1_行27 , \单周期_单级中断_1_行28 , \单周期_单级中断_1_行29 , \单周期_单级中断_1_行30 ,
       \单周期_单级中断_1_行31 , \单周期_单级中断_1_行32 , \团队任务_选择显示_1__1 , \团队任务_选择显示_1__1_2 , \团队任务_选择显示_1__1_3 ,
       \团队任务_选择显示_1__1_4 , \团队任务_选择显示_1__2 , \团队任务_选择显示_1__2_2 , \团队任务_选择显示_1__2_3 , \团队任务_选择显示_1__2_4 ,
       \团队任务_选择显示_1__3 , \团队任务_选择显示_1__3_2 , \团队任务_选择显示_1__3_3 , \团队任务_选择显示_1__3_4 , \团队任务_选择显示_1__4 ,
       \团队任务_选择显示_1__4_2 , \团队任务_选择显示_1__4_3 , \团队任务_选择显示_1__4_4 , \团队任务_选择显示_1__5 , \团队任务_选择显示_1__5_2 ,
       \团队任务_选择显示_1__5_3 , \团队任务_选择显示_1__5_4 , \团队任务_选择显示_1__6 , \团队任务_选择显示_1__6_2 , \团队任务_选择显示_1__6_3 ,
       \团队任务_选择显示_1__6_4 , \团队任务_选择显示_1__7 , \团队任务_选择显示_1__7_2 , \团队任务_选择显示_1__7_3 , \团队任务_选择显示_1__7_4 ,
       \团队任务_选择显示_1__8 , \团队任务_选择显示_1__8_2 , \团队任务_选择显示_1__8_3 , \团队任务_选择显示_1__8_4 ;

  \团队任务_进制转换  \u_团队任务_进制转换_1  (.\十六进制输入 (8'h5), .\百 (\init_百 ), .\十 (\init_十 ), .\个 (\init_个 ));
  Hex_Digit_Display hex_digit_display_1 (.value(\init_百 ));  // open: dp
  Hex_Digit_Display hex_digit_display_2 (.value(\init_十 ));  // open: dp
  Hex_Digit_Display hex_digit_display_3 (.value(\init_个 ));  // open: dp
  and and_1 (and_1_out, IS_START, ~END);  // AND_Gate
  Hex_Digit_Display hex_digit_display_4 (.value(\百 ));  // open: dp
  \团队任务_音频  \u_团队任务_音频_1  (
    .\频率 (\团队任务_音频_1_频率 ), .\边界触碰警告 (\触碰边界警告 ), .\频率倍数 (16'h30), .CLK(CLK), .RST(RST), .EN(and_1_out),
    .EN_2(\团队任务_音频_1_en_2 ));
  Counter #(.width(16), .max('hffff), .ongoal("stay"), .trigger("rising"), .behavior("new")) counter_1 (
    .D({16{1'b0}}), .count(SHOW), .Q(counter_1_q), .clk(CLK), .clr(RST));  // open: load, carry, preset, down
  Hex_Digit_Display hex_digit_display_5 (.value(\十 ));  // open: dp
  Hex_Digit_Display hex_digit_display_6 (.value(\个 ));  // open: dp
  LED #(.active("true")) led_1 (.in(\扣除生命值 ));
  LED #(.active("true")) led_2 (.in(\触碰边界警告 ));
  // Buzzer #(.freq_measure("Hz"), .vol_width(4)) buzzer_1: pin names not known; wires that end beside it: \团队任务_音频_1_频率 , \团队任务_音频_1_en_2 , \音量 
  D_Flip_Flop #(.trigger("rising"), .Pre_Clr_Positions("LEGACY"), .NegatePresetClear("false"), .enable("true"), .NewFFLayout("false")) d_ff_1 (
    .clk(START), .D(1'b1), .Q(IS_START), .reset(RST));  // open: Qn, preset, en
  and and_2 (SHOW, IS_START, comparator_1_lt);
  Comparator #(.width(16), .mode("unsigned")) comparator_1 (
    .a(counter_1_q), .b(16'h64), .lt(comparator_1_lt));  // open: gt, eq
  DotMatrix #(.inputtype("column"), .matrixcols(32), .matrixrows(32), .persist(0), .dotshape("square")) dotmatrix_1 (
    .col0(\团队任务_选择显示_1__1 ), .col1(\团队任务_选择显示_1__2 ), .col2(\团队任务_选择显示_1__3 ), .col3(\团队任务_选择显示_1__4 ),
    .col4(\团队任务_选择显示_1__5 ), .col5(\团队任务_选择显示_1__6 ), .col6(\团队任务_选择显示_1__7 ), .col7(\团队任务_选择显示_1__8 ),
    .col8(\团队任务_选择显示_1__1_2 ), .col9(\团队任务_选择显示_1__2_2 ), .col10(\团队任务_选择显示_1__3_2 ),
    .col11(\团队任务_选择显示_1__4_2 ), .col12(\团队任务_选择显示_1__5_2 ), .col13(\团队任务_选择显示_1__6_2 ),
    .col14(\团队任务_选择显示_1__7_2 ), .col15(\团队任务_选择显示_1__8_2 ), .col16(\团队任务_选择显示_1__1_3 ),
    .col17(\团队任务_选择显示_1__2_3 ), .col18(\团队任务_选择显示_1__3_3 ), .col19(\团队任务_选择显示_1__4_3 ),
    .col20(\团队任务_选择显示_1__5_3 ), .col21(\团队任务_选择显示_1__6_3 ), .col22(\团队任务_选择显示_1__7_3 ),
    .col23(\团队任务_选择显示_1__8_3 ), .col24(\团队任务_选择显示_1__1_4 ), .col25(\团队任务_选择显示_1__2_4 ),
    .col26(\团队任务_选择显示_1__3_4 ), .col27(\团队任务_选择显示_1__4_4 ), .col28(\团队任务_选择显示_1__5_4 ),
    .col29(\团队任务_选择显示_1__6_4 ), .col30(\团队任务_选择显示_1__7_4 ), .col31(\团队任务_选择显示_1__8_4 ));
  or or_1 (\左 , \按钮_左 , \摇杆_左 , \键盘_左 );
  or or_2 (\右 , \按钮_右 , \摇杆_右 , \键盘_右 );
  or or_3 (\上 , \按钮_上 , \摇杆_上 , \键盘_上 );
  or or_4 (\下 , \按钮_下 , \摇杆_下 , \键盘_下 );
  \团队任务_选择显示  \u_团队任务_选择显示_1  (
    .in_4(\单周期_单级中断_1_行1 ), .in_5(\单周期_单级中断_1_行2 ), .in_6(\单周期_单级中断_1_行3 ), .in_7(\单周期_单级中断_1_行4 ),
    .in_8(\单周期_单级中断_1_行5 ), .in_9(\单周期_单级中断_1_行6 ), .in_10(\单周期_单级中断_1_行7 ), .in_11(\单周期_单级中断_1_行8 ),
    .in_12(\单周期_单级中断_1_行9 ), .in_13(\单周期_单级中断_1_行10 ), .in_14(\单周期_单级中断_1_行11 ), .in_15(\单周期_单级中断_1_行12 ),
    .in_16(\单周期_单级中断_1_行13 ), .in_17(\单周期_单级中断_1_行14 ), .in_18(\单周期_单级中断_1_行15 ), .in_19(\单周期_单级中断_1_行16 ),
    .in_20(\单周期_单级中断_1_行17 ), .in_21(\单周期_单级中断_1_行18 ), .in_22(\单周期_单级中断_1_行19 ), .in_23(\单周期_单级中断_1_行20 ),
    .in_24(\单周期_单级中断_1_行21 ), .in_25(\单周期_单级中断_1_行22 ), .in_26(\单周期_单级中断_1_行23 ), .in_27(\单周期_单级中断_1_行24 ),
    .in_28(\单周期_单级中断_1_行25 ), .in_29(\单周期_单级中断_1_行26 ), .in_30(\单周期_单级中断_1_行27 ), .in_31(\单周期_单级中断_1_行28 ),
    .in_32(\单周期_单级中断_1_行29 ), .in_33(\单周期_单级中断_1_行30 ), .in_34(\单周期_单级中断_1_行31 ), .in_35(\单周期_单级中断_1_行32 ),
    ._1(\团队任务_选择显示_1__1 ), ._2(\团队任务_选择显示_1__2 ), ._3(\团队任务_选择显示_1__3 ), ._4(\团队任务_选择显示_1__4 ),
    ._5(\团队任务_选择显示_1__5 ), ._6(\团队任务_选择显示_1__6 ), ._7(\团队任务_选择显示_1__7 ), ._8(\团队任务_选择显示_1__8 ),
    ._1_2(\团队任务_选择显示_1__1_2 ), ._2_2(\团队任务_选择显示_1__2_2 ), ._3_2(\团队任务_选择显示_1__3_2 ),
    ._4_2(\团队任务_选择显示_1__4_2 ), ._5_2(\团队任务_选择显示_1__5_2 ), ._6_2(\团队任务_选择显示_1__6_2 ),
    ._7_2(\团队任务_选择显示_1__7_2 ), ._8_2(\团队任务_选择显示_1__8_2 ), ._1_3(\团队任务_选择显示_1__1_3 ),
    ._2_3(\团队任务_选择显示_1__2_3 ), ._3_3(\团队任务_选择显示_1__3_3 ), ._4_3(\团队任务_选择显示_1__4_3 ),
    ._5_3(\团队任务_选择显示_1__5_3 ), ._6_3(\团队任务_选择显示_1__6_3 ), ._7_3(\团队任务_选择显示_1__7_3 ),
    ._8_3(\团队任务_选择显示_1__8_3 ), ._1_4(\团队任务_选择显示_1__1_4 ), ._2_4(\团队任务_选择显示_1__2_4 ),
    ._3_4(\团队任务_选择显示_1__3_4 ), ._4_4(\团队任务_选择显示_1__4_4 ), ._5_4(\团队任务_选择显示_1__5_4 ),
    ._6_4(\团队任务_选择显示_1__6_4 ), ._7_4(\团队任务_选择显示_1__7_4 ), ._8_4(\团队任务_选择显示_1__8_4 ), .END(END), .\碰撞 (1'b0),
    .START(SHOW));
  \单周期_单级中断  \u_单周期_单级中断_1  (
    .LEFT(\左 ), .RIGHT(\右 ), .START(SHOW), .CLK(and_3_out), .UP(\上 ), .DOWN(\下 ), .RST(RST),
    .\碰撞信号 (\单周期_单级中断_1_碰撞信号 ), .\边界警告 (\单周期_单级中断_1_边界警告 ), .\行1 (\单周期_单级中断_1_行1 ), .\行2 (\单周期_单级中断_1_行2 ),
    .\行3 (\单周期_单级中断_1_行3 ), .\行4 (\单周期_单级中断_1_行4 ), .\行5 (\单周期_单级中断_1_行5 ), .\行6 (\单周期_单级中断_1_行6 ),
    .\行7 (\单周期_单级中断_1_行7 ), .\行8 (\单周期_单级中断_1_行8 ), .\行9 (\单周期_单级中断_1_行9 ), .\行10 (\单周期_单级中断_1_行10 ),
    .\行11 (\单周期_单级中断_1_行11 ), .\行12 (\单周期_单级中断_1_行12 ), .\行13 (\单周期_单级中断_1_行13 ), .\行14 (\单周期_单级中断_1_行14 ),
    .\行15 (\单周期_单级中断_1_行15 ), .\行16 (\单周期_单级中断_1_行16 ), .\行17 (\单周期_单级中断_1_行17 ), .\行18 (\单周期_单级中断_1_行18 ),
    .\行19 (\单周期_单级中断_1_行19 ), .\行20 (\单周期_单级中断_1_行20 ), .\行21 (\单周期_单级中断_1_行21 ), .\行22 (\单周期_单级中断_1_行22 ),
    .\行23 (\单周期_单级中断_1_行23 ), .\行24 (\单周期_单级中断_1_行24 ), .\行25 (\单周期_单级中断_1_行25 ), .\行26 (\单周期_单级中断_1_行26 ),
    .\行27 (\单周期_单级中断_1_行27 ), .\行28 (\单周期_单级中断_1_行28 ), .\行29 (\单周期_单级中断_1_行29 ), .\行30 (\单周期_单级中断_1_行30 ),
    .\行31 (\单周期_单级中断_1_行31 ), .\行32 (\单周期_单级中断_1_行32 ));
  and and_3 (and_3_out, CLK, ~END);  // AND_Gate
  Joystick #(.bits(4)) joystick_1 (.x(joystick_1_x), .y(joystick_1_y));
  Button button_1 (.out(START));
  Button button_2 (.out(RST));
  Clock #(.highDuration(1), .lowDuration(1)) clock_1 (.out(CLK));
  Slider #(.width(4), .Direction("left_to_right"), .value('h1)) slider_1 (.out(\音量 ));
  Keyboard #(.Char_bit_width(7), .buflen(32), .trigger("rising")) keyboard_1 (
    .clk(CLK), .clr(RST), .data(keyboard_1_data));  // open: re, avail
  and and_4 (\扣除生命值 , \单周期_单级中断_1_碰撞信号 , ~END);  // AND_Gate
  and and_5 (\触碰边界警告 , \单周期_单级中断_1_边界警告 , ~END);  // AND_Gate
  Counter #(.width(8), .max('hff), .ongoal("wrap"), .trigger("rising"), .behavior("new")) counter_2 (
    .load(START_t), .D(8'h5), .Q(counter_2_q), .clk(or_5_out), .clr(RST), .down(1'b1));  // open: count, carry, preset
  or or_5 (or_5_out, START_t, \扣除生命值 );
  Comparator #(.width(4), .mode("unsigned")) comparator_2 (
    .a(joystick_1_x), .b(joystick_1_y), .gt(comparator_2_gt), .eq(comparator_2_eq), .lt(comparator_2_lt));
  Comparator #(.width(4), .mode("unsigned")) comparator_3 (
    .a(joystick_1_x), .b(4'b1000), .gt(comparator_3_gt), .lt(comparator_3_lt));  // open: eq
  Comparator #(.width(4), .mode("unsigned")) comparator_4 (
    .a(joystick_1_y), .b(4'b1000), .gt(comparator_4_gt), .lt(comparator_4_lt));  // open: eq
  Button button_3 (.out(\按钮_上 ));
  Button button_4 (.out(\按钮_左 ));
  Button button_5 (.out(\按钮_下 ));
  \团队任务_键盘解析  \u_团队任务_键盘解析_1  (
    .\键盘输入 (keyboard_1_data), .W(\键盘_上 ), .S(\键盘_下 ), .A(\键盘_左 ), .D(\键盘_右 ), .CLK(CLK), .RST(RST));
  Comparator #(.width(8), .mode("unsigned")) comparator_5 (
    .a({8{1'b0}}), .b(counter_2_q), .eq(comparator_5_eq));  // open: gt, lt
  \团队任务_进制转换  \u_团队任务_进制转换_2  (.\十六进制输入 (counter_2_q), .\百 (\百 ), .\十 (\十 ), .\个 (\个 ));
  or or_6 (or_6_out, comparator_2_eq, comparator_2_lt);
  Button button_6 (.out(\按钮_右 ));
  and and_6 (END, IS_START, comparator_5_eq);
  and and_7 (and_7_out, comparator_2_gt, comparator_3_gt);
  and and_8 (and_8_out, or_6_out, comparator_3_lt);
  and and_9 (and_9_out, or_6_out, comparator_4_gt);
  and and_10 (and_10_out, comparator_2_gt, comparator_4_lt);
  and and_11 (\摇杆_右 , CLK, and_7_out);
  and and_12 (\摇杆_左 , CLK, and_8_out);
  and and_13 (\摇杆_下 , CLK, and_9_out);
  and and_14 (\摇杆_上 , CLK, and_10_out);

  // Notes on the sheet:
  //   初始生命值
  //   剩余生命值
  //   Airplane Fight
endmodule

module \团队任务_进制转换  (
  input  [7:0] \十六进制输入 ,
  output [3:0] \百 ,
  output [3:0] \十 ,
  output [3:0] \个 
);

  wire [7:0] divider_1_out, divider_1_rem, divider_2_out, divider_2_rem;

  Divider #(.width(8)) divider_1 (.a(\十六进制输入 ), .b(8'ha), .out(divider_1_out), .rem(divider_1_rem));  // open: upper
  Divider #(.width(8)) divider_2 (
    .a(divider_1_out), .b(8'ha), .out(divider_2_out), .rem(divider_2_rem));  // open: upper
  Bit_Extender #(.in_width(8), .out_width(4), .\type ("zero")) bit_extender_1 (.in(divider_2_out), .out(\百 ));
  Bit_Extender #(.in_width(8), .out_width(4), .\type ("zero")) bit_extender_2 (.in(divider_2_rem), .out(\十 ));
  Bit_Extender #(.in_width(8), .out_width(4), .\type ("zero")) bit_extender_3 (.in(divider_1_rem), .out(\个 ));
endmodule

module \团队任务_高低位转换  (
  input  [31:0] in_1,
  output [31:0] out_2
);


  assign out_2 = {in_1[0], in_1[1], in_1[2], in_1[3], in_1[4], in_1[5], in_1[6], in_1[7], in_1[8], in_1[9], in_1[10], in_1[11], in_1[12], in_1[13], in_1[14], in_1[15], in_1[16], in_1[17], in_1[18], in_1[19], in_1[20], in_1[21], in_1[22], in_1[23], in_1[24], in_1[25], in_1[26], in_1[27], in_1[28], in_1[29], in_1[30], in_1[31]};
endmodule

module \团队任务_选择显示  (
  input  \碰撞 ,
  input  END,
  input  START,
  input  [31:0] in_4,
  input  [31:0] in_5,
  input  [31:0] in_6,
  input  [31:0] in_7,
  input  [31:0] in_8,
  input  [31:0] in_9,
  input  [31:0] in_10,
  input  [31:0] in_11,
  input  [31:0] in_12,
  input  [31:0] in_13,
  input  [31:0] in_14,
  input  [31:0] in_15,
  input  [31:0] in_16,
  input  [31:0] in_17,
  input  [31:0] in_18,
  input  [31:0] in_19,
  input  [31:0] in_20,
  input  [31:0] in_21,
  input  [31:0] in_22,
  input  [31:0] in_23,
  input  [31:0] in_24,
  input  [31:0] in_25,
  input  [31:0] in_26,
  input  [31:0] in_27,
  input  [31:0] in_28,
  input  [31:0] in_29,
  input  [31:0] in_30,
  input  [31:0] in_31,
  input  [31:0] in_32,
  input  [31:0] in_33,
  input  [31:0] in_34,
  input  [31:0] in_35,
  output [31:0] _1,
  output [31:0] _2,
  output [31:0] _3,
  output [31:0] _4,
  output [31:0] _5,
  output [31:0] _6,
  output [31:0] _7,
  output [31:0] _8,
  output [31:0] _1_2,
  output [31:0] _2_2,
  output [31:0] _3_2,
  output [31:0] _4_2,
  output [31:0] _5_2,
  output [31:0] _6_2,
  output [31:0] _7_2,
  output [31:0] _8_2,
  output [31:0] _1_3,
  output [31:0] _2_3,
  output [31:0] _3_3,
  output [31:0] _4_3,
  output [31:0] _5_3,
  output [31:0] _6_3,
  output [31:0] _7_3,
  output [31:0] _8_3,
  output [31:0] _1_4,
  output [31:0] _2_4,
  output [31:0] _3_4,
  output [31:0] _4_4,
  output [31:0] _5_4,
  output [31:0] _6_4,
  output [31:0] _7_4,
  output [31:0] _8_4
);

  wire [1:0] OP;

  Multiplexer #(.select(1), .width(2), .disabled("Z"), .enable("false")) multiplexer_1 (
    .in0({\碰撞 , END}), .in1(2'b11), .out(OP), .sel(START));
  \团队任务_多路选择封装_单个  \u_团队任务_多路选择封装_单个_1  (
    .in_2(in_4), .in_3({32{1'b0}}), .out_6(_1), .in_1(OP), .in_4({32{1'b0}}), .in_5({32{1'b0}}));
  \团队任务_多路选择封装_单个  \u_团队任务_多路选择封装_单个_2  (
    .in_2(in_12), .in_3(32'h7c000), .out_6(_1_2), .in_1(OP), .in_4({32{1'b0}}), .in_5(32'h48000));
  \团队任务_多路选择封装_单个  \u_团队任务_多路选择封装_单个_3  (
    .in_2(in_20), .in_3(32'h10000), .out_6(_1_3), .in_1(OP), .in_4({32{1'b0}}), .in_5(32'h48000));
  \团队任务_多路选择封装_单个  \u_团队任务_多路选择封装_单个_4  (
    .in_2(in_28), .in_3({32{1'b0}}), .out_6(_1_4), .in_1(OP), .in_4({32{1'b0}}), .in_5(32'h40000));
  \团队任务_多路选择封装_单个  \u_团队任务_多路选择封装_单个_5  (
    .in_2(in_5), .in_3({32{1'b0}}), .out_6(_2), .in_1(OP), .in_4({32{1'b0}}), .in_5({32{1'b0}}));
  \团队任务_多路选择封装_单个  \u_团队任务_多路选择封装_单个_6  (
    .in_2(in_13), .in_3(32'h54000), .out_6(_2_2), .in_1(OP), .in_4({32{1'b0}}), .in_5({32{1'b0}}));
  \团队任务_多路选择封装_单个  \u_团队任务_多路选择封装_单个_7  (
    .in_2(in_21), .in_3(32'h7c000), .out_6(_2_3), .in_1(OP), .in_4({32{1'b0}}), .in_5(32'h3c000));
  \团队任务_多路选择封装_单个  \u_团队任务_多路选择封装_单个_8  (
    .in_2(in_29), .in_3({32{1'b0}}), .out_6(_2_4), .in_1(OP), .in_4({32{1'b0}}), .in_5(32'h7c000));
  \团队任务_多路选择封装_单个  \u_团队任务_多路选择封装_单个_9  (
    .in_2(in_6), .in_3({32{1'b0}}), .out_6(_3), .in_1(OP), .in_4({32{1'b0}}), .in_5({32{1'b0}}));
  \团队任务_多路选择封装_单个  \u_团队任务_多路选择封装_单个_10  (
    .in_2(in_7), .in_3({32{1'b0}}), .out_6(_4), .in_1(OP), .in_4({32{1'b0}}), .in_5({32{1'b0}}));
  \团队任务_多路选择封装_单个  \u_团队任务_多路选择封装_单个_11  (
    .in_2(in_14), .in_3(32'h54000), .out_6(_3_2), .in_1(OP), .in_4({32{1'b0}}), .in_5(32'h40000));
  \团队任务_多路选择封装_单个  \u_团队任务_多路选择封装_单个_12  (
    .in_2(in_15), .in_3(32'h54000), .out_6(_4_2), .in_1(OP), .in_4({32{1'b0}}), .in_5(32'h7c000));
  \团队任务_多路选择封装_单个  \u_团队任务_多路选择封装_单个_13  (
    .in_2(in_22), .in_3({32{1'b0}}), .out_6(_3_3), .in_1(OP), .in_4({32{1'b0}}), .in_5({32{1'b0}}));
  \团队任务_多路选择封装_单个  \u_团队任务_多路选择封装_单个_14  (
    .in_2(in_23), .in_3({32{1'b0}}), .out_6(_4_3), .in_1(OP), .in_4({32{1'b0}}), .in_5(32'h7c000));
  \团队任务_多路选择封装_单个  \u_团队任务_多路选择封装_单个_15  (
    .in_2(in_30), .in_3({32{1'b0}}), .out_6(_3_4), .in_1(OP), .in_4({32{1'b0}}), .in_5(32'h40000));
  \团队任务_多路选择封装_单个  \u_团队任务_多路选择封装_单个_16  (
    .in_2(in_31), .in_3({32{1'b0}}), .out_6(_4_4), .in_1(OP), .in_4({32{1'b0}}), .in_5({32{1'b0}}));
  \团队任务_多路选择封装_单个  \u_团队任务_多路选择封装_单个_17  (
    .in_2(in_8), .in_3({32{1'b0}}), .out_6(_5), .in_1(OP), .in_4({32{1'b0}}), .in_5({32{1'b0}}));
  \团队任务_多路选择封装_单个  \u_团队任务_多路选择封装_单个_18  (
    .in_2(in_16), .in_3({32{1'b0}}), .out_6(_5_2), .in_1(OP), .in_4({32{1'b0}}), .in_5(32'h40000));
  \团队任务_多路选择封装_单个  \u_团队任务_多路选择封装_单个_19  (
    .in_2(in_24), .in_3(32'h7c000), .out_6(_5_3), .in_1(OP), .in_4({32{1'b0}}), .in_5(32'h48000));
  \团队任务_多路选择封装_单个  \u_团队任务_多路选择封装_单个_20  (
    .in_2(in_32), .in_3({32{1'b0}}), .out_6(_5_4), .in_1(OP), .in_4({32{1'b0}}), .in_5({32{1'b0}}));
  \团队任务_多路选择封装_单个  \u_团队任务_多路选择封装_单个_21  (
    .in_2(in_9), .in_3({32{1'b0}}), .out_6(_6), .in_1(OP), .in_4({32{1'b0}}), .in_5(32'h24000));
  \团队任务_多路选择封装_单个  \u_团队任务_多路选择封装_单个_22  (
    .in_2(in_17), .in_3({32{1'b0}}), .out_6(_6_2), .in_1(OP), .in_4({32{1'b0}}), .in_5({32{1'b0}}));
  \团队任务_多路选择封装_单个  \u_团队任务_多路选择封装_单个_23  (
    .in_2(in_25), .in_3(32'h44000), .out_6(_6_3), .in_1(OP), .in_4({32{1'b0}}), .in_5(32'h48000));
  \团队任务_多路选择封装_单个  \u_团队任务_多路选择封装_单个_24  (
    .in_2(in_33), .in_3({32{1'b0}}), .out_6(_6_4), .in_1(OP), .in_4({32{1'b0}}), .in_5({32{1'b0}}));
  \团队任务_多路选择封装_单个  \u_团队任务_多路选择封装_单个_25  (
    .in_2(in_10), .in_3({32{1'b0}}), .out_6(_7), .in_1(OP), .in_4({32{1'b0}}), .in_5(32'h54000));
  \团队任务_多路选择封装_单个  \u_团队任务_多路选择封装_单个_26  (
    .in_2(in_11), .in_3({32{1'b0}}), .out_6(_8), .in_1(OP), .in_4({32{1'b0}}), .in_5(32'h54000));
  \团队任务_多路选择封装_单个  \u_团队任务_多路选择封装_单个_27  (
    .in_2(in_18), .in_3(32'h7c000), .out_6(_7_2), .in_1(OP), .in_4({32{1'b0}}), .in_5(32'h3c000));
  \团队任务_多路选择封装_单个  \u_团队任务_多路选择封装_单个_28  (
    .in_2(in_19), .in_3(32'h20000), .out_6(_8_2), .in_1(OP), .in_4({32{1'b0}}), .in_5(32'h48000));
  \团队任务_多路选择封装_单个  \u_团队任务_多路选择封装_单个_29  (
    .in_2(in_26), .in_3(32'h44000), .out_6(_7_3), .in_1(OP), .in_4({32{1'b0}}), .in_5(32'h34000));
  \团队任务_多路选择封装_单个  \u_团队任务_多路选择封装_单个_30  (
    .in_2(in_27), .in_3(32'h38000), .out_6(_8_3), .in_1(OP), .in_4({32{1'b0}}), .in_5({32{1'b0}}));
  \团队任务_多路选择封装_单个  \u_团队任务_多路选择封装_单个_31  (
    .in_2(in_34), .in_3({32{1'b0}}), .out_6(_7_4), .in_1(OP), .in_4({32{1'b0}}), .in_5({32{1'b0}}));
  \团队任务_多路选择封装_单个  \u_团队任务_多路选择封装_单个_32  (
    .in_2(in_35), .in_3({32{1'b0}}), .out_6(_8_4), .in_1(OP), .in_4({32{1'b0}}), .in_5({32{1'b0}}));
endmodule

module \团队任务_多路选择封装_单个  (
  input  [1:0] in_1,
  input  [31:0] in_2,
  input  [31:0] in_3,
  input  [31:0] in_4,
  input  [31:0] in_5,
  output [31:0] out_6
);

  wire [31:0] \团队任务_高低位转换_1_out_2 ;

  \团队任务_高低位转换  \u_团队任务_高低位转换_1  (.in_1(in_2), .out_2(\团队任务_高低位转换_1_out_2 ));
  Multiplexer #(.select(2), .width(32), .disabled(0), .enable("false")) multiplexer_1 (
    .in0(\团队任务_高低位转换_1_out_2 ), .in1(in_3), .in2(in_4), .in3(in_5), .out(out_6), .sel(in_1));
endmodule

module \团队任务_时间频率转换  (
  input  [15:0] in_1,
  input  CLK,
  input  RST,
  output CLK_P
);

  wire comparator_1_eq, comparator_2_eq, comparator_2_gt;
  wire [15:0] counter_1_q, shifter_1_out;

  Shifter #(.width(16), .shift("lr")) shifter_1 (.in(in_1), .\dist (4'b0001), .out(shifter_1_out));
  Counter #(.width(16), .max('hffff), .ongoal("wrap"), .trigger("rising"), .behavior("new")) counter_1 (
    .load(comparator_1_eq), .D({16{1'b0}}), .Q(counter_1_q), .clk(CLK), .clr(RST));  // open: count, carry, preset, down
  Comparator #(.width(16), .mode("unsigned")) comparator_1 (
    .a(in_1), .b(counter_1_q), .eq(comparator_1_eq));  // open: gt, lt
  Comparator #(.width(16), .mode("unsigned")) comparator_2 (
    .a(shifter_1_out), .b(counter_1_q), .gt(comparator_2_gt), .eq(comparator_2_eq));  // open: lt
  nor nor_1 (CLK_P, comparator_2_gt, comparator_2_eq);
endmodule

module \团队任务_音频  (
  input  CLK,
  input  RST,
  input  [15:0] \频率倍数 ,
  input  \边界触碰警告 ,
  input  EN,
  output [13:0] \频率 ,
  output EN_2
);

  wire and_1_out, CLK_P;
  wire [7:0] counter_1_q;
  wire [13:0] rom_1_data;

  Counter #(.width(8), .max('hff), .ongoal("wrap"), .trigger("rising"), .behavior("new")) counter_1 (
    .Q(counter_1_q), .clk(and_1_out), .clr(RST));  // open: load, D, count, carry, preset, down
  and and_1 (and_1_out, EN, CLK_P);
  \团队任务_时间频率转换  \u_团队任务_时间频率转换_1  (.in_1(\频率倍数 ), .CLK_P(CLK_P), .CLK(CLK), .RST(RST));
  ROM #(.addrWidth(8), .dataWidth(14), .Select("low")) rom_1 (.addr(counter_1_q), .data(rom_1_data));
  Multiplexer #(.select(1), .width(14), .disabled("Z"), .enable("false")) multiplexer_1 (
    .in0(rom_1_data), .in1(14'h115), .out(\频率 ), .sel(\边界触碰警告 ));

  assign EN_2 = EN;

  // Notes on the sheet:
  //   contents of rom_1 (hex, n*v repeats v):
  //   523 0 587 0 659 0 698 0 784 0 784 0 784 698 659 0 698 0 698 0 698 659 587 0 523 0 659 0 784 0 0 0
  //   523 0 587 0 659 0 698 0 784 0 784 0 784 698 659 0 698 0 698 0 698 659 587 0 523 0 659 0 523 0 0 0
  //   880 0 880 0 880 784 698 0 784 0 784 0 784 698 659 0 698 0 698 0 698 659 587 0 523 0 659 0 784 0 0 0
  //   880 0 880 0 880 784 698 0 784 0 784 0 784 698 659 0 698 0 698 0 698 659 587 0 523 0 659 0 523 0 0 0
  //   523 0 587 0 659 0 698 0 784 0 784 0 784 698 659 0 698 0 698 0 698 659 587 0 523 0 659 0 784 0 0 0
  //   523 0 587 0 659 0 698 0 784 0 784 0 784 698 659 0 698 0 698 0 698 659 587 0 523 0 659 0 523 0 0 0
  //   880 0 880 0 880 784 698 0 784 0 784 0 784 698 659 0 698 0 698 0 698 659 587 0 523 0 659 0 784 0 0 0
  //   880 0 880 0 880 784 698 0 784 0 784 0 784 698 659 0 698 0 698 0 698 659 587 0 523 0 659 0 523
endmodule

module \团队任务_键盘解析  (
  input  CLK,
  input  RST,
  input  [6:0] \键盘输入 ,
  output W,
  output S,
  output A,
  output D
);

  wire comparator_1_eq, comparator_2_eq, comparator_3_eq, comparator_4_eq;

  Comparator #(.width(7), .mode("unsigned")) comparator_1 (
    .a(\键盘输入 ), .b(7'b1110111), .eq(comparator_1_eq));  // open: gt, lt
  Comparator #(.width(7), .mode("unsigned")) comparator_2 (
    .a(\键盘输入 ), .b(7'b1110011), .eq(comparator_2_eq));  // open: gt, lt
  Comparator #(.width(7), .mode("unsigned")) comparator_3 (
    .a(\键盘输入 ), .b(7'b1100001), .eq(comparator_3_eq));  // open: gt, lt
  Comparator #(.width(7), .mode("unsigned")) comparator_4 (
    .a(\键盘输入 ), .b(7'b1100100), .eq(comparator_4_eq));  // open: gt, lt
  Register #(.width(1), .trigger("rising"), .Select("low")) register_1 (
    .D(comparator_1_eq), .Q(W), .clk(CLK), .clr(RST));  // open: en
  Register #(.width(1), .trigger("rising"), .Select("low")) register_2 (
    .D(comparator_2_eq), .Q(S), .clk(CLK), .clr(RST));  // open: en
  Register #(.width(1), .trigger("rising"), .Select("low")) register_3 (
    .D(comparator_3_eq), .Q(A), .clk(CLK), .clr(RST));  // open: en
  Register #(.width(1), .trigger("rising"), .Select("low")) register_4 (
    .D(comparator_4_eq), .Q(D), .clk(CLK), .clr(RST));  // open: en
endmodule
